// Logisim project cpu21-riscv（final）.circ as structural Verilog: 24 circuits, main circuit ◇单周期RISC-V
module \单周期RISC_V  (
  input  IR1,
  input  IR2,
  input  IR3,
  output RegWrite,
  output MemWrite,
  output [31:0] PC,
  output [31:0] IR,
  output [31:0] RDin,
  output [31:0] MDin,
  output [31:0] LedData,
  output [31:0] out_11
);

  wire Aluequal, Alugreatequal, Aluless, AluSrcB, and_1_out, and_2_out, and_3_out, and_4_out, and_5_out,
       AUIPC, BE, BEQ, BGE, BNE, CLK, clock_1_out, comparator_1_eq, comparator_2_eq, comparator_2_lt, CSR,
       d_ff_1_q, ecall, Go, halt, IR1_t, IR2_t, IR3_t, IRA, IRB, IRC, JAL, JALR, LB, MemToReg, nand_1_out,
       not_1_out, not_2_out, not_3_out, not_4_out, not_6_out, or_5_out, RST, S_type, URET, W1, W2, W3;
  wire [3:0] AluOP;
  wire [4:0] multiplexer_2_out, multiplexer_3_out;
  wire [7:0] multiplexer_9_out;
  wire [11:0] multiplexer_4_out;
  wire [12:0] CNT_num;
  wire [15:0] \总周期数 ;
  wire [31:0] Alures, and_6_out, AUIPCresult, BEaddr, bit_extender_1_out, bit_extender_2_out,
       bit_extender_3_out, bit_extender_4_out, JALaddr, multiplexer_5_out, multiplexer_6_out,
       multiplexer_7_out, multiplexer_8_out, multiplexer_11_out, multiplexer_12_out, nextPC, not_5_out, R1,
       ram_1_data, shifter_1_out, shifter_2_out;

  Button \u_继续运行  (.out(Go));
  Button _1 (.out(IRA));
  Button _2 (.out(IRB));
  Button _3 (.out(IRC));
  LED #(.active("true")) led_1 (.in(W1));
  LED #(.active("true")) led_2 (.in(W2));
  LED #(.active("true")) led_3 (.in(W3));
  Hex_Digit_Display hex_digit_display_1 (.value(LedData[31:28]));  // open: dp
  not not_1 (not_1_out, ecall);
  Counter #(.width(16), .max('hffff), .ongoal("wrap"), .trigger("rising"), .behavior("new")) counter_1 (
    .D({16{1'b0}}), .count(not_1_out), .Q(\总周期数 ), .clk(CLK));  // open: load, carry, clr, preset, down
  Register #(.width(32), .trigger("rising"), .Select("low")) u_PC (
    .D(out_11), .en(not_2_out), .Q(PC), .clk(CLK), .clr(RST));
  not not_2 (not_2_out, halt);
  Comparator #(.width(32), .mode("twosComplement")) comparator_1 (
    .a(R1), .b(32'h22), .eq(comparator_1_eq));  // open: gt, lt
  Hex_Digit_Display hex_digit_display_2 (.value(LedData[27:24]));  // open: dp
  Hex_Digit_Display hex_digit_display_3 (.value(LedData[23:20]));  // open: dp
  not not_3 (not_3_out, comparator_1_eq);
  and and_1 (and_1_out, comparator_1_eq, ecall);
  Hex_Digit_Display hex_digit_display_4 (.value(LedData[15:12]));  // open: dp
  Hex_Digit_Display hex_digit_display_5 (.value(LedData[19:16]));  // open: dp
  // RiscV_Probe riscv_probe_1: pin names not known; wires that end beside it: IR
  Adder #(.width(32)) adder_1 (.a(PC), .b(32'h4), .out(nextPC));  // open: cin, cout
  and and_2 (and_2_out, ecall, not_3_out);
  Register #(.width(32), .trigger("rising"), .Select("low")) register_1 (
    .D(MDin), .en(and_1_out), .Q(LedData), .clk(CLK));  // open: clr
  Hex_Digit_Display hex_digit_display_6 (.value(LedData[7:4]));  // open: dp
  Hex_Digit_Display hex_digit_display_7 (.value(LedData[11:8]));  // open: dp
  // Probe on \总周期数 
  ROM #(.addrWidth(10), .dataWidth(32), .Select("high")) rom_1 (.addr(PC[11:2]), .data(IR));
  Multiplexer #(.select(1), .width(1), .disabled("Z"), .enable("false")) multiplexer_1 (
    .in0(and_2_out), .in1(1'b0), .out(halt), .sel(Go));
  Hex_Digit_Display hex_digit_display_8 (.value(LedData[3:0]));  // open: dp
  \单周期硬布线控制器  \u_单周期硬布线控制器_1  (
    .Funct({IR[30], IR[25], IR[14:12]}), .OP(IR[6:2]), .ALU_OP(AluOP), .MemToReg(MemToReg),
    .MemWrite(MemWrite), .ALU_SRC(AluSrcB), .RegWrite(RegWrite), .ecall(ecall), .S_type(S_type), .Jalr(JALR),
    .Beq(BEQ), .JAL(JAL), .Bne(BNE), .in_3(IR[21]), .uret(URET), .CSR(CSR), .AUIPC(AUIPC), .LB(LB), .BGE(BGE));  // open: RSread, RTread
  Multiplexer #(.select(1), .width(5), .disabled("Z"), .enable("false")) multiplexer_2 (
    .in0(IR[19:15]), .in1(5'b10001), .out(multiplexer_2_out), .sel(ecall));
  Multiplexer #(.select(1), .width(5), .disabled("Z"), .enable("false")) multiplexer_3 (
    .in0(IR[24:20]), .in1(5'b01010), .out(multiplexer_3_out), .sel(ecall));
  Multiplexer #(.select(1), .width(12), .disabled("Z"), .enable("false")) multiplexer_4 (
    .in0(IR[31:20]), .in1({IR[31:25], IR[11:7]}), .out(multiplexer_4_out), .sel(S_type));
  or or_1 (IR1_t, IR1, IRA);
  assign bit_extender_1_out = {{20{IR[31]}}, {IR[31], IR[7], IR[30:25], IR[11:8]}};  // Bit_Extender bit_extender_1
  assign bit_extender_2_out = {{12{IR[31]}}, {IR[31], IR[19:12], IR[20], IR[30:21]}};  // Bit_Extender bit_extender_2
  or or_2 (IR2_t, IR2, IRB);
  Regifile regifile_1 (
    .Din(RDin), .Clk(CLK), .R1(R1), .R2(MDin), .WE(RegWrite), .W_num(IR[11:7]), .R1_num(multiplexer_2_out),
    .R2_num(multiplexer_3_out));
  assign bit_extender_3_out = {{20{multiplexer_4_out[11]}}, multiplexer_4_out};  // Bit_Extender bit_extender_3
  Shifter #(.width(32), .shift("ll")) shifter_1 (.in(bit_extender_1_out), .\dist (5'b00001), .out(shifter_1_out));
  Shifter #(.width(32), .shift("ll")) shifter_2 (.in(bit_extender_2_out), .\dist (5'b00001), .out(shifter_2_out));
  or or_3 (IR3_t, IR3, IRC);
  Multiplexer #(.select(1), .width(32), .disabled("Z"), .enable("false")) multiplexer_5 (
    .in0(MDin), .in1(bit_extender_3_out), .out(multiplexer_5_out), .sel(AluSrcB));
  Adder #(.width(32)) adder_2 (.a(shifter_1_out), .b(PC), .out(BEaddr), .cin(1'b0));  // open: cout
  Adder #(.width(32)) adder_3 (.a(shifter_2_out), .b(PC), .out(JALaddr), .cin(1'b0));  // open: cout
  Adder #(.width(32)) adder_4 (.a({IR[31:12], {12{1'b0}}}), .b(PC), .out(AUIPCresult), .cin(1'b0));  // open: cout
  ALU alu_1 (
    .X(R1), .Y(multiplexer_5_out), .AluOP(AluOP), .Equal(Aluequal), .Result(Alures), .out_4(Alugreatequal),
    .out_6(Aluless));  // open: Result_2
  Multiplexer #(.select(1), .width(32), .disabled("Z"), .enable("false")) multiplexer_6 (
    .in0(Alures), .in1(AUIPCresult), .out(multiplexer_6_out), .sel(AUIPC));
  not not_4 (not_4_out, MemWrite);
  Multiplexer #(.select(1), .width(32), .disabled("Z"), .enable("false")) multiplexer_7 (
    .in0(nextPC), .in1(BEaddr), .out(multiplexer_7_out), .sel(BE));
  assign not_5_out = ~32'h1;  // NOT_Gate not_5, 32 bits wide
  and and_3 (and_3_out, Aluequal, BEQ);
  not not_6 (not_6_out, Aluequal);
  and and_4 (and_4_out, not_6_out, BNE);
  and and_5 (and_5_out, Alugreatequal, BGE);
  RAM #(.addrWidth(10), .dataWidth(32), .bus("separate"), .Select("high")) ram_1 (
    .addr(multiplexer_6_out[11:2]), .din(MDin), .data(ram_1_data), .str(MemWrite), .clk(CLK), .ld(not_4_out));  // open: sel, clr
  Multiplexer #(.select(1), .width(32), .disabled("Z"), .enable("false")) multiplexer_8 (
    .in0(multiplexer_7_out), .in1(JALaddr), .out(multiplexer_8_out), .sel(JAL));
  assign and_6_out = Alures & not_5_out;  // AND_Gate and_6, 32 bits wide
  or or_4 (BE, and_3_out, and_4_out, and_5_out);
  Multiplexer #(.select(2), .width(8), .disabled("Z"), .enable("false")) multiplexer_9 (
    .in0(ram_1_data[7:0]), .in1(ram_1_data[15:8]), .in2(ram_1_data[23:16]), .in3(ram_1_data[31:24]),
    .out(multiplexer_9_out), .sel(Alures[1:0]));
  Multiplexer #(.select(1), .width(32), .disabled("Z"), .enable("false")) multiplexer_10 (
    .in0(multiplexer_8_out), .in1(and_6_out), .out(out_11), .sel(JALR));
  assign bit_extender_4_out = {{24{multiplexer_9_out[7]}}, multiplexer_9_out};  // Bit_Extender bit_extender_4
  D_Flip_Flop #(.trigger("high"), .Pre_Clr_Positions("LEGACY"), .NegatePresetClear("false"), .enable("true"), .NewFFLayout("false")) d_ff_1 (.Q(d_ff_1_q));  // open: clk, D, Qn, preset, en, reset
  // Probe on 13'hc
  Multiplexer #(.select(1), .width(32), .disabled("Z"), .enable("false")) multiplexer_11 (
    .in0(ram_1_data), .in1(bit_extender_4_out), .out(multiplexer_11_out), .sel(LB));
  Comparator #(.width(13), .mode("twosComplement")) comparator_2 (
    .a(CNT_num), .b(13'hc), .eq(comparator_2_eq), .lt(comparator_2_lt));  // open: gt
  Clock #(.highDuration(1), .lowDuration(1)) clock_1 (.out(clock_1_out));
  Multiplexer #(.select(1), .width(32), .disabled("Z"), .enable("false")) multiplexer_12 (
    .in0(multiplexer_6_out), .in1(multiplexer_11_out), .out(multiplexer_12_out), .sel(MemToReg));
  or or_5 (or_5_out, JAL, JALR);
  Counter #(.width(13), .max('h1fff), .ongoal("stay"), .trigger("rising"), .behavior("old")) counter_2 (
    .count(comparator_2_lt), .Q(CNT_num), .clk(clock_1_out));  // open: load, D, carry, clr, preset
  Multiplexer #(.select(1), .width(32), .disabled("Z"), .enable("false")) multiplexer_13 (
    .in0(multiplexer_12_out), .in1(nextPC), .out(RDin), .sel(or_5_out));
  nand nand_1 (nand_1_out, d_ff_1_q, comparator_2_eq);
  assign CLK = nand_1_out ? clock_1_out : 1'bz;  // Controlled_Buffer controlled_buffer_1
  Pull_Resistor #(.pull(1)) pull_resistor_1 (.node(CLK));

  // Other names for the same wires on the sheet: PCaddr[31:0] = out_11; R2[31:0] = MDin

  // Notes on the sheet:
  //   中断源
  //   中断等待指示
  //   数码管输出应该用寄存器锁存，否则显示数据只能一闪而过
  //   数码管输出
  //   指令探针
  //   指令存储器
  //   指令字
  //   contents of rom_1 (hex, n*v repeats v):
  //   100493 100006f 100493 200913 300993 100006f 100493 200913 300993 100006f 100493 200913 300993
  //   100006f 100493 200913 300993 40c000ef 100413 100493 1f49493 900533 2200893 73 24d493 48463 fedff06f
  //   900533 2200893 73 100493 249493 900533 2200893 73 48463 fedff06f 100493 1f49493 900533 2200893 73
  //   4034d493 900533 2200893 73 4044d493 900533 2200893 73 4044d493 900533 2200893 73 4044d493 900533
  //   2200893 73 4044d493 900533 2200893 73 4044d493 900533 2200893 73 4044d493 900533 2200893 73 4044d493
  //   900533 2200893 73 100413 1f41993 41f9d993 433 c00913 300b13 140413 f47413 800293 100313 499993
  //   89e9b3 1300533 2200893 73 406282b3 fe0294e3 140413 f00f93 1f47433 1c41413 800293 100313 49d993
  //   89e9b3 1300533 2200893 73 406282b3 fe0294e3 1c45413 406b0b33 b0463 f95ff06f 2b3 fff2c293 829293
  //   ff2e293 500533 2200893 73 fff00413 493 84a023 140413 448493 84a023 140413 448493 84a023 140413
  //   448493 84a023 140413 448493 84a023 140413 448493 84a023 140413 448493 84a023 140413 448493 84a023
  //   140413 448493 84a023 140413 448493 84a023 140413 448493 84a023 140413 448493 84a023 140413 448493
  //   84a023 140413 448493 84a023 140413 448493 84a023 140413 448493 84a023 140413 448493 140413 433
  //   3c00493 42983 4aa03 149a2b3 28663 134a023 1442023 ffc48493 fe9412e3 800533 2200893 73 440413 3c00493
  //   fc9416e3 a00893 73 fff00293 7700493 849493 7748493 900533 2200893 73 1000e13 54c4b3 900533 2200893
  //   73 fffe0e13 fe0e16e3 a00893 73 13 430497 900533 2200893 73 430497 900533 2200893 73 430497 900533
  //   2200893 73 430497 900533 2200893 73 430497 900533 2200893 73 430497 900533 2200893 73 430497 900533
  //   2200893 73 430497 900533 2200893 73 a00893 73 313 1000e13 13 8400493 849493 8348493 400913 891913
  //   490913 849493 8248493 849493 8148493 891913 490913 891913 490913 932023 12484b3 430313 fffe0e13
  //   fe0e18e3 2000e13 313 30483 900533 2200893 73 130313 fffe0e13 fe0e14e3 a00893 73 f00493 900533
  //   2200893 73 fff48493 fe04d8e3 a00893 73 413 140413 800533 2200893 73 240413 800533 2200893 73 340413
  //   800533 2200893 73 440413 800533 2200893 73 540413 800533 2200893 73 640413 800533 2200893 73 740413
  //   800533 2200893 73 840413 800533 2200893 2200893 73 8067
  //   JAL
  //   JALR
  //   URET
  //   Beq
  //   Bne
  //   MemToReg
  //   MemWrite
  //   AluOP
  //   AluSrcB
  //   RegWrite
  //   数据存储器
  //   为方便自动评测，需要输出PC，IR，寄存器堆写如数据RDin
  //   RAM写使能MemWrite、RAM写入数据MDin等信号
  //   控制位
  //   暂停节拍，不能为0
  //   戳工具置1进入计数暂停模式，ctrl+k时钟自动运行到对应节拍暂停
  //   ctrl+k关闭时钟连续运行，将控制位置零，进入单步调试模式调试
  //   用这个时钟源需要去掉电路中的其他时钟源
  //   可计数暂停的时钟源
endmodule

// 单周期硬布线控制器
module \单周期硬布线控制器  (
  input  [4:0] OP,
  input  [4:0] Funct,
  input  in_3,
  output [3:0] ALU_OP,
  output uret,
  output MemToReg,
  output ecall,
  output MemWrite,
  output RSread,
  output ALU_SRC,
  output RegWrite,
  output S_type,
  output Beq,
  output Bne,
  output Jalr,
  output RTread,
  output JAL,
  output CSR,
  output AUIPC,
  output LB,
  output BGE
);

  wire \控制信号自动生成_1_ecall ;

  \运算控制器自动生成  \u_运算控制器自动生成_1  (
    .OP2(OP[0]), .OP3(OP[1]), .OP4(OP[2]), .OP5(OP[3]), .OP6(OP[4]), .F12(Funct[0]), .F13(Funct[1]),
    .F14(Funct[2]), .F25(Funct[3]), .F30(Funct[4]), .S0(ALU_OP[0]), .S1(ALU_OP[1]), .S2(ALU_OP[2]),
    .S3(ALU_OP[3]));
  \控制信号自动生成  \u_控制信号自动生成_1  (
    .OP2(OP[0]), .OP3(OP[1]), .MemToReg(MemToReg), .OP4(OP[2]), .OP5(OP[3]), .OP6(OP[4]), .F12(Funct[0]),
    .MemWrite(MemWrite), .F13(Funct[1]), .F14(Funct[2]), .F25(Funct[3]), .F30(Funct[4]), .ALU_SRC(ALU_SRC),
    .RSread(RSread), .RegWrite(RegWrite), .RTread(RTread), .ecall(\控制信号自动生成_1_ecall ), .S_Type(S_type),
    .BEQ(Beq), .BNE(Bne), .JALR(Jalr), .JAL(JAL), .CSR(CSR), .AUIPC(AUIPC), .LB(LB), .BGE(BGE));
  and and_1 (uret, in_3, \控制信号自动生成_1_ecall );
  and and_2 (ecall, ~in_3, \控制信号自动生成_1_ecall );  // AND_Gate

  // Other names for the same wires on the sheet: IR21 = in_3; OP_CODE[4:0] = OP

  // Notes on the sheet:
  //   运算器控制器，根据指令生成运算器功能选择信号
endmodule

// 运算器控制器
module \运算控制器自动生成  (
  input  OP2,
  input  OP3,
  input  OP4,
  input  OP5,
  input  OP6,
  input  F12,
  input  F13,
  input  F14,
  input  F25,
  input  F30,
  output S0,
  output S1,
  output S2,
  output S3
);

  wire and_1_out, and_2_out, and_3_out, and_4_out, and_5_out, and_6_out, and_7_out, and_8_out, and_9_out,
       and_10_out, and_11_out, and_12_out, and_13_out, and_14_out, and_15_out, and_16_out, and_17_out,
       and_18_out, and_19_out, and_20_out, and_21_out, and_22_out, and_23_out, and_24_out, and_25_out,
       and_26_out, and_27_out, and_28_out, and_29_out, and_30_out, and_31_out, and_32_out, not_1_out,
       not_2_out, not_3_out, not_4_out, not_5_out, not_6_out, not_7_out, not_8_out, not_9_out, not_10_out,
       not_11_out, not_12_out, not_13_out, not_14_out, not_15_out, not_16_out, not_17_out, not_18_out,
       not_19_out, not_20_out, not_21_out, not_22_out, not_23_out, not_24_out, not_25_out, not_26_out,
       not_27_out, not_28_out, not_29_out, not_30_out, not_31_out, not_32_out, not_33_out, not_34_out,
       not_35_out, not_36_out, not_37_out, not_38_out, not_39_out, not_40_out, not_41_out, not_42_out,
       not_43_out, not_44_out, not_45_out, not_46_out, not_47_out, not_48_out, not_49_out, not_50_out,
       not_51_out, not_52_out, not_53_out, not_54_out, not_55_out, not_56_out, not_57_out, not_58_out,
       not_59_out, not_60_out, not_61_out, not_62_out, not_63_out, not_64_out, not_65_out, not_66_out,
       not_67_out, not_68_out, not_69_out, not_70_out, not_71_out, not_72_out, not_73_out, not_74_out,
       not_75_out, not_76_out, not_77_out, not_78_out, not_79_out, not_80_out, not_81_out, not_82_out,
       not_83_out, not_84_out, not_85_out, not_86_out, not_87_out, not_88_out, not_89_out, not_90_out,
       not_91_out, not_92_out, not_93_out, not_94_out, not_95_out, not_96_out, not_97_out, not_98_out,
       not_99_out, not_100_out, not_101_out, not_102_out, not_103_out, not_104_out, not_105_out, not_106_out,
       not_107_out, not_108_out, not_109_out, not_110_out, not_111_out, not_112_out, not_113_out,
       not_114_out, not_115_out, not_116_out, not_117_out, not_118_out, not_119_out, not_120_out,
       not_121_out, not_122_out, not_123_out, not_124_out, not_125_out, not_126_out, not_127_out,
       not_128_out, not_129_out, not_130_out, not_131_out, not_132_out, not_133_out, not_134_out,
       not_135_out, not_136_out, not_137_out, not_138_out, not_139_out, not_140_out, not_141_out,
       not_142_out, not_143_out, not_144_out, not_145_out, not_146_out, not_147_out, not_148_out,
       not_149_out, not_150_out, not_151_out, not_152_out, not_153_out, not_154_out, not_155_out,
       not_156_out, not_157_out, not_158_out, not_159_out, not_160_out, not_161_out, not_162_out,
       not_163_out, not_164_out;

  not not_1 (not_1_out, OP2);
  not not_2 (not_2_out, OP3);
  not not_3 (not_3_out, OP5);
  not not_4 (not_4_out, OP6);
  not not_5 (not_5_out, F12);
  not not_6 (not_6_out, F14);
  not not_7 (not_7_out, OP2);
  not not_8 (not_8_out, OP3);
  not not_9 (not_9_out, OP4);
  not not_10 (not_10_out, OP6);
  not not_11 (not_11_out, F12);
  not not_12 (not_12_out, F14);
  not not_13 (not_13_out, OP2);
  not not_14 (not_14_out, OP3);
  not not_15 (not_15_out, OP4);
  not not_16 (not_16_out, F13);
  not not_17 (not_17_out, OP2);
  not not_18 (not_18_out, OP3);
  not not_19 (not_19_out, OP5);
  not not_20 (not_20_out, OP6);
  not not_21 (not_21_out, F12);
  not not_22 (not_22_out, F13);
  not not_23 (not_23_out, OP2);
  not not_24 (not_24_out, OP3);
  not not_25 (not_25_out, OP6);
  not not_26 (not_26_out, F12);
  not not_27 (not_27_out, F13);
  not not_28 (not_28_out, F25);
  not not_29 (not_29_out, F30);
  not not_30 (not_30_out, OP2);
  not not_31 (not_31_out, OP3);
  not not_32 (not_32_out, OP6);
  not not_33 (not_33_out, F12);
  not not_34 (not_34_out, F14);
  not not_35 (not_35_out, F25);
  not not_36 (not_36_out, F30);
  not not_37 (not_37_out, OP2);
  not not_38 (not_38_out, OP3);
  not not_39 (not_39_out, OP5);
  not not_40 (not_40_out, OP6);
  not not_41 (not_41_out, F13);
  not not_42 (not_42_out, F25);
  not not_43 (not_43_out, OP2);
  not not_44 (not_44_out, OP3);
  not not_45 (not_45_out, OP5);
  not not_46 (not_46_out, OP6);
  not not_47 (not_47_out, OP2);
  not not_48 (not_48_out, OP3);
  not not_49 (not_49_out, OP6);
  not not_50 (not_50_out, F25);
  not not_51 (not_51_out, F30);
  not not_52 (not_52_out, OP2);
  not not_53 (not_53_out, OP3);
  not not_54 (not_54_out, OP3);
  not not_55 (not_55_out, OP4);
  not not_56 (not_56_out, F12);
  not not_57 (not_57_out, F13);
  not not_58 (not_58_out, F14);
  not not_59 (not_59_out, OP2);
  not not_60 (not_60_out, OP3);
  not not_61 (not_61_out, OP4);
  not not_62 (not_62_out, F13);
  not not_63 (not_63_out, OP2);
  not not_64 (not_64_out, OP3);
  not not_65 (not_65_out, OP5);
  not not_66 (not_66_out, OP6);
  not not_67 (not_67_out, F12);
  not not_68 (not_68_out, F14);
  not not_69 (not_69_out, OP2);
  not not_70 (not_70_out, OP3);
  not not_71 (not_71_out, OP6);
  not not_72 (not_72_out, F12);
  not not_73 (not_73_out, F14);
  not not_74 (not_74_out, F25);
  not not_75 (not_75_out, F30);
  not not_76 (not_76_out, OP2);
  not not_77 (not_77_out, OP3);
  not not_78 (not_78_out, OP5);
  not not_79 (not_79_out, OP6);
  not not_80 (not_80_out, F25);
  not not_81 (not_81_out, F30);
  not not_82 (not_82_out, OP2);
  not not_83 (not_83_out, OP3);
  not not_84 (not_84_out, OP5);
  not not_85 (not_85_out, OP6);
  not not_86 (not_86_out, OP2);
  not not_87 (not_87_out, OP3);
  not not_88 (not_88_out, OP6);
  not not_89 (not_89_out, F25);
  not not_90 (not_90_out, F30);
  not not_91 (not_91_out, OP2);
  not not_92 (not_92_out, OP3);
  not not_93 (not_93_out, OP6);
  not not_94 (not_94_out, F12);
  not not_95 (not_95_out, F13);
  not not_96 (not_96_out, F14);
  not not_97 (not_97_out, F25);
  not not_98 (not_98_out, OP2);
  not not_99 (not_99_out, OP3);
  not not_100 (not_100_out, OP2);
  not not_101 (not_101_out, OP3);
  not not_102 (not_102_out, OP5);
  not not_103 (not_103_out, OP6);
  not not_104 (not_104_out, F12);
  not not_105 (not_105_out, F13);
  not not_106 (not_106_out, F14);
  not not_107 (not_107_out, OP2);
  not not_108 (not_108_out, OP3);
  not not_109 (not_109_out, OP4);
  not not_110 (not_110_out, OP6);
  not not_111 (not_111_out, F12);
  not not_112 (not_112_out, F14);
  not not_113 (not_113_out, OP2);
  not not_114 (not_114_out, OP3);
  not not_115 (not_115_out, OP6);
  not not_116 (not_116_out, F12);
  not not_117 (not_117_out, F13);
  not not_118 (not_118_out, F14);
  not not_119 (not_119_out, F25);
  not not_120 (not_120_out, OP2);
  not not_121 (not_121_out, OP3);
  not not_122 (not_122_out, OP5);
  not not_123 (not_123_out, OP6);
  not not_124 (not_124_out, OP2);
  not not_125 (not_125_out, OP3);
  not not_126 (not_126_out, OP6);
  not not_127 (not_127_out, F25);
  not not_128 (not_128_out, F30);
  not not_129 (not_129_out, OP2);
  not not_130 (not_130_out, OP3);
  not not_131 (not_131_out, OP3);
  not not_132 (not_132_out, OP4);
  not not_133 (not_133_out, F12);
  not not_134 (not_134_out, F13);
  not not_135 (not_135_out, F14);
  not not_136 (not_136_out, OP2);
  not not_137 (not_137_out, OP3);
  not not_138 (not_138_out, OP4);
  not not_139 (not_139_out, F13);
  not not_140 (not_140_out, OP2);
  not not_141 (not_141_out, OP3);
  not not_142 (not_142_out, OP5);
  not not_143 (not_143_out, OP6);
  not not_144 (not_144_out, F12);
  not not_145 (not_145_out, OP2);
  not not_146 (not_146_out, OP3);
  not not_147 (not_147_out, OP6);
  not not_148 (not_148_out, F12);
  not not_149 (not_149_out, F25);
  not not_150 (not_150_out, F30);
  not not_151 (not_151_out, OP2);
  not not_152 (not_152_out, OP3);
  not not_153 (not_153_out, OP5);
  not not_154 (not_154_out, OP6);
  not not_155 (not_155_out, F12);
  not not_156 (not_156_out, OP2);
  not not_157 (not_157_out, OP3);
  not not_158 (not_158_out, OP6);
  not not_159 (not_159_out, F14);
  not not_160 (not_160_out, F25);
  not not_161 (not_161_out, F30);
  not not_162 (not_162_out, OP2);
  not not_163 (not_163_out, OP3);
  not not_164 (not_164_out, F12);
  and and_1 (and_1_out, not_1_out, not_2_out, not_3_out, not_4_out, not_5_out, not_6_out);
  and and_2 (and_2_out, not_7_out, not_8_out, not_9_out, not_10_out, not_11_out, F13, not_12_out);
  and and_3 (and_3_out, not_13_out, not_14_out, not_15_out, OP5, OP6, F12, not_16_out, F14);
  and and_4 (and_4_out, not_17_out, not_18_out, OP4, not_19_out, not_20_out, not_21_out, not_22_out);
  and and_5 (and_5_out, not_23_out, not_24_out, OP4, not_25_out, not_26_out, not_27_out, not_28_out, not_29_out);
  and and_6 (and_6_out, not_30_out, not_31_out, OP4, not_32_out, not_33_out, not_34_out, not_35_out, not_36_out);
  and and_7 (and_7_out, not_37_out, not_38_out, OP4, not_39_out, not_40_out, not_41_out, F14, not_42_out, F30);
  and and_8 (and_8_out, not_43_out, not_44_out, OP4, not_45_out, not_46_out, F12, F13, F14);
  and and_9 (and_9_out, not_47_out, not_48_out, OP4, not_49_out, F12, F13, F14, not_50_out, not_51_out);
  and and_10 (and_10_out, not_52_out, not_53_out, OP4, OP5, OP6, F12, F13, F14);
  and and_11 (and_11_out, OP2, not_54_out, not_55_out, OP5, OP6, not_56_out, not_57_out, not_58_out);
  and and_12 (and_12_out, not_59_out, not_60_out, not_61_out, OP5, OP6, F12, not_62_out, F14);
  and and_13 (and_13_out, not_63_out, not_64_out, OP4, not_65_out, not_66_out, not_67_out, F13, not_68_out);
  and and_14 (and_14_out, not_69_out, not_70_out, OP4, not_71_out, not_72_out, F13, not_73_out, not_74_out, not_75_out);
  and and_15 (and_15_out, not_76_out, not_77_out, OP4, not_78_out, not_79_out, F12, F14, not_80_out, not_81_out);
  and and_16 (and_16_out, not_82_out, not_83_out, OP4, not_84_out, not_85_out, F12, F13, F14);
  and and_17 (and_17_out, not_86_out, not_87_out, OP4, not_88_out, F12, F13, F14, not_89_out, not_90_out);
  and and_18 (and_18_out, not_91_out, not_92_out, OP4, OP5, not_93_out, not_94_out, not_95_out, not_96_out, not_97_out, F30);
  and and_19 (and_19_out, not_98_out, not_99_out, OP4, OP5, OP6, F12, F13, F14);
  and and_20 (and_20_out, not_100_out, not_101_out, not_102_out, not_103_out, not_104_out, not_105_out, not_106_out);
  and and_21 (and_21_out, not_107_out, not_108_out, not_109_out, not_110_out, not_111_out, F13, not_112_out);
  and and_22 (and_22_out, not_113_out, not_114_out, OP4, not_115_out, not_116_out, not_117_out, not_118_out, not_119_out);
  and and_23 (and_23_out, not_120_out, not_121_out, OP4, not_122_out, not_123_out, F12, F13, F14);
  and and_24 (and_24_out, not_124_out, not_125_out, OP4, OP5, not_126_out, F12, F13, not_127_out, not_128_out);
  and and_25 (and_25_out, not_129_out, not_130_out, OP4, OP5, OP6, F12, F13, F14);
  and and_26 (and_26_out, OP2, not_131_out, not_132_out, OP5, OP6, not_133_out, not_134_out, not_135_out);
  and and_27 (and_27_out, not_136_out, not_137_out, not_138_out, OP5, OP6, F12, not_139_out, F14);
  and and_28 (and_28_out, not_140_out, not_141_out, OP4, not_142_out, not_143_out, not_144_out, F14);
  and and_29 (and_29_out, not_145_out, not_146_out, OP4, not_147_out, not_148_out, F14, not_149_out, not_150_out);
  and and_30 (and_30_out, not_151_out, not_152_out, OP4, not_153_out, not_154_out, not_155_out, F13);
  and and_31 (and_31_out, not_156_out, not_157_out, OP4, OP5, not_158_out, F13, not_159_out, not_160_out, not_161_out);
  and and_32 (and_32_out, not_162_out, not_163_out, OP4, OP5, OP6, not_164_out, F13, F14);
  or or_1 (S2, and_20_out, and_21_out, and_22_out, and_23_out, and_24_out, and_25_out, and_26_out);
  or or_2 (S3, and_27_out, and_28_out, and_29_out, and_30_out, and_31_out, and_32_out);
  or or_3 (S0, and_1_out, and_2_out, and_3_out, and_4_out, and_5_out, and_6_out, and_7_out, and_8_out, and_9_out, and_10_out, and_11_out);
  or or_4 (S1, and_12_out, and_13_out, and_14_out, and_15_out, and_16_out, and_17_out, and_18_out, and_19_out);
endmodule

// 控制信号生成
module \控制信号自动生成  (
  input  OP2,
  input  OP3,
  input  OP4,
  input  OP5,
  input  OP6,
  input  F12,
  input  F13,
  input  F14,
  input  F25,
  input  F30,
  output MemToReg,
  output MemWrite,
  output ALU_SRC,
  output RSread,
  output RegWrite,
  output RTread,
  output ecall,
  output S_Type,
  output BEQ,
  output BNE,
  output JALR,
  output JAL,
  output CSR,
  output AUIPC,
  output LB,
  output BGE
);

  wire and_3_out, and_4_out, and_5_out, and_6_out, and_7_out, and_8_out, and_9_out, and_10_out, and_11_out,
       and_12_out, and_13_out, and_14_out, and_15_out, and_16_out, and_17_out, and_18_out, and_19_out,
       and_20_out, and_21_out, and_22_out, and_23_out, and_24_out, and_25_out, and_26_out, and_27_out,
       and_28_out, and_29_out, and_30_out, and_31_out, and_32_out, and_33_out, and_34_out, and_35_out,
       and_36_out, and_37_out, and_38_out, not_1_out, not_2_out, not_3_out, not_4_out, not_5_out, not_6_out,
       not_7_out, not_8_out, not_9_out, not_10_out, not_11_out, not_12_out, not_13_out, not_14_out,
       not_15_out, not_16_out, not_17_out, not_18_out, not_19_out, not_20_out, not_21_out, not_22_out,
       not_23_out, not_24_out, not_25_out, not_26_out, not_27_out, not_28_out, not_29_out, not_30_out,
       not_31_out, not_32_out, not_33_out, not_34_out, not_35_out, not_36_out, not_37_out, not_38_out,
       not_39_out, not_40_out, not_41_out, not_42_out, not_43_out, not_44_out, not_45_out, not_46_out,
       not_47_out, not_48_out, not_49_out, not_50_out, not_51_out, not_52_out, not_53_out, not_54_out,
       not_55_out, not_56_out, not_57_out, not_58_out, not_59_out, not_60_out, not_61_out, not_62_out,
       not_63_out, not_64_out, not_65_out, not_66_out, not_67_out, not_68_out, not_69_out, not_70_out,
       not_71_out, not_72_out, not_73_out, not_74_out, not_75_out, not_76_out, not_77_out, not_78_out,
       not_79_out, not_80_out, not_81_out, not_82_out, not_83_out, not_84_out, not_85_out, not_86_out,
       not_87_out, not_88_out, not_89_out, not_90_out, not_91_out, not_92_out, not_93_out, not_94_out,
       not_95_out, not_96_out, not_97_out, not_98_out, not_99_out, not_100_out, not_101_out, not_102_out,
       not_103_out, not_104_out, not_105_out, not_106_out, not_107_out, not_108_out, not_109_out,
       not_110_out, not_111_out, not_112_out, not_113_out, not_114_out, not_115_out, not_116_out,
       not_117_out, not_118_out, not_119_out, not_120_out, not_121_out, not_122_out, not_123_out,
       not_124_out, not_125_out, not_126_out, not_127_out, not_128_out, not_129_out, not_130_out,
       not_131_out, not_132_out, not_133_out, not_134_out, not_135_out, not_136_out, not_137_out,
       not_138_out, not_139_out, not_140_out, not_141_out, not_142_out, not_143_out, not_144_out,
       not_145_out, not_146_out, not_147_out, not_148_out, not_149_out, not_150_out, not_151_out,
       not_152_out, not_153_out, not_154_out, not_155_out, not_156_out, not_157_out, not_158_out,
       not_159_out, not_160_out, not_161_out, not_162_out, not_163_out, not_164_out, not_165_out,
       not_166_out, not_167_out, not_168_out, not_169_out, not_170_out, not_171_out, not_172_out,
       not_173_out, not_174_out, not_175_out, not_176_out, not_177_out, not_178_out, not_179_out,
       not_180_out, not_181_out, not_182_out, not_183_out, not_184_out, not_185_out, not_186_out,
       not_187_out, not_188_out, not_189_out, not_190_out, not_191_out, not_192_out, not_193_out,
       not_194_out, not_195_out, not_196_out, not_197_out, not_198_out, not_199_out, not_200_out,
       not_201_out, not_202_out, not_203_out, not_204_out, not_205_out, not_206_out, not_207_out,
       not_208_out, not_209_out, not_210_out, not_211_out, not_212_out, not_213_out, not_214_out,
       not_215_out, not_216_out, not_217_out, not_218_out, not_219_out, not_220_out, not_221_out,
       not_222_out, not_223_out, not_224_out, not_225_out, not_226_out, not_227_out, not_228_out,
       not_229_out, not_230_out, not_231_out, not_232_out, not_233_out, not_234_out, not_235_out,
       not_236_out, not_237_out, not_238_out, not_239_out, not_240_out, not_241_out, not_242_out;

  not not_1 (not_1_out, OP2);
  not not_2 (not_2_out, OP3);
  not not_3 (not_3_out, OP4);
  not not_4 (not_4_out, OP5);
  not not_5 (not_5_out, OP6);
  not not_6 (not_6_out, F12);
  not not_7 (not_7_out, F14);
  not not_8 (not_8_out, OP2);
  not not_9 (not_9_out, OP3);
  not not_10 (not_10_out, OP4);
  not not_11 (not_11_out, OP6);
  not not_12 (not_12_out, F12);
  not not_13 (not_13_out, F14);
  not not_14 (not_14_out, OP2);
  not not_15 (not_15_out, OP3);
  not not_16 (not_16_out, OP5);
  not not_17 (not_17_out, OP6);
  not not_18 (not_18_out, F12);
  not not_19 (not_19_out, F14);
  not not_20 (not_20_out, OP2);
  not not_21 (not_21_out, OP3);
  not not_22 (not_22_out, OP4);
  not not_23 (not_23_out, OP6);
  not not_24 (not_24_out, F12);
  not not_25 (not_25_out, F14);
  not not_26 (not_26_out, OP2);
  not not_27 (not_27_out, OP3);
  not not_28 (not_28_out, OP5);
  not not_29 (not_29_out, OP6);
  not not_30 (not_30_out, F12);
  not not_31 (not_31_out, OP2);
  not not_32 (not_32_out, OP3);
  not not_33 (not_33_out, OP5);
  not not_34 (not_34_out, OP6);
  not not_35 (not_35_out, F13);
  not not_36 (not_36_out, F25);
  not not_37 (not_37_out, F30);
  not not_38 (not_38_out, OP2);
  not not_39 (not_39_out, OP3);
  not not_40 (not_40_out, OP5);
  not not_41 (not_41_out, OP6);
  not not_42 (not_42_out, F25);
  not not_43 (not_43_out, OP2);
  not not_44 (not_44_out, OP3);
  not not_45 (not_45_out, OP5);
  not not_46 (not_46_out, OP6);
  not not_47 (not_47_out, OP3);
  not not_48 (not_48_out, OP4);
  not not_49 (not_49_out, F12);
  not not_50 (not_50_out, F13);
  not not_51 (not_51_out, F14);
  not not_52 (not_52_out, OP2);
  not not_53 (not_53_out, OP3);
  not not_54 (not_54_out, OP5);
  not not_55 (not_55_out, OP6);
  not not_56 (not_56_out, F12);
  not not_57 (not_57_out, F14);
  not not_58 (not_58_out, OP2);
  not not_59 (not_59_out, OP3);
  not not_60 (not_60_out, OP4);
  not not_61 (not_61_out, OP6);
  not not_62 (not_62_out, F12);
  not not_63 (not_63_out, F14);
  not not_64 (not_64_out, OP2);
  not not_65 (not_65_out, OP3);
  not not_66 (not_66_out, F12);
  not not_67 (not_67_out, F13);
  not not_68 (not_68_out, F14);
  not not_69 (not_69_out, OP3);
  not not_70 (not_70_out, OP4);
  not not_71 (not_71_out, F12);
  not not_72 (not_72_out, F13);
  not not_73 (not_73_out, F14);
  not not_74 (not_74_out, OP2);
  not not_75 (not_75_out, OP3);
  not not_76 (not_76_out, OP4);
  not not_77 (not_77_out, F13);
  not not_78 (not_78_out, OP2);
  not not_79 (not_79_out, OP3);
  not not_80 (not_80_out, OP5);
  not not_81 (not_81_out, OP6);
  not not_82 (not_82_out, F12);
  not not_83 (not_83_out, OP2);
  not not_84 (not_84_out, OP3);
  not not_85 (not_85_out, OP5);
  not not_86 (not_86_out, OP6);
  not not_87 (not_87_out, F13);
  not not_88 (not_88_out, F25);
  not not_89 (not_89_out, F30);
  not not_90 (not_90_out, OP2);
  not not_91 (not_91_out, OP3);
  not not_92 (not_92_out, OP6);
  not not_93 (not_93_out, F12);
  not not_94 (not_94_out, F13);
  not not_95 (not_95_out, F14);
  not not_96 (not_96_out, F25);
  not not_97 (not_97_out, OP2);
  not not_98 (not_98_out, OP3);
  not not_99 (not_99_out, OP6);
  not not_100 (not_100_out, F12);
  not not_101 (not_101_out, F25);
  not not_102 (not_102_out, F30);
  not not_103 (not_103_out, OP2);
  not not_104 (not_104_out, OP3);
  not not_105 (not_105_out, OP5);
  not not_106 (not_106_out, OP6);
  not not_107 (not_107_out, F25);
  not not_108 (not_108_out, OP2);
  not not_109 (not_109_out, OP3);
  not not_110 (not_110_out, OP5);
  not not_111 (not_111_out, OP6);
  not not_112 (not_112_out, OP2);
  not not_113 (not_113_out, OP3);
  not not_114 (not_114_out, OP6);
  not not_115 (not_115_out, F25);
  not not_116 (not_116_out, F30);
  not not_117 (not_117_out, OP2);
  not not_118 (not_118_out, OP3);
  not not_119 (not_119_out, OP5);
  not not_120 (not_120_out, OP6);
  not not_121 (not_121_out, F12);
  not not_122 (not_122_out, F14);
  not not_123 (not_123_out, OP2);
  not not_124 (not_124_out, OP3);
  not not_125 (not_125_out, OP6);
  not not_126 (not_126_out, F12);
  not not_127 (not_127_out, F13);
  not not_128 (not_128_out, F14);
  not not_129 (not_129_out, F25);
  not not_130 (not_130_out, OP2);
  not not_131 (not_131_out, OP3);
  not not_132 (not_132_out, OP6);
  not not_133 (not_133_out, F12);
  not not_134 (not_134_out, F25);
  not not_135 (not_135_out, F30);
  not not_136 (not_136_out, OP3);
  not not_137 (not_137_out, OP5);
  not not_138 (not_138_out, OP6);
  not not_139 (not_139_out, F12);
  not not_140 (not_140_out, OP3);
  not not_141 (not_141_out, OP5);
  not not_142 (not_142_out, OP6);
  not not_143 (not_143_out, F13);
  not not_144 (not_144_out, F25);
  not not_145 (not_145_out, F30);
  not not_146 (not_146_out, OP3);
  not not_147 (not_147_out, OP5);
  not not_148 (not_148_out, OP6);
  not not_149 (not_149_out, F25);
  not not_150 (not_150_out, OP3);
  not not_151 (not_151_out, OP5);
  not not_152 (not_152_out, OP6);
  not not_153 (not_153_out, OP2);
  not not_154 (not_154_out, OP3);
  not not_155 (not_155_out, OP6);
  not not_156 (not_156_out, F25);
  not not_157 (not_157_out, F30);
  not not_158 (not_158_out, OP4);
  not not_159 (not_159_out, F12);
  not not_160 (not_160_out, F13);
  not not_161 (not_161_out, F14);
  not not_162 (not_162_out, OP3);
  not not_163 (not_163_out, OP5);
  not not_164 (not_164_out, OP6);
  not not_165 (not_165_out, OP4);
  not not_166 (not_166_out, OP2);
  not not_167 (not_167_out, OP3);
  not not_168 (not_168_out, OP4);
  not not_169 (not_169_out, OP6);
  not not_170 (not_170_out, F12);
  not not_171 (not_171_out, F14);
  not not_172 (not_172_out, OP2);
  not not_173 (not_173_out, OP3);
  not not_174 (not_174_out, F12);
  not not_175 (not_175_out, F13);
  not not_176 (not_176_out, F14);
  not not_177 (not_177_out, OP2);
  not not_178 (not_178_out, OP3);
  not not_179 (not_179_out, OP4);
  not not_180 (not_180_out, F13);
  not not_181 (not_181_out, OP2);
  not not_182 (not_182_out, OP3);
  not not_183 (not_183_out, OP6);
  not not_184 (not_184_out, F12);
  not not_185 (not_185_out, F25);
  not not_186 (not_186_out, F30);
  not not_187 (not_187_out, OP2);
  not not_188 (not_188_out, OP3);
  not not_189 (not_189_out, F12);
  not not_190 (not_190_out, F13);
  not not_191 (not_191_out, F14);
  not not_192 (not_192_out, F25);
  not not_193 (not_193_out, OP2);
  not not_194 (not_194_out, OP3);
  not not_195 (not_195_out, OP6);
  not not_196 (not_196_out, F25);
  not not_197 (not_197_out, F30);
  not not_198 (not_198_out, OP2);
  not not_199 (not_199_out, OP3);
  not not_200 (not_200_out, F12);
  not not_201 (not_201_out, F13);
  not not_202 (not_202_out, F14);
  not not_203 (not_203_out, OP2);
  not not_204 (not_204_out, OP3);
  not not_205 (not_205_out, OP4);
  not not_206 (not_206_out, OP6);
  not not_207 (not_207_out, F12);
  not not_208 (not_208_out, F14);
  not not_209 (not_209_out, OP2);
  not not_210 (not_210_out, OP3);
  not not_211 (not_211_out, OP4);
  not not_212 (not_212_out, F12);
  not not_213 (not_213_out, F13);
  not not_214 (not_214_out, F14);
  not not_215 (not_215_out, OP2);
  not not_216 (not_216_out, OP3);
  not not_217 (not_217_out, OP4);
  not not_218 (not_218_out, F13);
  not not_219 (not_219_out, F14);
  not not_220 (not_220_out, OP3);
  not not_221 (not_221_out, OP4);
  not not_222 (not_222_out, F12);
  not not_223 (not_223_out, F13);
  not not_224 (not_224_out, F14);
  not not_225 (not_225_out, OP4);
  not not_226 (not_226_out, OP2);
  not not_227 (not_227_out, OP3);
  not not_228 (not_228_out, OP3);
  not not_229 (not_229_out, OP5);
  not not_230 (not_230_out, OP6);
  not not_231 (not_231_out, OP2);
  not not_232 (not_232_out, OP3);
  not not_233 (not_233_out, OP4);
  not not_234 (not_234_out, OP5);
  not not_235 (not_235_out, OP6);
  not not_236 (not_236_out, F12);
  not not_237 (not_237_out, F13);
  not not_238 (not_238_out, F14);
  not not_239 (not_239_out, OP2);
  not not_240 (not_240_out, OP3);
  not not_241 (not_241_out, OP4);
  not not_242 (not_242_out, F13);
  and and_1 (MemToReg, not_1_out, not_2_out, not_3_out, not_4_out, not_5_out, not_6_out, not_7_out);
  and and_2 (MemWrite, not_8_out, not_9_out, not_10_out, OP5, not_11_out, not_12_out, F13, not_13_out);
  and and_3 (and_3_out, not_14_out, not_15_out, not_16_out, not_17_out, not_18_out, not_19_out);
  and and_4 (and_4_out, not_20_out, not_21_out, not_22_out, not_23_out, not_24_out, F13, not_25_out);
  and and_5 (and_5_out, not_26_out, not_27_out, OP4, not_28_out, not_29_out, not_30_out);
  and and_6 (and_6_out, not_31_out, not_32_out, OP4, not_33_out, not_34_out, not_35_out, not_36_out, not_37_out);
  and and_7 (and_7_out, not_38_out, not_39_out, OP4, not_40_out, not_41_out, F14, not_42_out);
  and and_8 (and_8_out, not_43_out, not_44_out, OP4, not_45_out, not_46_out, F13, F14);
  and and_9 (and_9_out, OP2, not_47_out, not_48_out, OP5, OP6, not_49_out, not_50_out, not_51_out);
  and and_10 (and_10_out, not_52_out, not_53_out, not_54_out, not_55_out, not_56_out, not_57_out);
  and and_11 (and_11_out, not_58_out, not_59_out, not_60_out, not_61_out, not_62_out, F13, not_63_out);
  and and_12 (and_12_out, not_64_out, not_65_out, OP5, OP6, not_66_out, not_67_out, not_68_out);
  and and_13 (and_13_out, not_69_out, not_70_out, OP5, OP6, not_71_out, not_72_out, not_73_out);
  and and_14 (and_14_out, not_74_out, not_75_out, not_76_out, OP5, OP6, F12, not_77_out);
  and and_15 (and_15_out, not_78_out, not_79_out, OP4, not_80_out, not_81_out, not_82_out);
  and and_16 (and_16_out, not_83_out, not_84_out, OP4, not_85_out, not_86_out, not_87_out, not_88_out, not_89_out);
  and and_17 (and_17_out, not_90_out, not_91_out, OP4, not_92_out, not_93_out, not_94_out, not_95_out, not_96_out);
  and and_18 (and_18_out, not_97_out, not_98_out, OP4, not_99_out, not_100_out, not_101_out, not_102_out);
  and and_19 (and_19_out, not_103_out, not_104_out, OP4, not_105_out, not_106_out, F14, not_107_out);
  and and_20 (and_20_out, not_108_out, not_109_out, OP4, not_110_out, not_111_out, F13, F14);
  and and_21 (and_21_out, not_112_out, not_113_out, OP4, OP5, not_114_out, F13, not_115_out, not_116_out);
  and and_22 (and_22_out, not_117_out, not_118_out, not_119_out, not_120_out, not_121_out, not_122_out);
  and and_23 (and_23_out, not_123_out, not_124_out, OP4, not_125_out, not_126_out, not_127_out, not_128_out, not_129_out);
  and and_24 (and_24_out, not_130_out, not_131_out, OP4, not_132_out, not_133_out, not_134_out, not_135_out);
  and and_25 (and_25_out, not_136_out, OP4, not_137_out, not_138_out, not_139_out);
  and and_26 (and_26_out, not_140_out, OP4, not_141_out, not_142_out, not_143_out, not_144_out, not_145_out);
  and and_27 (and_27_out, not_146_out, OP4, not_147_out, not_148_out, F14, not_149_out);
  and and_28 (and_28_out, not_150_out, OP4, not_151_out, not_152_out, F13, F14);
  and and_29 (and_29_out, not_153_out, not_154_out, OP4, OP5, not_155_out, F13, not_156_out, not_157_out);
  and and_30 (and_30_out, OP2, not_158_out, OP5, OP6, not_159_out, not_160_out, not_161_out);
  and and_31 (and_31_out, OP2, not_162_out, OP4, not_163_out, not_164_out);
  and and_32 (and_32_out, OP2, OP3, not_165_out, OP5, OP6);
  and and_33 (and_33_out, not_166_out, not_167_out, not_168_out, OP5, not_169_out, not_170_out, F13, not_171_out);
  and and_34 (and_34_out, not_172_out, not_173_out, OP5, OP6, not_174_out, not_175_out, not_176_out);
  and and_35 (and_35_out, not_177_out, not_178_out, not_179_out, OP5, OP6, F12, not_180_out);
  and and_36 (and_36_out, not_181_out, not_182_out, OP4, OP5, not_183_out, not_184_out, not_185_out, not_186_out);
  and and_37 (and_37_out, not_187_out, not_188_out, OP4, OP5, not_189_out, not_190_out, not_191_out, not_192_out);
  and and_38 (and_38_out, not_193_out, not_194_out, OP4, OP5, not_195_out, F13, not_196_out, not_197_out);
  and and_39 (ecall, not_198_out, not_199_out, OP4, OP5, OP6, not_200_out, not_201_out, not_202_out);
  and and_40 (S_Type, not_203_out, not_204_out, not_205_out, OP5, not_206_out, not_207_out, F13, not_208_out);
  and and_41 (BEQ, not_209_out, not_210_out, not_211_out, OP5, OP6, not_212_out, not_213_out, not_214_out);
  and and_42 (BNE, not_215_out, not_216_out, not_217_out, OP5, OP6, F12, not_218_out, not_219_out);
  and and_43 (JALR, OP2, not_220_out, not_221_out, OP5, OP6, not_222_out, not_223_out, not_224_out);
  and and_44 (JAL, OP2, OP3, not_225_out, OP5, OP6);
  and and_45 (CSR, not_226_out, not_227_out, OP4, OP5, OP6, F13, F14);
  and and_46 (AUIPC, OP2, not_228_out, OP4, not_229_out, not_230_out);
  and and_47 (LB, not_231_out, not_232_out, not_233_out, not_234_out, not_235_out, not_236_out, not_237_out, not_238_out);
  and and_48 (BGE, not_239_out, not_240_out, not_241_out, OP5, OP6, F12, not_242_out, F14);
  or or_1 (ALU_SRC, and_3_out, and_4_out, and_5_out, and_6_out, and_7_out, and_8_out, and_9_out);
  or or_2 (RTread, and_33_out, and_34_out, and_35_out, and_36_out, and_37_out, and_38_out);
  or or_3 (RSread, and_10_out, and_11_out, and_12_out, and_13_out, and_14_out, and_15_out, and_16_out, and_17_out, and_18_out, and_19_out, and_20_out, and_21_out);
  or or_4 (RegWrite, and_22_out, and_23_out, and_24_out, and_25_out, and_26_out, and_27_out, and_28_out, and_29_out, and_30_out, and_31_out, and_32_out);
endmodule

// ALU
module ALU (
  input  [31:0] X,
  input  [31:0] Y,
  input  [3:0] AluOP,
  output out_4,
  output Equal,
  output out_6,
  output [31:0] Result,
  output [31:0] Result_2
);

  wire [0:0] comparator_1_lt, comparator_2_lt;
  wire [31:0] adder_1_out, AND_out, divider_1_out, divider_1_rem, multiplier_1_cout, multiplier_1_out,
       NOR_out, OR_out, shifter_1_out, shifter_2_out, shifter_3_out, subtractor_1_out, XOR_out;

  assign AND_out = X & Y;  // AND_Gate AND, 32 bits wide
  assign OR_out = X | Y;  // OR_Gate OR, 32 bits wide
  Shifter #(.width(32), .shift("ll")) shifter_1 (.in(X), .\dist (Y[4:0]), .out(shifter_1_out));
  Shifter #(.width(32), .shift("ar")) shifter_2 (.in(X), .\dist (Y[4:0]), .out(shifter_2_out));
  Shifter #(.width(32), .shift("lr")) shifter_3 (.in(X), .\dist (Y[4:0]), .out(shifter_3_out));
  Multiplier #(.width(32)) multiplier_1 (.a(X), .b(Y), .out(multiplier_1_out), .cout(multiplier_1_cout));  // open: cin
  Divider #(.width(32)) divider_1 (.a(X), .b(Y), .out(divider_1_out), .rem(divider_1_rem));  // open: upper
  Adder #(.width(32)) adder_1 (.a(X), .b(Y), .out(adder_1_out));  // open: cin, cout
  Subtractor #(.width(32)) subtractor_1 (.a(X), .b(Y), .out(subtractor_1_out));  // open: bin, bout
  assign XOR_out = X ^ Y;  // XOR_Gate XOR, 32 bits wide
  assign NOR_out = ~(X | Y);  // NOR_Gate NOR, 32 bits wide
  Comparator #(.width(32), .mode("twosComplement")) comparator_1 (
    .a(X), .b(Y), .eq(Equal), .lt(comparator_1_lt[0]));  // open: gt
  Comparator #(.width(32), .mode("unsigned")) comparator_2 (.a(X), .b(Y), .lt(comparator_2_lt[0]));  // open: gt, eq
  Multiplexer #(.select(4), .width(32), .disabled("Z"), .enable("false")) multiplexer_1 (
    .in0(shifter_1_out), .in1(shifter_2_out), .in2(shifter_3_out), .in3(multiplier_1_out),
    .in4(divider_1_out), .in5(adder_1_out), .in6(subtractor_1_out), .in7(AND_out), .in8(OR_out),
    .in9(XOR_out), .in10(NOR_out), .in11({{31{1'b0}}, comparator_1_lt[0]}),
    .in12({{31{1'b0}}, comparator_2_lt[0]}), .in13({32{1'b0}}), .in14({32{1'b0}}), .in15({32{1'b0}}),
    .out(Result), .sel(AluOP));
  Multiplexer #(.select(4), .width(32), .disabled("Z"), .enable("false")) multiplexer_2 (
    .in0({32{1'b0}}), .in1({32{1'b0}}), .in2({32{1'b0}}), .in3(multiplier_1_cout), .in4(divider_1_rem),
    .in5({32{1'b0}}), .in6({32{1'b0}}), .in7({32{1'b0}}), .in8({32{1'b0}}), .in9({32{1'b0}}),
    .in10({32{1'b0}}), .in11({32{1'b0}}), .in12({32{1'b0}}), .in13({32{1'b0}}), .in14({32{1'b0}}),
    .in15({32{1'b0}}), .out(Result_2), .sel(AluOP));
  Multiplexer #(.select(4), .width(1), .disabled("Z"), .enable("false")) multiplexer_3 (
    .in0(1'b0), .in1(1'b0), .in2(1'b0), .in3(1'b0), .in4(1'b0), .in5(1'b0), .in6(1'b0), .in7(1'b0),
    .in8(1'b0), .in9(1'b0), .in10(1'b0), .in11(comparator_1_lt[0]), .in12(comparator_2_lt[0]), .in13(1'b0),
    .in14(1'b0), .in15(1'b0), .out(out_6), .sel(AluOP));
  not not_1 (out_4, out_6);

  // Other names for the same wires on the sheet: Result2[31:0] = Result_2; S[3:0] = AluOP; tunnel = out_6;
  //   tunnel_t = out_4

  // Notes on the sheet:
  //   不要改变此引脚区域内容，也不要改变ALU封装形式
  //   输入引脚
  //   输出引脚
endmodule

module Regifile (
  input  [31:0] Din,
  input  Clk,
  input  WE,
  input  [4:0] R1_num,
  input  [4:0] W_num,
  input  [4:0] R2_num,
  output [31:0] R1,
  output [31:0] R2
);

  // RegisterFile registerfile_1: pin names not known; wires that end beside it: Din, Clk, WE, W_num, R1_num, R2_num, R1, R2
endmodule

module \理想流水线  (
  output RegWrite,
  output MemWrite,
  output [31:0] IF_PC,
  output [31:0] ID_PC,
  output [31:0] EX_PC,
  output [31:0] M_PC,
  output [31:0] WB_PC,
  output [31:0] RDin,
  output [31:0] MDin,
  output [31:0] LedData
);

  wire and_1_out, and_2_out, and_3_out, and_4_out, and_5_out, and_6_out, CLK, clock_1_out, comparator_1_eq,
       comparator_2_eq, comparator_2_lt, d_ff_1_q, EN, EX_Aluequal, EX_Alugreatequal, EX_Aluless, EX_AluSrcB,
       EX_AUIPC, EX_BE, EX_BEQ, EX_BGE, EX_BNE, EX_ecall, EX_JAL, EX_JALR, EX_LB, EX_MemToReg, EX_MemWrite,
       EX_RegWrite, EX_S_type, Go, halt, ID_AluSrcB, ID_AUIPC, ID_BEQ, ID_BGE, ID_BNE, ID_CSR, ID_ecall,
       ID_JAL, ID_JALR, ID_LB, ID_MemToReg, ID_MemWrite, ID_RegWrite, ID_S_type, ID_URET, IR1, IR2, IR3,
       MEM_AluSrcB, MEM_AUIPC, MEM_BE, MEM_BEQ, MEM_BGE, MEM_ecall, MEM_JAL, MEM_JALR, MEM_LB, MEM_MemToReg,
       MEM_RegWrite, MEM_S_type, nand_1_out, not_2_out, not_3_out, not_4_out, not_5_out, not_6_out,
       not_7_out, or_2_out, RST, W1, W2, W3, WB_AluSrcB, WB_AUIPC, WB_BE, WB_BEQ, WB_BGE, WB_BNE, WB_ecall,
       WB_JAL, WB_JALR, WB_LB, WB_MemToReg, WB_MemWrite, WB_S_type;
  wire [3:0] EX_AluOP, ID_AluOP, MEM_AluOP, WB_AluOP;
  wire [4:0] EX_W_num, funct, MEM_W_num, multiplexer_3_out, multiplexer_4_out, WB_W_num;
  wire [7:0] multiplexer_8_out;
  wire [11:0] multiplexer_5_out;
  wire [12:0] CNT_num;
  wire [15:0] \LoadUse次数 , \总周期数 , \插入气泡数 , \无条件分支数 , \条件分支成功数 ;
  wire [31:0] bit_extender_2_out, bit_extender_3_out, bit_extender_4_out, EX_AUIPCresult, EX_BEaddr, EX_imm,
       EX_IR, EX_JALaddr, EX_nextPC, EX_R1, EX_R2, EX_Result, ID_AUIPCresult, ID_BEaddr, ID_imm, ID_IR,
       ID_JALaddr, ID_nextPC, ID_R1, ID_R2, IF_IR, IF_nextPC, MEM_ALUout, MEM_BEaddr, MEM_imm, MEM_IR,
       MEM_JALaddr, MEM_nextPC, MEM_R1, mem_wb_1_aluresultout, mem_wb_1_memout, multiplexer_6_out,
       multiplexer_7_out, multiplexer_9_out, multiplexer_10_out, ram_1_data, shifter_1_out, shifter_2_out,
       WB_BEaddr, WB_imm, WB_IR, WB_JALaddr, WB_nextPC;

  Button \u_总复位  (.out(RST));
  Button _1 (.out(IR1));
  Button _2 (.out(IR2));
  Button _3 (.out(IR3));
  // Probe on \总周期数 
  // Probe on \总周期数 
  Button \u_继续运行  (.out(Go));
  LED #(.active("true")) led_1 (.in(W1));
  LED #(.active("true")) led_2 (.in(W2));
  LED #(.active("true")) led_3 (.in(W3));
  Register #(.width(32), .trigger("rising"), .Select("low")) PC (
    .D(IF_nextPC), .en(EN), .Q(IF_PC), .clk(CLK), .clr(RST));
  Hex_Digit_Display hex_digit_display_1 (.value(LedData[31:28]));  // open: dp
  // Probe on IF_PC[19:0]
  // RiscV_Probe riscv_probe_1: pin names not known; wires that end beside it: IF_IR
  not not_1 (EN, halt);
  not not_2 (not_2_out, WB_ecall);
  Counter #(.width(16), .max('hffff), .ongoal("wrap"), .trigger("rising"), .behavior("new")) counter_1 (
    .D({16{1'b0}}), .count(not_2_out), .Q(\总周期数 ), .clk(CLK));  // open: load, carry, clr, preset, down
  Hex_Digit_Display hex_digit_display_2 (.value(LedData[27:24]));  // open: dp
  Hex_Digit_Display hex_digit_display_3 (.value(LedData[23:20]));  // open: dp
  // Probe on ID_PC[19:0]
  // RiscV_Probe riscv_probe_2: pin names not known; wires that end beside it: {ID_IR[31], funct[4], ID_IR[29:26], funct[3], ID_IR[24:15], funct[2], ID_IR[13:0]}
  Adder #(.width(32)) adder_1 (.a(IF_PC), .b(32'h4), .out(IF_nextPC));  // open: cin, cout
  Hex_Digit_Display hex_digit_display_4 (.value(LedData[19:16]));  // open: dp
  Hex_Digit_Display hex_digit_display_5 (.value(LedData[15:12]));  // open: dp
  ROM #(.addrWidth(10), .dataWidth(32), .Select("high")) \u_指令存储器  (.addr(IF_PC[11:2]), .data(IF_IR));
  Hex_Digit_Display hex_digit_display_6 (.value(LedData[7:4]));  // open: dp
  Hex_Digit_Display hex_digit_display_7 (.value(LedData[11:8]));  // open: dp
  // Probe on EX_PC[19:0]
  // RiscV_Probe riscv_probe_3: pin names not known; wires that end beside it: EX_IR
  // RiscV_Probe riscv_probe_4: pin names not known; wires that end beside it: IF_IR
  Hex_Digit_Display hex_digit_display_8 (.value(LedData[3:0]));  // open: dp
  Comparator #(.width(32), .mode("twosComplement")) comparator_1 (
    .a(ID_R1), .b(32'h22), .eq(comparator_1_eq));  // open: gt, lt
  // Probe on \总周期数 
  // Probe on M_PC[19:0]
  // RiscV_Probe riscv_probe_5: pin names not known; wires that end beside it: MEM_IR
  IF_ID if_id_1 (
    .PCin(IF_PC), .nextPCin(IF_nextPC), .IRin(IF_IR), .EN(EN), .CLK(CLK), .RESET(1'b0), .PCout(ID_PC),
    .nextPCout(ID_nextPC),
    .IRout({ID_IR[31], funct[4], ID_IR[29:26], funct[3], ID_IR[24:15], funct[2], ID_IR[13:0]}));
  not not_3 (not_3_out, comparator_1_eq);
  and and_1 (and_1_out, comparator_1_eq, WB_ecall);
  Register #(.width(32), .trigger("rising"), .Select("low")) register_1 (
    .D(ID_R2), .en(and_1_out), .Q(LedData), .clk(CLK));  // open: clr
  // Probe on \总周期数 
  // Probe on \无条件分支数 
  // Probe on \条件分支成功数 
  // Probe on \插入气泡数 
  // Probe on \LoadUse次数 
  // RiscV_Probe riscv_probe_6: pin names not known; wires that end beside it: {ID_IR[31], funct[4], ID_IR[29:26], funct[3], ID_IR[24:15], funct[2], ID_IR[13:0]}
  and and_2 (and_2_out, WB_ecall, not_3_out);
  Multiplexer #(.select(1), .width(1), .disabled("Z"), .enable("false")) multiplexer_1 (
    .in0(and_2_out), .in1(1'b0), .out(halt), .sel(Go));
  // Probe on IF_PC[11:0]
  // Probe on WB_PC[19:0]
  // RiscV_Probe riscv_probe_7: pin names not known; wires that end beside it: WB_IR
  and and_3 (and_3_out, not_4_out, not_5_out);
  not not_4 (not_4_out, ID_IR[0]);
  not not_5 (not_5_out, ID_IR[1]);
  // Probe on ID_PC[11:0]
  // Probe on EX_PC[11:0]
  Multiplexer #(.select(1), .width(2), .disabled("Z"), .enable("false")) multiplexer_2 (
    .in0(ID_IR[13:12]), .in1(2'b11), .out(funct[1:0]), .sel(and_3_out));
  // Probe on M_PC[11:0]
  D_Flip_Flop #(.trigger("high"), .Pre_Clr_Positions("LEGACY"), .NegatePresetClear("false"), .enable("true"), .NewFFLayout("false")) d_ff_1 (.Q(d_ff_1_q));  // open: clk, D, Qn, preset, en, reset
  // Probe on 13'h2
  // Probe on WB_PC[11:0]
  Comparator #(.width(13), .mode("twosComplement")) comparator_2 (
    .a(CNT_num), .b(13'h2), .eq(comparator_2_eq), .lt(comparator_2_lt));  // open: gt
  Clock #(.highDuration(1), .lowDuration(1)) clock_1 (.out(clock_1_out));
  nand nand_1 (nand_1_out, d_ff_1_q, comparator_2_eq);
  Counter #(.width(13), .max('h1fff), .ongoal("stay"), .trigger("rising"), .behavior("old")) counter_2 (
    .count(comparator_2_lt), .Q(CNT_num), .clk(clock_1_out));  // open: load, D, carry, clr, preset
  \单周期硬布线控制器  \u_单周期硬布线控制器_1  (
    .Funct(funct), .OP(ID_IR[6:2]), .ALU_OP(ID_AluOP), .MemToReg(ID_MemToReg), .MemWrite(ID_MemWrite),
    .ALU_SRC(ID_AluSrcB), .RegWrite(ID_RegWrite), .ecall(ID_ecall), .S_type(ID_S_type), .Jalr(ID_JALR),
    .Beq(ID_BEQ), .JAL(ID_JAL), .Bne(ID_BNE), .in_3(ID_IR[21]), .uret(ID_URET), .CSR(ID_CSR),
    .AUIPC(ID_AUIPC), .LB(ID_LB), .BGE(ID_BGE));  // open: RSread, RTread
  Multiplexer #(.select(1), .width(5), .disabled("Z"), .enable("false")) multiplexer_3 (
    .in0(ID_IR[19:15]), .in1(5'b10001), .out(multiplexer_3_out), .sel(ID_ecall));
  Multiplexer #(.select(1), .width(5), .disabled("Z"), .enable("false")) multiplexer_4 (
    .in0(ID_IR[24:20]), .in1(5'b01010), .out(multiplexer_4_out), .sel(ID_ecall));
  Multiplexer #(.select(1), .width(12), .disabled("Z"), .enable("false")) multiplexer_5 (
    .in0({ID_IR[31], funct[4], ID_IR[29:26], funct[3], ID_IR[24:20]}),
    .in1({ID_IR[31], funct[4], ID_IR[29:26], funct[3], ID_IR[11:7]}), .out(multiplexer_5_out), .sel(ID_S_type));
  assign CLK = nand_1_out ? clock_1_out : 1'bz;  // Controlled_Buffer controlled_buffer_1
  Pull_Resistor #(.pull(1)) pull_resistor_1 (.node(CLK));
  assign ID_imm = {{20{multiplexer_5_out[11]}}, multiplexer_5_out};  // Bit_Extender bit_extender_1
  assign bit_extender_2_out = {{20{ID_IR[31]}}, {ID_IR[31], ID_IR[7], funct[4], ID_IR[29:26], funct[3], ID_IR[11:8]}};  // Bit_Extender bit_extender_2
  assign bit_extender_3_out = {{12{ID_IR[31]}}, {ID_IR[31], ID_IR[19:15], funct[2], ID_IR[13:12], ID_IR[20], funct[4], ID_IR[29:26], funct[3], ID_IR[24:21]}};  // Bit_Extender bit_extender_3
  Regifile regifile_1 (
    .Din(RDin), .Clk(CLK), .R1(ID_R1), .R2(ID_R2), .WE(RegWrite), .W_num(WB_W_num),
    .R1_num(multiplexer_3_out), .R2_num(multiplexer_4_out));
  Shifter #(.width(32), .shift("ll")) shifter_1 (.in(bit_extender_2_out), .\dist (5'b00001), .out(shifter_1_out));
  Shifter #(.width(32), .shift("ll")) shifter_2 (.in(bit_extender_3_out), .\dist (5'b00001), .out(shifter_2_out));
  Adder #(.width(32)) adder_2 (.a(shifter_1_out), .b(ID_PC), .out(ID_BEaddr), .cin(1'b0));  // open: cout
  Adder #(.width(32)) adder_3 (.a(shifter_2_out), .b(ID_PC), .out(ID_JALaddr), .cin(1'b0));  // open: cout
  Adder #(.width(32)) adder_4 (
    .a({ID_IR[31], funct[4], ID_IR[29:26], funct[3], ID_IR[24:15], funct[2], ID_IR[13:12], {12{1'b0}}}),
    .b(ID_PC), .out(ID_AUIPCresult), .cin(1'b0));  // open: cout
  ID_EX id_ex_1 (
    .RegWritein(ID_RegWrite), .MemToRegin(ID_MemToReg), .MemWritein(ID_MemWrite), .ALUOPin(ID_AluOP),
    .ALUSrcin(ID_AluSrcB), .ecallin(ID_ecall), .S_typein(ID_S_type), .BEQin(ID_BEQ), .BNEin(ID_BNE),
    .JALin(ID_JAL), .JALRin(ID_JALR), .AUIPCin(ID_AUIPC), .LBin(ID_LB), .BGEin(ID_BGE), .R1in(ID_R1),
    .R2in(ID_R2), .W_in(ID_IR[11:7]), .immin(ID_imm), .BEaddrin(ID_BEaddr), .PCin(ID_PC),
    .nextPCin(ID_nextPC), .JALaddrin(ID_JALaddr),
    .IRin({ID_IR[31], funct[4], ID_IR[29:26], funct[3], ID_IR[24:15], funct[2], ID_IR[13:0]}), .RESET(1'b0),
    .EN(EN), .CLK(CLK), .RegWriteout(EX_RegWrite), .MemToRegout(EX_MemToReg), .MemWriteout(EX_MemWrite),
    .ALUOPout(EX_AluOP), .ALUSrcout(EX_AluSrcB), .ecallout(EX_ecall), .S_typeout(EX_S_type), .BEQout(EX_BEQ),
    .BNEout(EX_BNE), .JALout(EX_JAL), .JALRout(EX_JALR), .AUIPCout(EX_AUIPC), .LBout(EX_LB), .BGEout(EX_BGE),
    .R1out(EX_R1), .R2out(EX_R2), .W_out(EX_W_num), .immout(EX_imm), .BEaddrout(EX_BEaddr), .PCout(EX_PC),
    .nextPCout(EX_nextPC), .JALaddrout(EX_JALaddr), .IRout(EX_IR), .AUIPCresin(ID_AUIPCresult),
    .AUIPCresout(EX_AUIPCresult));  // open: RS_Fin, RS_Fout, RT_Fin, RT_Fout
  Multiplexer #(.select(1), .width(32), .disabled("Z"), .enable("false")) multiplexer_6 (
    .in0(EX_R2), .in1(EX_imm), .out(multiplexer_6_out), .sel(EX_AluSrcB));
  ALU alu_1 (
    .X(EX_R1), .Y(multiplexer_6_out), .AluOP(EX_AluOP), .Equal(EX_Aluequal), .Result(EX_Result),
    .out_4(EX_Alugreatequal), .out_6(EX_Aluless));  // open: Result_2
  not not_6 (not_6_out, EX_Aluequal);
  and and_4 (and_4_out, EX_Aluequal, EX_BEQ);
  and and_5 (and_5_out, not_6_out, EX_BNE);
  and and_6 (and_6_out, EX_Alugreatequal, EX_BGE);
  or or_1 (EX_BE, and_4_out, and_5_out, and_6_out);
  Multiplexer #(.select(1), .width(32), .disabled("Z"), .enable("false")) multiplexer_7 (
    .in0(EX_Result), .in1(EX_AUIPCresult), .out(multiplexer_7_out), .sel(EX_AUIPC));
  EX_MEM ex_mem_1 (
    .RegWritein(EX_RegWrite), .MemToRegin(EX_MemToReg), .MemWritein(EX_MemWrite), .ALUOPin(EX_AluOP),
    .ALUSrcin(EX_AluSrcB), .ecallin(EX_ecall), .S_typein(EX_S_type), .BEQin(EX_BEQ), .BNEin(EX_BNE),
    .JALin(EX_JAL), .JALRin(EX_JALR), .AUIPCin(EX_AUIPC), .LBin(EX_LB), .BGEin(EX_BGE), .R1in(EX_R1),
    .R2in(EX_R2), .W_in(EX_W_num), .immin(EX_imm), .BEaddrin(EX_BEaddr), .PCin(EX_PC), .nextPCin(EX_nextPC),
    .JALaddrin(EX_JALaddr), .IRin(EX_IR), .BEin(EX_BE), .ALUResultin(multiplexer_7_out), .RESET(1'b0),
    .EN(EN), .CLK(CLK), .RegWriteout(MEM_RegWrite), .MemToRegout(MEM_MemToReg), .MemWriteout(MemWrite),
    .ALUOPout(MEM_AluOP), .ALUSrcout(MEM_AluSrcB), .ecallout(MEM_ecall), .S_typeout(MEM_S_type),
    .BEQout(MEM_BEQ), .BNEout(MEM_BEQ), .JALout(MEM_JAL), .JALRout(MEM_JALR), .AUIPCout(MEM_AUIPC),
    .LBout(MEM_LB), .BGEout(MEM_BGE), .R1out(MEM_R1), .R2out(MDin), .W_out(MEM_W_num), .immout(MEM_imm),
    .BEaddrout(MEM_BEaddr), .PCout(M_PC), .nextPCout(MEM_nextPC), .JALaddrout(MEM_JALaddr), .IRout(MEM_IR),
    .BEout(MEM_BE), .ALUResultout(MEM_ALUout));
  not not_7 (not_7_out, MemWrite);
  RAM #(.addrWidth(10), .dataWidth(32), .bus("separate"), .Select("high")) ram_1 (
    .addr(MEM_ALUout[11:2]), .din(MDin), .data(ram_1_data), .str(MemWrite), .clk(CLK), .ld(not_7_out));  // open: sel, clr
  Multiplexer #(.select(2), .width(8), .disabled("Z"), .enable("false")) multiplexer_8 (
    .in0(ram_1_data[7:0]), .in1(ram_1_data[15:8]), .in2(ram_1_data[23:16]), .in3(ram_1_data[31:24]),
    .out(multiplexer_8_out), .sel(MEM_ALUout[1:0]));
  assign bit_extender_4_out = {{24{multiplexer_8_out[7]}}, multiplexer_8_out};  // Bit_Extender bit_extender_4
  Multiplexer #(.select(1), .width(32), .disabled("Z"), .enable("false")) multiplexer_9 (
    .in0(ram_1_data), .in1(bit_extender_4_out), .out(multiplexer_9_out), .sel(MEM_LB));
  MEM_WB mem_wb_1 (
    .RegWritein(MEM_RegWrite), .MemToRegin(MEM_MemToReg), .MemWritein(MemWrite), .ALUOPin(MEM_AluOP),
    .ALUSrcin(MEM_AluSrcB), .ecallin(MEM_ecall), .S_typein(MEM_S_type), .BEQin(MEM_BEQ), .BNEin(MEM_BEQ),
    .JALin(MEM_JAL), .JALRin(MEM_JALR), .AUIPCin(MEM_AUIPC), .LBin(MEM_LB), .BGEin(MEM_BGE),
    .W_in(MEM_W_num), .immin(MEM_imm), .BEaddrin(MEM_BEaddr), .PCin(M_PC), .nextPCin(MEM_nextPC),
    .JALaddrin(MEM_JALaddr), .IRin(MEM_IR), .BEin(MEM_BE), .ALUResultin(MEM_ALUout), .RESET(1'b0), .EN(EN),
    .CLK(CLK), .RegWriteout(RegWrite), .MemToRegout(WB_MemToReg), .MemWriteout(WB_MemWrite),
    .ALUOPout(WB_AluOP), .ALUSrcout(WB_AluSrcB), .ecallout(WB_ecall), .S_typeout(WB_S_type), .BEQout(WB_BEQ),
    .BNEout(WB_BNE), .JALout(WB_JAL), .JALRout(WB_JALR), .AUIPCout(WB_AUIPC), .LBout(WB_LB), .BGEout(WB_BGE),
    .W_out(WB_W_num), .immout(WB_imm), .BEaddrout(WB_BEaddr), .PCout(WB_PC), .nextPCout(WB_nextPC),
    .JALaddrout(WB_JALaddr), .IRout(WB_IR), .BEout(WB_BE), .ALUResultout(mem_wb_1_aluresultout),
    .Memin(multiplexer_9_out), .Memout(mem_wb_1_memout));  // open: R1in, R1out, R2in, R2out
  Multiplexer #(.select(1), .width(32), .disabled("Z"), .enable("false")) multiplexer_10 (
    .in0(mem_wb_1_aluresultout), .in1(mem_wb_1_memout), .out(multiplexer_10_out), .sel(WB_MemToReg));
  or or_2 (or_2_out, WB_JAL, MEM_JALR);
  Multiplexer #(.select(1), .width(32), .disabled("Z"), .enable("false")) multiplexer_11 (
    .in0(multiplexer_10_out), .in1(WB_nextPC), .out(RDin), .sel(or_2_out));

  // Other names for the same wires on the sheet: ID_W_num[4:0] = ID_IR[11:7]; ID_IR (some bits) = funct[4:2];
  //   MEM_BNE = MEM_BEQ; MEM_MemWrite = MemWrite; MEM_PC[31:0] = M_PC; MEM_R2[31:0] = MDin; WB_RegWrite = RegWrite

  // Notes on the sheet:
  //   中断源
  //   时空图监测，可删除
  //   中断等待指示
  //   数码管输出
  //   contents of 指令存储器 (hex, n*v repeats v):
  //   413 493 913 993 46413 14e493 296913 39e993 842023 942223 1242423 1342623 a00893 493 913 993 73
  //   指令探针
  //   控制位
  //   流水调试日志用
  //   暂停节拍，不能为0
  //   戳工具置1进入计数暂停模式，ctrl+k时钟自动运行到对应节拍暂停
  //   ctrl+k关闭时钟连续运行，将控制位置零，进入单步调试模式调试
  //   用这个时钟源需要去掉电路中的其他时钟源
  //   JALR
  //   URET
  //   Bne
  //   AluOP
  //   AluSrcB
  //   RegWrite
  //   可计数暂停的时钟源
  //   MemToReg
  //   MemWrite
  //   为方便自动评测，需要输出流水线各段保存的PC值，注意是PC不是PC+4，另外ID段寄存器写入信息，Mem段内存写入信息也要输出
endmodule

module \气泡流水线  (
  output RegWrite,
  output MemWrite,
  output [31:0] IF_PC,
  output [31:0] ID_PC,
  output [31:0] EX_PC,
  output [31:0] M_PC,
  output [31:0] WB_PC,
  output [31:0] RDin,
  output [31:0] MDin,
  output [31:0] LedData
);

  wire and_1_out, and_2_out, and_3_out, and_4_out, and_6_out, and_7_out, and_8_out, bubble, CLK, clock_1_out,
       comparator_1_eq, comparator_2_eq, comparator_2_lt, d_ff_1_q, EN, EX_Aluequal, EX_Alugreatequal,
       EX_Aluless, EX_AluSrcB, EX_AUIPC, EX_BE, EX_BEQ, EX_BGE, EX_BNE, EX_Branch, EX_ecall, EX_JAL, EX_JALR,
       EX_JUMP, EX_LB, EX_MemToReg, EX_MemWrite, EX_RegWrite, EX_S_type, Go, halt, ID_AluSrcB, ID_AUIPC,
       ID_BEQ, ID_BGE, ID_BNE, ID_CSR, ID_ecall, ID_JAL, ID_JALR, ID_LB, ID_MemToReg, ID_MemWrite,
       ID_RegWrite, ID_S_type, ID_URET, IR1, IR2, IR3, MEM_AluSrcB, MEM_AUIPC, MEM_BE, MEM_BEQ, MEM_BGE,
       MEM_ecall, MEM_JAL, MEM_JALR, MEM_LB, MEM_MemToReg, MEM_RegWrite, MEM_S_type, nand_1_out, nor_1_out,
       nor_2_out, not_2_out, not_3_out, not_4_out, not_5_out, not_6_out, not_7_out, not_9_out, or_1_out,
       or_5_out, RST, W1, W2, W3, WB_AluSrcB, WB_AUIPC, WB_BE, WB_BEQ, WB_BGE, WB_BNE, WB_ecall, WB_JAL,
       WB_JALR, WB_LB, WB_MemToReg, WB_MemWrite, WB_S_type, \单周期硬布线控制器_1_rsread , \单周期硬布线控制器_1_rtread ;
  wire [3:0] EX_AluOP, ID_AluOP, MEM_AluOP, WB_AluOP;
  wire [4:0] EX_W_num, funct, MEM_W_num, RSid, RTid, WB_W_num;
  wire [7:0] multiplexer_10_out;
  wire [11:0] multiplexer_4_out;
  wire [12:0] CNT_num;
  wire [15:0] \LoadUse次数 , \总周期数 , \插入气泡数 , \无条件分支数 , \条件分支成功数 ;
  wire [31:0] and_9_out, bit_extender_1_out, bit_extender_2_out, bit_extender_4_out, EX_AUIPCresult,
       EX_BEaddr, EX_imm, EX_IR, EX_JALaddr, EX_nextPC, EX_R1, EX_R2, EX_Result, ID_AUIPCresult, ID_BEaddr,
       ID_imm, ID_IR, ID_JALaddr, ID_nextPC, ID_R1, ID_R2, IF_IR, IF_nextPC, MEM_ALUout, MEM_BEaddr, MEM_imm,
       MEM_IR, MEM_JALaddr, MEM_nextPC, MEM_R1, mem_wb_1_aluresultout, mem_wb_1_memout, multiplexer_5_out,
       multiplexer_6_out, multiplexer_7_out, multiplexer_9_out, multiplexer_11_out, multiplexer_12_out,
       not_8_out, PCaddr, ram_1_data, shifter_1_out, shifter_2_out, WB_BEaddr, WB_imm, WB_IR, WB_JALaddr,
       WB_nextPC, WB_R1, WB_R2;

  Button \u_总复位  (.out(RST));
  Button _1 (.out(IR1));
  Button _2 (.out(IR2));
  Button _3 (.out(IR3));
  // Probe on \总周期数 
  // Probe on \总周期数 
  Button \u_继续运行  (.out(Go));
  LED #(.active("true")) led_1 (.in(W1));
  LED #(.active("true")) led_2 (.in(W2));
  LED #(.active("true")) led_3 (.in(W3));
  Hex_Digit_Display hex_digit_display_1 (.value(LedData[31:28]));  // open: dp
  // Probe on IF_PC[19:0]
  // RiscV_Probe riscv_probe_1: pin names not known; wires that end beside it: IF_IR
  Register #(.width(32), .trigger("rising"), .Select("low")) PC (
    .D(PCaddr), .en(nor_1_out), .Q(IF_PC), .clk(CLK), .clr(RST));
  nor nor_1 (nor_1_out, halt, bubble);
  Hex_Digit_Display hex_digit_display_2 (.value(LedData[23:20]));  // open: dp
  Hex_Digit_Display hex_digit_display_3 (.value(LedData[27:24]));  // open: dp
  // Probe on ID_PC[19:0]
  // RiscV_Probe riscv_probe_2: pin names not known; wires that end beside it: {ID_IR[31], funct[4], ID_IR[29:26], funct[3], ID_IR[24:15], funct[2], ID_IR[13:0]}
  not not_1 (EN, halt);
  Counter #(.width(16), .max('hffff), .ongoal("wrap"), .trigger("rising"), .behavior("new")) counter_1 (
    .D({16{1'b0}}), .Q(\总周期数 ), .clk(and_1_out));  // open: load, count, carry, clr, preset, down
  and and_1 (and_1_out, CLK, not_2_out);
  not not_2 (not_2_out, WB_ecall);
  Hex_Digit_Display hex_digit_display_4 (.value(LedData[19:16]));  // open: dp
  Hex_Digit_Display hex_digit_display_5 (.value(LedData[15:12]));  // open: dp
  Adder #(.width(32)) adder_1 (.a(IF_PC), .b(32'h4), .out(IF_nextPC));  // open: cin, cout
  Hex_Digit_Display hex_digit_display_6 (.value(LedData[11:8]));  // open: dp
  Hex_Digit_Display hex_digit_display_7 (.value(LedData[7:4]));  // open: dp
  // Probe on EX_PC[19:0]
  // RiscV_Probe riscv_probe_3: pin names not known; wires that end beside it: EX_IR
  ROM #(.addrWidth(10), .dataWidth(32), .Select("high")) \u_指令存储器  (.addr(IF_PC[11:2]), .data(IF_IR));
  Hex_Digit_Display hex_digit_display_8 (.value(LedData[3:0]));  // open: dp
  // RiscV_Probe riscv_probe_4: pin names not known; wires that end beside it: IF_IR
  // Probe on \总周期数 
  // Probe on M_PC[19:0]
  // RiscV_Probe riscv_probe_5: pin names not known; wires that end beside it: MEM_IR
  nor nor_2 (nor_2_out, halt, bubble);
  Comparator #(.width(32), .mode("twosComplement")) comparator_1 (
    .a(WB_R1), .b(32'h22), .eq(comparator_1_eq));  // open: gt, lt
  and and_2 (and_2_out, comparator_1_eq, WB_ecall);
  // Probe on \总周期数 
  // Probe on \无条件分支数 
  // Probe on \条件分支成功数 
  // Probe on \插入气泡数 
  // Probe on \LoadUse次数 
  IF_ID if_id_1 (
    .PCin(IF_PC), .nextPCin(IF_nextPC), .IRin(IF_IR), .EN(nor_2_out), .CLK(CLK), .RESET(EX_Branch),
    .PCout(ID_PC), .nextPCout(ID_nextPC),
    .IRout({ID_IR[31], funct[4], ID_IR[29:26], funct[3], ID_IR[24:15], funct[2], ID_IR[13:0]}));
  and and_3 (and_3_out, WB_ecall, not_3_out);
  not not_3 (not_3_out, comparator_1_eq);
  Register #(.width(32), .trigger("rising"), .Select("low")) register_1 (
    .D(WB_R2), .en(and_2_out), .Q(LedData), .clk(CLK));  // open: clr
  // Probe on IF_PC[11:0]
  // Probe on WB_PC[19:0]
  // RiscV_Probe riscv_probe_6: pin names not known; wires that end beside it: WB_IR
  // RiscV_Probe riscv_probe_7: pin names not known; wires that end beside it: {ID_IR[31], funct[4], ID_IR[29:26], funct[3], ID_IR[24:15], funct[2], ID_IR[13:0]}
  not not_4 (not_4_out, ID_IR[0]);
  not not_5 (not_5_out, ID_IR[1]);
  not not_6 (not_6_out, Go);
  // Probe on EX_PC[11:0]
  // Probe on ID_PC[11:0]
  and and_4 (and_4_out, not_4_out, not_5_out);
  and and_5 (halt, not_6_out, and_3_out);
  // Probe on M_PC[11:0]
  D_Flip_Flop #(.trigger("high"), .Pre_Clr_Positions("LEGACY"), .NegatePresetClear("false"), .enable("true"), .NewFFLayout("false")) d_ff_1 (.Q(d_ff_1_q));  // open: clk, D, Qn, preset, en, reset
  // Probe on 13'h48
  Multiplexer #(.select(1), .width(2), .disabled("Z"), .enable("false")) multiplexer_1 (
    .in0(ID_IR[13:12]), .in1(2'b11), .out(funct[1:0]), .sel(and_4_out));
  // Probe on WB_PC[11:0]
  Comparator #(.width(13), .mode("twosComplement")) comparator_2 (
    .a(CNT_num), .b(13'h48), .eq(comparator_2_eq), .lt(comparator_2_lt));  // open: gt
  Clock #(.highDuration(1), .lowDuration(1)) clock_1 (.out(clock_1_out));
  nand nand_1 (nand_1_out, d_ff_1_q, comparator_2_eq);
  Counter #(.width(13), .max('h1fff), .ongoal("stay"), .trigger("rising"), .behavior("old")) counter_2 (
    .count(comparator_2_lt), .Q(CNT_num), .clk(clock_1_out));  // open: load, D, carry, clr, preset
  assign CLK = nand_1_out ? clock_1_out : 1'bz;  // Controlled_Buffer controlled_buffer_1
  \单周期硬布线控制器  \u_单周期硬布线控制器_1  (
    .Funct(funct), .OP(ID_IR[6:2]), .ALU_OP(ID_AluOP), .MemToReg(ID_MemToReg), .MemWrite(ID_MemWrite),
    .ALU_SRC(ID_AluSrcB), .RegWrite(ID_RegWrite), .ecall(ID_ecall), .S_type(ID_S_type), .Jalr(ID_JALR),
    .Beq(ID_BEQ), .JAL(ID_JAL), .Bne(ID_BNE), .in_3(ID_IR[21]), .uret(ID_URET), .CSR(ID_CSR),
    .AUIPC(ID_AUIPC), .LB(ID_LB), .BGE(ID_BGE), .RSread(\单周期硬布线控制器_1_rsread ), .RTread(\单周期硬布线控制器_1_rtread ));
  Multiplexer #(.select(1), .width(5), .disabled("Z"), .enable("false")) multiplexer_2 (
    .in0(ID_IR[19:15]), .in1(5'b10001), .out(RSid), .sel(ID_ecall));
  Multiplexer #(.select(1), .width(5), .disabled("Z"), .enable("false")) multiplexer_3 (
    .in0(ID_IR[24:20]), .in1(5'b01010), .out(RTid), .sel(ID_ecall));
  Multiplexer #(.select(1), .width(12), .disabled("Z"), .enable("false")) multiplexer_4 (
    .in0({ID_IR[31], funct[4], ID_IR[29:26], funct[3], ID_IR[24:20]}),
    .in1({ID_IR[31], funct[4], ID_IR[29:26], funct[3], ID_IR[11:7]}), .out(multiplexer_4_out), .sel(ID_S_type));
  Pull_Resistor #(.pull(1)) pull_resistor_1 (.node(CLK));
  assign bit_extender_1_out = {{20{ID_IR[31]}}, {ID_IR[31], ID_IR[7], funct[4], ID_IR[29:26], funct[3], ID_IR[11:8]}};  // Bit_Extender bit_extender_1
  assign bit_extender_2_out = {{12{ID_IR[31]}}, {ID_IR[31], ID_IR[19:15], funct[2], ID_IR[13:12], ID_IR[20], funct[4], ID_IR[29:26], funct[3], ID_IR[24:21]}};  // Bit_Extender bit_extender_2
  Regifile regifile_1 (
    .Din(RDin), .Clk(CLK), .R1(ID_R1), .R2(ID_R2), .WE(RegWrite), .W_num(WB_W_num), .R1_num(RSid),
    .R2_num(RTid));
  assign ID_imm = {{20{multiplexer_4_out[11]}}, multiplexer_4_out};  // Bit_Extender bit_extender_3
  Shifter #(.width(32), .shift("ll")) shifter_1 (.in(bit_extender_1_out), .\dist (5'b00001), .out(shifter_1_out));
  Shifter #(.width(32), .shift("ll")) shifter_2 (.in(bit_extender_2_out), .\dist (5'b00001), .out(shifter_2_out));
  bubble_judge bubble_judge_1 (
    .RSin(\单周期硬布线控制器_1_rsread ), .RTin(\单周期硬布线控制器_1_rtread ), .RSid(RSid), .RTid(RTid),
    .EX_Regwrite(EX_RegWrite), .MEM_Regwrite(MEM_RegWrite), .EX_Wid(EX_W_num), .MEM_Wid(MEM_W_num),
    .bubble(bubble));
  Adder #(.width(32)) adder_2 (.a(shifter_1_out), .b(ID_PC), .out(ID_BEaddr), .cin(1'b0));  // open: cout
  Adder #(.width(32)) adder_3 (.a(shifter_2_out), .b(ID_PC), .out(ID_JALaddr), .cin(1'b0));  // open: cout
  Adder #(.width(32)) adder_4 (
    .a({ID_IR[31], funct[4], ID_IR[29:26], funct[3], ID_IR[24:15], funct[2], ID_IR[13:12], {12{1'b0}}}),
    .b(ID_PC), .out(ID_AUIPCresult), .cin(1'b0));  // open: cout
  or or_1 (or_1_out, EX_Branch, bubble);
  ID_EX id_ex_1 (
    .RegWritein(ID_RegWrite), .MemToRegin(ID_MemToReg), .MemWritein(ID_MemWrite), .ALUOPin(ID_AluOP),
    .ALUSrcin(ID_AluSrcB), .ecallin(ID_ecall), .S_typein(ID_S_type), .BEQin(ID_BEQ), .BNEin(ID_BNE),
    .JALin(ID_JAL), .JALRin(ID_JALR), .AUIPCin(ID_AUIPC), .LBin(ID_LB), .BGEin(ID_BGE), .R1in(ID_R1),
    .R2in(ID_R2), .W_in(ID_IR[11:7]), .immin(ID_imm), .BEaddrin(ID_BEaddr), .PCin(ID_PC),
    .nextPCin(ID_nextPC), .JALaddrin(ID_JALaddr),
    .IRin({ID_IR[31], funct[4], ID_IR[29:26], funct[3], ID_IR[24:15], funct[2], ID_IR[13:0]}),
    .RESET(or_1_out), .EN(EN), .CLK(CLK), .RegWriteout(EX_RegWrite), .MemToRegout(EX_MemToReg),
    .MemWriteout(EX_MemWrite), .ALUOPout(EX_AluOP), .ALUSrcout(EX_AluSrcB), .ecallout(EX_ecall),
    .S_typeout(EX_S_type), .BEQout(EX_BEQ), .BNEout(EX_BNE), .JALout(EX_JAL), .JALRout(EX_JALR),
    .AUIPCout(EX_AUIPC), .LBout(EX_LB), .BGEout(EX_BGE), .R1out(EX_R1), .R2out(EX_R2), .W_out(EX_W_num),
    .immout(EX_imm), .BEaddrout(EX_BEaddr), .PCout(EX_PC), .nextPCout(EX_nextPC), .JALaddrout(EX_JALaddr),
    .IRout(EX_IR), .AUIPCresin(ID_AUIPCresult), .AUIPCresout(EX_AUIPCresult));  // open: RS_Fin, RS_Fout, RT_Fin, RT_Fout
  Multiplexer #(.select(1), .width(32), .disabled("Z"), .enable("false")) multiplexer_5 (
    .in0(EX_R2), .in1(EX_imm), .out(multiplexer_5_out), .sel(EX_AluSrcB));
  ALU alu_1 (
    .X(EX_R1), .Y(multiplexer_5_out), .AluOP(EX_AluOP), .Equal(EX_Aluequal), .Result(EX_Result),
    .out_4(EX_Alugreatequal), .out_6(EX_Aluless));  // open: Result_2
  not not_7 (not_7_out, EX_Aluequal);
  Multiplexer #(.select(1), .width(32), .disabled("Z"), .enable("false")) multiplexer_6 (
    .in0(IF_nextPC), .in1(EX_BEaddr), .out(multiplexer_6_out), .sel(EX_BE));
  assign not_8_out = ~32'h1;  // NOT_Gate not_8, 32 bits wide
  and and_6 (and_6_out, EX_Aluequal, EX_BEQ);
  and and_7 (and_7_out, not_7_out, EX_BNE);
  and and_8 (and_8_out, EX_Alugreatequal, EX_BGE);
  or or_2 (EX_JUMP, EX_JAL, EX_JALR);
  Multiplexer #(.select(1), .width(32), .disabled("Z"), .enable("false")) multiplexer_7 (
    .in0(multiplexer_6_out), .in1(EX_JALaddr), .out(multiplexer_7_out), .sel(EX_JAL));
  assign and_9_out = EX_Result & not_8_out;  // AND_Gate and_9, 32 bits wide
  or or_3 (EX_BE, and_6_out, and_7_out, and_8_out);
  Multiplexer #(.select(1), .width(32), .disabled("Z"), .enable("false")) multiplexer_8 (
    .in0(multiplexer_7_out), .in1(and_9_out), .out(PCaddr), .sel(EX_JALR));
  Multiplexer #(.select(1), .width(32), .disabled("Z"), .enable("false")) multiplexer_9 (
    .in0(EX_Result), .in1(EX_AUIPCresult), .out(multiplexer_9_out), .sel(EX_AUIPC));
  or or_4 (EX_Branch, EX_JUMP, EX_BE);
  EX_MEM ex_mem_1 (
    .RegWritein(EX_RegWrite), .MemToRegin(EX_MemToReg), .MemWritein(EX_MemWrite), .ALUOPin(EX_AluOP),
    .ALUSrcin(EX_AluSrcB), .ecallin(EX_ecall), .S_typein(EX_S_type), .BEQin(EX_BEQ), .BNEin(EX_BNE),
    .JALin(EX_JAL), .JALRin(EX_JALR), .AUIPCin(EX_AUIPC), .LBin(EX_LB), .BGEin(EX_BGE), .R1in(EX_R1),
    .R2in(EX_R2), .W_in(EX_W_num), .immin(EX_imm), .BEaddrin(EX_BEaddr), .PCin(EX_PC), .nextPCin(EX_nextPC),
    .JALaddrin(EX_JALaddr), .IRin(EX_IR), .BEin(EX_BE), .ALUResultin(multiplexer_9_out), .RESET(1'b0),
    .EN(EN), .CLK(CLK), .RegWriteout(MEM_RegWrite), .MemToRegout(MEM_MemToReg), .MemWriteout(MemWrite),
    .ALUOPout(MEM_AluOP), .ALUSrcout(MEM_AluSrcB), .ecallout(MEM_ecall), .S_typeout(MEM_S_type),
    .BEQout(MEM_BEQ), .BNEout(MEM_BEQ), .JALout(MEM_JAL), .JALRout(MEM_JALR), .AUIPCout(MEM_AUIPC),
    .LBout(MEM_LB), .BGEout(MEM_BGE), .R1out(MEM_R1), .R2out(MDin), .W_out(MEM_W_num), .immout(MEM_imm),
    .BEaddrout(MEM_BEaddr), .PCout(M_PC), .nextPCout(MEM_nextPC), .JALaddrout(MEM_JALaddr), .IRout(MEM_IR),
    .BEout(MEM_BE), .ALUResultout(MEM_ALUout));
  RAM #(.addrWidth(10), .dataWidth(32), .bus("separate"), .Select("high")) ram_1 (
    .addr(MEM_ALUout[11:2]), .din(MDin), .data(ram_1_data), .str(MemWrite), .clk(CLK), .ld(not_9_out));  // open: sel, clr
  not not_9 (not_9_out, MemWrite);
  Multiplexer #(.select(2), .width(8), .disabled("Z"), .enable("false")) multiplexer_10 (
    .in0(ram_1_data[7:0]), .in1(ram_1_data[15:8]), .in2(ram_1_data[23:16]), .in3(ram_1_data[31:24]),
    .out(multiplexer_10_out), .sel(MEM_ALUout[1:0]));
  assign bit_extender_4_out = {{24{multiplexer_10_out[7]}}, multiplexer_10_out};  // Bit_Extender bit_extender_4
  Multiplexer #(.select(1), .width(32), .disabled("Z"), .enable("false")) multiplexer_11 (
    .in0(ram_1_data), .in1(bit_extender_4_out), .out(multiplexer_11_out), .sel(MEM_LB));
  MEM_WB mem_wb_1 (
    .RegWritein(MEM_RegWrite), .MemToRegin(MEM_MemToReg), .MemWritein(MemWrite), .ALUOPin(MEM_AluOP),
    .ALUSrcin(MEM_AluSrcB), .ecallin(MEM_ecall), .S_typein(MEM_S_type), .BEQin(MEM_BEQ), .BNEin(MEM_BEQ),
    .JALin(MEM_JAL), .JALRin(MEM_JALR), .AUIPCin(MEM_AUIPC), .LBin(MEM_LB), .BGEin(MEM_BGE),
    .W_in(MEM_W_num), .immin(MEM_imm), .BEaddrin(MEM_BEaddr), .PCin(M_PC), .nextPCin(MEM_nextPC),
    .JALaddrin(MEM_JALaddr), .IRin(MEM_IR), .BEin(MEM_BE), .ALUResultin(MEM_ALUout), .RESET(1'b0), .EN(EN),
    .CLK(CLK), .RegWriteout(RegWrite), .MemToRegout(WB_MemToReg), .MemWriteout(WB_MemWrite),
    .ALUOPout(WB_AluOP), .ALUSrcout(WB_AluSrcB), .ecallout(WB_ecall), .S_typeout(WB_S_type), .BEQout(WB_BEQ),
    .BNEout(WB_BNE), .JALout(WB_JAL), .JALRout(WB_JALR), .AUIPCout(WB_AUIPC), .LBout(WB_LB), .BGEout(WB_BGE),
    .W_out(WB_W_num), .immout(WB_imm), .BEaddrout(WB_BEaddr), .PCout(WB_PC), .nextPCout(WB_nextPC),
    .JALaddrout(WB_JALaddr), .IRout(WB_IR), .BEout(WB_BE), .ALUResultout(mem_wb_1_aluresultout),
    .Memin(multiplexer_11_out), .Memout(mem_wb_1_memout), .R1in(MEM_R1), .R1out(WB_R1), .R2in(MDin),
    .R2out(WB_R2));
  Multiplexer #(.select(1), .width(32), .disabled("Z"), .enable("false")) multiplexer_12 (
    .in0(mem_wb_1_aluresultout), .in1(mem_wb_1_memout), .out(multiplexer_12_out), .sel(WB_MemToReg));
  or or_5 (or_5_out, WB_JAL, WB_JALR);
  Multiplexer #(.select(1), .width(32), .disabled("Z"), .enable("false")) multiplexer_13 (
    .in0(multiplexer_12_out), .in1(WB_nextPC), .out(RDin), .sel(or_5_out));

  // Other names for the same wires on the sheet: ID_W_num[4:0] = ID_IR[11:7]; ID_IR (some bits) = funct[4:2];
  //   MEM_BNE = MEM_BEQ; MEM_MemWrite = MemWrite; MEM_PC[31:0] = M_PC; MEM_R2[31:0] = MDin; WB_RegWrite = RegWrite

  // Notes on the sheet:
  //   中断源
  //   时空图监测，可删除
  //   中断等待指示
  //   数码管输出
  //   contents of 指令存储器 (hex, n*v repeats v):
  //   100493 100006f 100493 200913 300993 100006f 100493 200913 300993 100006f 100493 200913 300993
  //   100006f 100493 200913 300993 40c000ef 100413 100493 1f49493 900533 2200893 73 24d493 48463 fedff06f
  //   900533 2200893 73 100493 249493 900533 2200893 73 48463 fedff06f 100493 1f49493 900533 2200893 73
  //   4034d493 900533 2200893 73 4044d493 900533 2200893 73 4044d493 900533 2200893 73 4044d493 900533
  //   2200893 73 4044d493 900533 2200893 73 4044d493 900533 2200893 73 4044d493 900533 2200893 73 4044d493
  //   900533 2200893 73 100413 1f41993 41f9d993 433 c00913 300b13 140413 f47413 800293 100313 499993
  //   89e9b3 1300533 2200893 73 406282b3 fe0294e3 140413 f00f93 1f47433 1c41413 800293 100313 49d993
  //   89e9b3 1300533 2200893 73 406282b3 fe0294e3 1c45413 406b0b33 b0463 f95ff06f 2b3 fff2c293 829293
  //   ff2e293 500533 2200893 73 fff00413 493 84a023 140413 448493 84a023 140413 448493 84a023 140413
  //   448493 84a023 140413 448493 84a023 140413 448493 84a023 140413 448493 84a023 140413 448493 84a023
  //   140413 448493 84a023 140413 448493 84a023 140413 448493 84a023 140413 448493 84a023 140413 448493
  //   84a023 140413 448493 84a023 140413 448493 84a023 140413 448493 84a023 140413 448493 140413 433
  //   3c00493 42983 4aa03 149a2b3 28663 134a023 1442023 ffc48493 fe9412e3 800533 2200893 73 440413 3c00493
  //   fc9416e3 a00893 73 fff00293 7700493 849493 7748493 900533 2200893 73 1000e13 54c4b3 900533 2200893
  //   73 fffe0e13 fe0e16e3 a00893 73 13 430497 900533 2200893 73 430497 900533 2200893 73 430497 900533
  //   2200893 73 430497 900533 2200893 73 430497 900533 2200893 73 430497 900533 2200893 73 430497 900533
  //   2200893 73 430497 900533 2200893 73 a00893 73 313 1000e13 13 8400493 849493 8348493 400913 891913
  //   490913 849493 8248493 849493 8148493 891913 490913 891913 490913 932023 12484b3 430313 fffe0e13
  //   fe0e18e3 2000e13 313 30483 900533 2200893 73 130313 fffe0e13 fe0e14e3 a00893 73 f00493 900533
  //   2200893 73 fff48493 fe04d8e3 a00893 73 413 140413 800533 2200893 73 240413 800533 2200893 73 340413
  //   800533 2200893 73 440413 800533 2200893 73 540413 800533 2200893 73 640413 800533 2200893 73 740413
  //   800533 2200893 73 840413 800533 2200893 2200893 73 8067
  //   指令探针
  //   控制位
  //   流水调试日志用
  //   暂停节拍，不能为0
  //   戳工具置1进入计数暂停模式，ctrl+k时钟自动运行到对应节拍暂停
  //   ctrl+k关闭时钟连续运行，将控制位置零，进入单步调试模式调试
  //   JALR
  //   URET
  //   可计数暂停的时钟源
  //   Bne
  //   MemToReg
  //   MemWrite
  //   AluOP
  //   AluSrcB
  //   RegWrite
  //   为方便自动评测，需要输出流水线各段保存的PC值，注意是PC不是PC+4，另外ID段寄存器写入信息，Mem段内存写入信息也要输出
endmodule
module \重定向流水线  (
  output RegWrite,
  output MemWrite,
  output [31:0] IF_PC,
  output [31:0] ID_PC,
  output [31:0] EX_PC,
  output [31:0] M_PC,
  output [31:0] WB_PC,
  output [31:0] RDin,
  output [31:0] MDin,
  output [31:0] LedData
);

  wire and_1_out, and_2_out, and_3_out, and_4_out, and_6_out, and_7_out, and_8_out, and_9_out, and_10_out,
       and_11_out, and_12_out, CLK, clock_1_out, comparator_1_eq, comparator_2_eq, comparator_2_lt, d_ff_1_q,
       EN, EX_Aluequal, EX_Alugreatequal, EX_Aluless, EX_AluSrcB, EX_AUIPC, EX_BE, EX_BEQ, EX_BGE, EX_BNE,
       EX_Branch, EX_ecall, EX_JAL, EX_JALR, EX_JUMP, EX_LB, EX_MemToReg, EX_MemWrite, EX_RegWrite,
       EX_S_type, Go, halt, ID_AluSrcB, ID_AUIPC, ID_BEQ, ID_BGE, ID_BNE, ID_CSR, ID_ecall, ID_JAL, ID_JALR,
       ID_LB, ID_MemToReg, ID_MemWrite, ID_RegWrite, ID_S_type, ID_URET, IR1, IR2, IR3, load, MEM_AluSrcB,
       MEM_AUIPC, MEM_BE, MEM_BEQ, MEM_BGE, MEM_ecall, MEM_JAL, MEM_JALR, MEM_LB, MEM_MemToReg, MEM_RegWrite,
       MEM_S_type, nand_1_out, nor_1_out, nor_2_out, nor_3_out, not_2_out, not_3_out, not_4_out, not_5_out,
       not_6_out, not_7_out, not_8_out, not_9_out, not_10_out, not_12_out, or_1_out, or_2_out, or_3_out,
       or_7_out, RST, W1, W2, W3, WB_AluSrcB, WB_AUIPC, WB_BE, WB_BEQ, WB_BGE, WB_BNE, WB_ecall, WB_JAL,
       WB_JALR, WB_LB, WB_MemToReg, WB_MemWrite, WB_S_type, \单周期硬布线控制器_1_rsread , \单周期硬布线控制器_1_rtread ;
  wire [1:0] EX_RS_F, EX_RT_F, ID_RS_F, ID_RT_F;
  wire [3:0] EX_AluOP, ID_AluOP, MEM_AluOP, WB_AluOP;
  wire [4:0] EX_W_num, funct, MEM_W_num, RSid, RTid, WB_W_num;
  wire [7:0] multiplexer_12_out;
  wire [11:0] multiplexer_4_out;
  wire [12:0] CNT_num;
  wire [15:0] \LoadUse次数 , \总周期数 , \插入气泡数 , \无条件分支数 , \条件分支成功数 ;
  wire [31:0] and_13_out, bit_extender_1_out, bit_extender_2_out, bit_extender_4_out, EX_AUIPCresult,
       EX_BEaddr, EX_imm, EX_IR, EX_JALaddr, EX_nextPC, EX_R1, EX_R2, EX_Result, ID_AUIPCresult, ID_BEaddr,
       id_ex_1_r1out, id_ex_1_r2out, ID_imm, ID_IR, ID_JALaddr, ID_nextPC, ID_R1, ID_R2, IF_IR, IF_nextPC,
       MEM_ALUout, MEM_BEaddr, MEM_imm, MEM_IR, MEM_JALaddr, MEM_nextPC, MEM_R1, mem_wb_1_aluresultout,
       mem_wb_1_memout, multiplexer_7_out, multiplexer_8_out, multiplexer_9_out, multiplexer_11_out,
       multiplexer_13_out, multiplexer_14_out, not_11_out, PCaddr, ram_1_data, shifter_1_out, shifter_2_out,
       WB_BEaddr, WB_imm, WB_IR, WB_JALaddr, WB_nextPC, WB_R1, WB_R2;

  Button \u_总复位  (.out(RST));
  Button _1 (.out(IR1));
  Button _2 (.out(IR2));
  Button _3 (.out(IR3));
  // Probe on \总周期数 
  // Probe on \总周期数 
  Button \u_继续运行  (.out(Go));
  LED #(.active("true")) led_1 (.in(W1));
  LED #(.active("true")) led_2 (.in(W2));
  LED #(.active("true")) led_3 (.in(W3));
  Hex_Digit_Display hex_digit_display_1 (.value(LedData[31:28]));  // open: dp
  // Probe on IF_PC[19:0]
  // RiscV_Probe riscv_probe_1: pin names not known; wires that end beside it: IF_IR
  Register #(.width(32), .trigger("rising"), .Select("low")) PC (
    .D(PCaddr), .en(nor_1_out), .Q(IF_PC), .clk(CLK), .clr(RST));
  nor nor_1 (nor_1_out, halt, load);
  and and_1 (and_1_out, CLK, not_2_out);
  Hex_Digit_Display hex_digit_display_2 (.value(LedData[27:24]));  // open: dp
  Hex_Digit_Display hex_digit_display_3 (.value(LedData[23:20]));  // open: dp
  // Probe on ID_PC[19:0]
  // RiscV_Probe riscv_probe_2: pin names not known; wires that end beside it: {ID_IR[31], funct[4], ID_IR[29:26], funct[3], ID_IR[24:15], funct[2], ID_IR[13:0]}
  not not_1 (EN, halt);
  Counter #(.width(16), .max('hffff), .ongoal("wrap"), .trigger("rising"), .behavior("new")) counter_1 (
    .D({16{1'b0}}), .Q(\总周期数 ), .clk(and_1_out), .clr(RST));  // open: load, count, carry, preset, down
  not not_2 (not_2_out, WB_ecall);
  Hex_Digit_Display hex_digit_display_4 (.value(LedData[19:16]));  // open: dp
  Hex_Digit_Display hex_digit_display_5 (.value(LedData[15:12]));  // open: dp
  Adder #(.width(32)) adder_1 (.a(IF_PC), .b(32'h4), .out(IF_nextPC));  // open: cin, cout
  Comparator #(.width(32), .mode("twosComplement")) comparator_1 (
    .a(WB_R1), .b(32'h22), .eq(comparator_1_eq));  // open: gt, lt
  and and_2 (and_2_out, comparator_1_eq, WB_ecall);
  Hex_Digit_Display hex_digit_display_6 (.value(LedData[7:4]));  // open: dp
  Hex_Digit_Display hex_digit_display_7 (.value(LedData[11:8]));  // open: dp
  // Probe on EX_PC[19:0]
  // RiscV_Probe riscv_probe_3: pin names not known; wires that end beside it: EX_IR
  ROM #(.addrWidth(10), .dataWidth(32), .Select("high")) \u_指令存储器  (.addr(IF_PC[11:2]), .data(IF_IR));
  and and_3 (and_3_out, WB_ecall, not_3_out);
  not not_3 (not_3_out, comparator_1_eq);
  Register #(.width(32), .trigger("rising"), .Select("low")) register_1 (
    .D(WB_R2), .en(and_2_out), .Q(LedData), .clk(CLK));  // open: clr
  Counter #(.width(16), .max('hffff), .ongoal("wrap"), .trigger("rising"), .behavior("new")) counter_2 (
    .D({16{1'b0}}), .count(load), .Q(\LoadUse次数 ), .clk(and_4_out), .clr(RST));  // open: load, carry, preset, down
  and and_4 (and_4_out, CLK, not_4_out);
  not not_4 (not_4_out, WB_ecall);
  Hex_Digit_Display hex_digit_display_8 (.value(LedData[3:0]));  // open: dp
  // RiscV_Probe riscv_probe_4: pin names not known; wires that end beside it: IF_IR
  not not_5 (not_5_out, Go);
  // Probe on \总周期数 
  // Probe on M_PC[19:0]
  // RiscV_Probe riscv_probe_5: pin names not known; wires that end beside it: MEM_IR
  nor nor_2 (nor_2_out, halt, load);
  and and_5 (halt, not_5_out, and_3_out);
  // Probe on \总周期数 
  // Probe on \无条件分支数 
  // Probe on \条件分支成功数 
  // Probe on \插入气泡数 
  // Probe on \LoadUse次数 
  IF_ID if_id_1 (
    .PCin(IF_PC), .nextPCin(IF_nextPC), .IRin(IF_IR), .EN(nor_2_out), .CLK(CLK), .RESET(EX_Branch),
    .PCout(ID_PC), .nextPCout(ID_nextPC),
    .IRout({ID_IR[31], funct[4], ID_IR[29:26], funct[3], ID_IR[24:15], funct[2], ID_IR[13:0]}));
  or or_1 (or_1_out, EX_JAL, EX_JALR);
  Counter #(.width(16), .max('hffff), .ongoal("wrap"), .trigger("rising"), .behavior("new")) counter_3 (
    .D({16{1'b0}}), .count(or_1_out), .Q(\无条件分支数 ), .clk(and_6_out), .clr(RST));  // open: load, carry, preset, down
  and and_6 (and_6_out, CLK, not_6_out);
  not not_6 (not_6_out, WB_ecall);
  // Probe on IF_PC[11:0]
  // Probe on WB_PC[19:0]
  // RiscV_Probe riscv_probe_6: pin names not known; wires that end beside it: WB_IR
  // RiscV_Probe riscv_probe_7: pin names not known; wires that end beside it: {ID_IR[31], funct[4], ID_IR[29:26], funct[3], ID_IR[24:15], funct[2], ID_IR[13:0]}
  not not_7 (not_7_out, ID_IR[0]);
  not not_8 (not_8_out, ID_IR[1]);
  // Probe on ID_PC[11:0]
  // Probe on EX_PC[11:0]
  and and_7 (and_7_out, not_7_out, not_8_out);
  // Probe on M_PC[11:0]
  D_Flip_Flop #(.trigger("high"), .Pre_Clr_Positions("LEGACY"), .NegatePresetClear("false"), .enable("true"), .NewFFLayout("false")) d_ff_1 (.Q(d_ff_1_q));  // open: clk, D, Qn, preset, en, reset
  // Probe on 13'hc
  Multiplexer #(.select(1), .width(2), .disabled("Z"), .enable("false")) multiplexer_1 (
    .in0(ID_IR[13:12]), .in1(2'b11), .out(funct[1:0]), .sel(and_7_out));
  and and_8 (and_8_out, EX_Branch, nor_3_out);
  nor nor_3 (nor_3_out, EX_JAL, EX_JALR);
  // Probe on WB_PC[11:0]
  Comparator #(.width(13), .mode("twosComplement")) comparator_2 (
    .a(CNT_num), .b(13'hc), .eq(comparator_2_eq), .lt(comparator_2_lt));  // open: gt
  Clock #(.highDuration(1), .lowDuration(1)) clock_1 (.out(clock_1_out));
  Counter #(.width(16), .max('hffff), .ongoal("wrap"), .trigger("rising"), .behavior("new")) counter_4 (
    .D({16{1'b0}}), .count(and_8_out), .Q(\条件分支成功数 ), .clk(CLK), .clr(RST));  // open: load, carry, preset, down
  nand nand_1 (nand_1_out, d_ff_1_q, comparator_2_eq);
  Counter #(.width(13), .max('h1fff), .ongoal("stay"), .trigger("rising"), .behavior("old")) counter_5 (
    .count(comparator_2_lt), .Q(CNT_num), .clk(clock_1_out));  // open: load, D, carry, clr, preset
  assign CLK = nand_1_out ? clock_1_out : 1'bz;  // Controlled_Buffer controlled_buffer_1
  \单周期硬布线控制器  \u_单周期硬布线控制器_1  (
    .Funct(funct), .OP(ID_IR[6:2]), .ALU_OP(ID_AluOP), .MemToReg(ID_MemToReg), .MemWrite(ID_MemWrite),
    .ALU_SRC(ID_AluSrcB), .RegWrite(ID_RegWrite), .ecall(ID_ecall), .S_type(ID_S_type), .Jalr(ID_JALR),
    .Beq(ID_BEQ), .JAL(ID_JAL), .Bne(ID_BNE), .in_3(ID_IR[21]), .uret(ID_URET), .CSR(ID_CSR),
    .AUIPC(ID_AUIPC), .LB(ID_LB), .BGE(ID_BGE), .RSread(\单周期硬布线控制器_1_rsread ), .RTread(\单周期硬布线控制器_1_rtread ));
  Multiplexer #(.select(1), .width(5), .disabled("Z"), .enable("false")) multiplexer_2 (
    .in0(ID_IR[19:15]), .in1(5'b10001), .out(RSid), .sel(ID_ecall));
  Multiplexer #(.select(1), .width(5), .disabled("Z"), .enable("false")) multiplexer_3 (
    .in0(ID_IR[24:20]), .in1(5'b01010), .out(RTid), .sel(ID_ecall));
  Multiplexer #(.select(1), .width(12), .disabled("Z"), .enable("false")) multiplexer_4 (
    .in0({ID_IR[31], funct[4], ID_IR[29:26], funct[3], ID_IR[24:20]}),
    .in1({ID_IR[31], funct[4], ID_IR[29:26], funct[3], ID_IR[11:7]}), .out(multiplexer_4_out), .sel(ID_S_type));
  Pull_Resistor #(.pull(1)) pull_resistor_1 (.node(CLK));
  assign bit_extender_1_out = {{20{ID_IR[31]}}, {ID_IR[31], ID_IR[7], funct[4], ID_IR[29:26], funct[3], ID_IR[11:8]}};  // Bit_Extender bit_extender_1
  assign bit_extender_2_out = {{12{ID_IR[31]}}, {ID_IR[31], ID_IR[19:15], funct[2], ID_IR[13:12], ID_IR[20], funct[4], ID_IR[29:26], funct[3], ID_IR[24:21]}};  // Bit_Extender bit_extender_2
  or or_2 (or_2_out, EX_Branch, load);
  Counter #(.width(16), .max('hffff), .ongoal("wrap"), .trigger("rising"), .behavior("new")) counter_6 (
    .D({16{1'b0}}), .count(or_2_out), .Q(\插入气泡数 ), .clk(and_9_out), .clr(RST));  // open: load, carry, preset, down
  and and_9 (and_9_out, CLK, not_9_out);
  not not_9 (not_9_out, WB_ecall);
  Regifile regifile_1 (
    .Din(RDin), .Clk(CLK), .R1(ID_R1), .R2(ID_R2), .WE(RegWrite), .W_num(WB_W_num), .R1_num(RSid),
    .R2_num(RTid));
  assign ID_imm = {{20{multiplexer_4_out[11]}}, multiplexer_4_out};  // Bit_Extender bit_extender_3
  load_judge load_judge_1 (
    .RSin(\单周期硬布线控制器_1_rsread ), .RTin(\单周期硬布线控制器_1_rtread ), .RSid(RSid), .RTid(RTid),
    .EX_Regwrite(EX_RegWrite), .MEM_Regwrite(MEM_RegWrite), .EX_Wid(EX_W_num), .MEM_Wid(MEM_W_num),
    .EX_MemToReg(EX_MemToReg), .RS_F(ID_RS_F), .RT_F(ID_RT_F), .load(load));
  Shifter #(.width(32), .shift("ll")) shifter_1 (.in(bit_extender_1_out), .\dist (5'b00001), .out(shifter_1_out));
  Shifter #(.width(32), .shift("ll")) shifter_2 (.in(bit_extender_2_out), .\dist (5'b00001), .out(shifter_2_out));
  Adder #(.width(32)) adder_2 (.a(shifter_1_out), .b(ID_PC), .out(ID_BEaddr), .cin(1'b0));  // open: cout
  Adder #(.width(32)) adder_3 (.a(shifter_2_out), .b(ID_PC), .out(ID_JALaddr), .cin(1'b0));  // open: cout
  Adder #(.width(32)) adder_4 (
    .a({ID_IR[31], funct[4], ID_IR[29:26], funct[3], ID_IR[24:15], funct[2], ID_IR[13:12], {12{1'b0}}}),
    .b(ID_PC), .out(ID_AUIPCresult), .cin(1'b0));  // open: cout
  or or_3 (or_3_out, EX_Branch, load);
  ID_EX id_ex_1 (
    .RegWritein(ID_RegWrite), .MemToRegin(ID_MemToReg), .MemWritein(ID_MemWrite), .ALUOPin(ID_AluOP),
    .ALUSrcin(ID_AluSrcB), .ecallin(ID_ecall), .S_typein(ID_S_type), .BEQin(ID_BEQ), .BNEin(ID_BNE),
    .JALin(ID_JAL), .JALRin(ID_JALR), .AUIPCin(ID_AUIPC), .LBin(ID_LB), .BGEin(ID_BGE), .R1in(ID_R1),
    .R2in(ID_R2), .W_in(ID_IR[11:7]), .immin(ID_imm), .BEaddrin(ID_BEaddr), .PCin(ID_PC),
    .nextPCin(ID_nextPC), .JALaddrin(ID_JALaddr),
    .IRin({ID_IR[31], funct[4], ID_IR[29:26], funct[3], ID_IR[24:15], funct[2], ID_IR[13:0]}),
    .RESET(or_3_out), .EN(EN), .CLK(CLK), .RegWriteout(EX_RegWrite), .MemToRegout(EX_MemToReg),
    .MemWriteout(EX_MemWrite), .ALUOPout(EX_AluOP), .ALUSrcout(EX_AluSrcB), .ecallout(EX_ecall),
    .S_typeout(EX_S_type), .BEQout(EX_BEQ), .BNEout(EX_BNE), .JALout(EX_JAL), .JALRout(EX_JALR),
    .AUIPCout(EX_AUIPC), .LBout(EX_LB), .BGEout(EX_BGE), .R1out(id_ex_1_r1out), .R2out(id_ex_1_r2out),
    .W_out(EX_W_num), .immout(EX_imm), .BEaddrout(EX_BEaddr), .PCout(EX_PC), .nextPCout(EX_nextPC),
    .JALaddrout(EX_JALaddr), .IRout(EX_IR), .RS_Fin(ID_RS_F), .RS_Fout(EX_RS_F), .RT_Fin(ID_RT_F),
    .RT_Fout(EX_RT_F), .AUIPCresin(ID_AUIPCresult), .AUIPCresout(EX_AUIPCresult));
  Multiplexer #(.select(2), .width(32), .disabled("Z"), .enable("false")) multiplexer_5 (
    .in0(id_ex_1_r1out), .in1(RDin), .in2(MEM_ALUout), .out(EX_R1), .sel(EX_RS_F));  // open: in3
  Multiplexer #(.select(2), .width(32), .disabled("Z"), .enable("false")) multiplexer_6 (
    .in0(id_ex_1_r2out), .in1(RDin), .in2(MEM_ALUout), .out(EX_R2), .sel(EX_RT_F));  // open: in3
  not not_10 (not_10_out, EX_Aluequal);
  Multiplexer #(.select(1), .width(32), .disabled("Z"), .enable("false")) multiplexer_7 (
    .in0(IF_nextPC), .in1(EX_BEaddr), .out(multiplexer_7_out), .sel(EX_BE));
  assign not_11_out = ~32'h1;  // NOT_Gate not_11, 32 bits wide
  Multiplexer #(.select(1), .width(32), .disabled("Z"), .enable("false")) multiplexer_8 (
    .in0(EX_R2), .in1(EX_imm), .out(multiplexer_8_out), .sel(EX_AluSrcB));
  and and_10 (and_10_out, EX_Aluequal, EX_BEQ);
  and and_11 (and_11_out, not_10_out, EX_BNE);
  and and_12 (and_12_out, EX_Alugreatequal, EX_BGE);
  or or_4 (EX_JUMP, EX_JAL, EX_JALR);
  Multiplexer #(.select(1), .width(32), .disabled("Z"), .enable("false")) multiplexer_9 (
    .in0(multiplexer_7_out), .in1(EX_JALaddr), .out(multiplexer_9_out), .sel(EX_JAL));
  assign and_13_out = EX_Result & not_11_out;  // AND_Gate and_13, 32 bits wide
  ALU alu_1 (
    .X(EX_R1), .Y(multiplexer_8_out), .AluOP(EX_AluOP), .Equal(EX_Aluequal), .Result(EX_Result),
    .out_4(EX_Alugreatequal), .out_6(EX_Aluless));  // open: Result_2
  or or_5 (EX_BE, and_10_out, and_11_out, and_12_out);
  Multiplexer #(.select(1), .width(32), .disabled("Z"), .enable("false")) multiplexer_10 (
    .in0(multiplexer_9_out), .in1(and_13_out), .out(PCaddr), .sel(EX_JALR));
  or or_6 (EX_Branch, EX_JUMP, EX_BE);
  Multiplexer #(.select(1), .width(32), .disabled("Z"), .enable("false")) multiplexer_11 (
    .in0(EX_Result), .in1(EX_AUIPCresult), .out(multiplexer_11_out), .sel(EX_AUIPC));
  EX_MEM ex_mem_1 (
    .RegWritein(EX_RegWrite), .MemToRegin(EX_MemToReg), .MemWritein(EX_MemWrite), .ALUOPin(EX_AluOP),
    .ALUSrcin(EX_AluSrcB), .ecallin(EX_ecall), .S_typein(EX_S_type), .BEQin(EX_BEQ), .BNEin(EX_BNE),
    .JALin(EX_JAL), .JALRin(EX_JALR), .AUIPCin(EX_AUIPC), .LBin(EX_LB), .BGEin(EX_BGE), .R1in(EX_R1),
    .R2in(EX_R2), .W_in(EX_W_num), .immin(EX_imm), .BEaddrin(EX_BEaddr), .PCin(EX_PC), .nextPCin(EX_nextPC),
    .JALaddrin(EX_JALaddr), .IRin(EX_IR), .BEin(EX_BE), .ALUResultin(multiplexer_11_out), .RESET(1'b0),
    .EN(EN), .CLK(CLK), .RegWriteout(MEM_RegWrite), .MemToRegout(MEM_MemToReg), .MemWriteout(MemWrite),
    .ALUOPout(MEM_AluOP), .ALUSrcout(MEM_AluSrcB), .ecallout(MEM_ecall), .S_typeout(MEM_S_type),
    .BEQout(MEM_BEQ), .BNEout(MEM_BEQ), .JALout(MEM_JAL), .JALRout(MEM_JALR), .AUIPCout(MEM_AUIPC),
    .LBout(MEM_LB), .BGEout(MEM_BGE), .R1out(MEM_R1), .R2out(MDin), .W_out(MEM_W_num), .immout(MEM_imm),
    .BEaddrout(MEM_BEaddr), .PCout(M_PC), .nextPCout(MEM_nextPC), .JALaddrout(MEM_JALaddr), .IRout(MEM_IR),
    .BEout(MEM_BE), .ALUResultout(MEM_ALUout));
  RAM #(.addrWidth(10), .dataWidth(32), .bus("separate"), .Select("high")) ram_1 (
    .addr(MEM_ALUout[11:2]), .din(MDin), .data(ram_1_data), .str(MemWrite), .clk(CLK), .ld(not_12_out));  // open: sel, clr
  not not_12 (not_12_out, MemWrite);
  Multiplexer #(.select(2), .width(8), .disabled("Z"), .enable("false")) multiplexer_12 (
    .in0(ram_1_data[7:0]), .in1(ram_1_data[15:8]), .in2(ram_1_data[23:16]), .in3(ram_1_data[31:24]),
    .out(multiplexer_12_out), .sel(MEM_ALUout[1:0]));
  assign bit_extender_4_out = {{24{multiplexer_12_out[7]}}, multiplexer_12_out};  // Bit_Extender bit_extender_4
  Multiplexer #(.select(1), .width(32), .disabled("Z"), .enable("false")) multiplexer_13 (
    .in0(ram_1_data), .in1(bit_extender_4_out), .out(multiplexer_13_out), .sel(MEM_LB));
  MEM_WB mem_wb_1 (
    .RegWritein(MEM_RegWrite), .MemToRegin(MEM_MemToReg), .MemWritein(MemWrite), .ALUOPin(MEM_AluOP),
    .ALUSrcin(MEM_AluSrcB), .ecallin(MEM_ecall), .S_typein(MEM_S_type), .BEQin(MEM_BEQ), .BNEin(MEM_BEQ),
    .JALin(MEM_JAL), .JALRin(MEM_JALR), .AUIPCin(MEM_AUIPC), .LBin(MEM_LB), .BGEin(MEM_BGE),
    .W_in(MEM_W_num), .immin(MEM_imm), .BEaddrin(MEM_BEaddr), .PCin(M_PC), .nextPCin(MEM_nextPC),
    .JALaddrin(MEM_JALaddr), .IRin(MEM_IR), .BEin(MEM_BE), .ALUResultin(MEM_ALUout), .RESET(1'b0), .EN(EN),
    .CLK(CLK), .RegWriteout(RegWrite), .MemToRegout(WB_MemToReg), .MemWriteout(WB_MemWrite),
    .ALUOPout(WB_AluOP), .ALUSrcout(WB_AluSrcB), .ecallout(WB_ecall), .S_typeout(WB_S_type), .BEQout(WB_BEQ),
    .BNEout(WB_BNE), .JALout(WB_JAL), .JALRout(WB_JALR), .AUIPCout(WB_AUIPC), .LBout(WB_LB), .BGEout(WB_BGE),
    .W_out(WB_W_num), .immout(WB_imm), .BEaddrout(WB_BEaddr), .PCout(WB_PC), .nextPCout(WB_nextPC),
    .JALaddrout(WB_JALaddr), .IRout(WB_IR), .BEout(WB_BE), .ALUResultout(mem_wb_1_aluresultout),
    .Memin(multiplexer_13_out), .Memout(mem_wb_1_memout), .R1in(MEM_R1), .R1out(WB_R1), .R2in(MDin),
    .R2out(WB_R2));
  Multiplexer #(.select(1), .width(32), .disabled("Z"), .enable("false")) multiplexer_14 (
    .in0(mem_wb_1_aluresultout), .in1(mem_wb_1_memout), .out(multiplexer_14_out), .sel(WB_MemToReg));
  or or_7 (or_7_out, WB_JAL, WB_JALR);
  Multiplexer #(.select(1), .width(32), .disabled("Z"), .enable("false")) multiplexer_15 (
    .in0(multiplexer_14_out), .in1(WB_nextPC), .out(RDin), .sel(or_7_out));

  // Other names for the same wires on the sheet: ID_W_num[4:0] = ID_IR[11:7]; ID_IR (some bits) = funct[4:2];
  //   MEM_BNE = MEM_BEQ; MEM_MemWrite = MemWrite; MEM_PC[31:0] = M_PC; MEM_R2[31:0] = MDin; WB_RegWrite = RegWrite

  // Notes on the sheet:
  //   中断源
  //   时空图监测，可删除
  //   中断等待指示
  //   数码管输出
  //   contents of 指令存储器 (hex, n*v repeats v):
  //   100493 100006f 100493 200913 300993 100006f 100493 200913 300993 100006f 100493 200913 300993
  //   100006f 100493 200913 300993 40c000ef 100413 100493 1f49493 900533 2200893 73 24d493 48463 fedff06f
  //   900533 2200893 73 100493 249493 900533 2200893 73 48463 fedff06f 100493 1f49493 900533 2200893 73
  //   4034d493 900533 2200893 73 4044d493 900533 2200893 73 4044d493 900533 2200893 73 4044d493 900533
  //   2200893 73 4044d493 900533 2200893 73 4044d493 900533 2200893 73 4044d493 900533 2200893 73 4044d493
  //   900533 2200893 73 100413 1f41993 41f9d993 433 c00913 300b13 140413 f47413 800293 100313 499993
  //   89e9b3 1300533 2200893 73 406282b3 fe0294e3 140413 f00f93 1f47433 1c41413 800293 100313 49d993
  //   89e9b3 1300533 2200893 73 406282b3 fe0294e3 1c45413 406b0b33 b0463 f95ff06f 2b3 fff2c293 829293
  //   ff2e293 500533 2200893 73 fff00413 493 84a023 140413 448493 84a023 140413 448493 84a023 140413
  //   448493 84a023 140413 448493 84a023 140413 448493 84a023 140413 448493 84a023 140413 448493 84a023
  //   140413 448493 84a023 140413 448493 84a023 140413 448493 84a023 140413 448493 84a023 140413 448493
  //   84a023 140413 448493 84a023 140413 448493 84a023 140413 448493 84a023 140413 448493 140413 433
  //   3c00493 42983 4aa03 149a2b3 28663 134a023 1442023 ffc48493 fe9412e3 800533 2200893 73 440413 3c00493
  //   fc9416e3 a00893 73 fff00293 7700493 849493 7748493 900533 2200893 73 1000e13 54c4b3 900533 2200893
  //   73 fffe0e13 fe0e16e3 a00893 73 13 430497 900533 2200893 73 430497 900533 2200893 73 430497 900533
  //   2200893 73 430497 900533 2200893 73 430497 900533 2200893 73 430497 900533 2200893 73 430497 900533
  //   2200893 73 430497 900533 2200893 73 a00893 73 313 1000e13 13 8400493 849493 8348493 400913 891913
  //   490913 849493 8248493 849493 8148493 891913 490913 891913 490913 932023 12484b3 430313 fffe0e13
  //   fe0e18e3 2000e13 313 30483 900533 2200893 73 130313 fffe0e13 fe0e14e3 a00893 73 f00493 900533
  //   2200893 73 fff48493 fe04d8e3 a00893 73 413 140413 800533 2200893 73 240413 800533 2200893 73 340413
  //   800533 2200893 73 440413 800533 2200893 73 540413 800533 2200893 73 640413 800533 2200893 73 740413
  //   800533 2200893 73 840413 800533 2200893 2200893 73 8067
  //   指令探针
  //   控制位
  //   流水调试日志用
  //   暂停节拍，不能为0
  //   戳工具置1进入计数暂停模式，ctrl+k时钟自动运行到对应节拍暂停
  //   ctrl+k关闭时钟连续运行，将控制位置零，进入单步调试模式调试
  //   JALR
  //   URET
  //   可计数暂停的时钟源
  //   Bne
  //   MemToReg
  //   MemWrite
  //   AluOP
  //   AluSrcB
  //   RegWrite
  //   为方便自动评测，需要输出流水线各段保存的PC值，注意是PC不是PC+4，另外ID段寄存器写入信息，Mem段内存写入信息也要输出
endmodule

module \中断按键参考电路  (
  input  \同步清零信号 ,
  output \与中断屏蔽位与 
);

  wire \_1号中断_out , and_1_out, clock_1_out, d_ff_1_q, or_1_out, or_2_out;

  Clock #(.highDuration(1), .lowDuration(1)) clock_1 (.out(clock_1_out));
  Button \_1号中断  (.out(\_1号中断_out ));
  LED #(.active("true")) \_1号中断等待指示灯  (.in(or_1_out));
  or or_1 (or_1_out, \与中断屏蔽位与 , d_ff_1_q);
  D_Flip_Flop #(.trigger("rising"), .Pre_Clr_Positions("LEGACY"), .NegatePresetClear("false"), .enable("true"), .NewFFLayout("false")) d_ff_1 (
    .clk(\_1号中断_out ), .D(1'b1), .Q(d_ff_1_q), .reset(\与中断屏蔽位与 ));  // open: Qn, preset, en
  or or_2 (or_2_out, d_ff_1_q, \与中断屏蔽位与 );
  and and_1 (and_1_out, or_2_out, ~\同步清零信号 );  // AND_Gate
  D_Flip_Flop #(.trigger("rising"), .Pre_Clr_Positions("LEGACY"), .NegatePresetClear("false"), .enable("true"), .NewFFLayout("false")) IR1 (
    .clk(clock_1_out), .D(and_1_out), .Q(\与中断屏蔽位与 ));  // open: Qn, preset, en, reset

  // Notes on the sheet:
  //   中断信号采样参考电路
  //   Reset 
endmodule

module \单周期_单级中断  (
  input  IR1,
  input  IR2,
  input  IR3,
  output RegWrite,
  output MemWrite,
  output [31:0] PC,
  output [31:0] IR,
  output [31:0] RDin,
  output [31:0] MDin,
  output [31:0] LedData,
  output [31:0] out_11
);

  wire Aluequal, Alugreatequal, Aluless, AluSrcB, and_1_out, and_2_out, and_3_out, and_4_out, and_5_out,
       and_7_out, and_8_out, and_9_out, AUIPC, BE, BEQ, BGE, BNE, CLK, clock_1_out, clock_2_out, clock_3_out,
       clock_4_out, comparator_1_eq, comparator_2_eq, comparator_3_eq, comparator_4_eq, comparator_5_eq,
       comparator_6_eq, comparator_7_eq, comparator_7_lt, CSR, d_ff_1_q, d_ff_2_q, d_ff_3_q, d_ff_4_q, ecall,
       Go, halt, IE, interr, IR1_q, IR1_reset, IR1_t, IR2_q, IR2_reset, IR2_t, IR3_q, IR3_reset, IR3_t, IRA,
       IRB, IRC, JAL, JALR, LB, MemToReg, nand_1_out, not_1_out, not_2_out, not_3_out, not_4_out, not_5_out,
       not_6_out, not_7_out, or_1_out, or_6_out, or_7_out, or_8_out, or_11_out, or_13_out,
       priority_encoder_1_gs, RST, S_type, URET, W1, W2, W3;
  wire [1:0] interrID, register_4_q;
  wire [3:0] AluOP;
  wire [4:0] multiplexer_2_out, multiplexer_3_out;
  wire [7:0] multiplexer_10_out;
  wire [11:0] multiplexer_4_out;
  wire [12:0] CNT_num;
  wire [31:0] Alures, and_10_out, BEaddr, bit_extender_1_out, bit_extender_2_out, bit_extender_3_out,
       bit_extender_4_out, EPC, JALaddr, multiplexer_5_out, multiplexer_6_out, multiplexer_7_out,
       multiplexer_8_out, multiplexer_11_out, multiplexer_13_out, multiplexer_14_out, nextPC, not_8_out,
       PCnew, R1, ram_1_data, shifter_1_out, shifter_2_out;

  Button \u_继续运行  (.out(Go));
  Button _1 (.out(IRA));
  Button _2 (.out(IRB));
  Button _3 (.out(IRC));
  LED #(.active("true")) led_1 (.in(W1));
  LED #(.active("true")) led_2 (.in(W2));
  LED #(.active("true")) led_3 (.in(W3));
  Hex_Digit_Display hex_digit_display_1 (.value(LedData[31:28]));  // open: dp
  Comparator #(.width(16), .mode("twosComplement")) comparator_1 (
    .a(16'h23b), .b({3'b000, CNT_num}), .eq(comparator_1_eq));  // open: gt, lt
  Comparator #(.width(16), .mode("twosComplement")) comparator_2 (
    .a({3'b000, CNT_num}), .b(16'h1), .eq(comparator_2_eq));  // open: gt, lt
  Comparator #(.width(16), .mode("twosComplement")) comparator_3 (
    .a({3'b000, CNT_num}), .b(16'h4), .eq(comparator_3_eq));  // open: gt, lt
  Comparator #(.width(16), .mode("twosComplement")) comparator_4 (
    .a({3'b000, CNT_num}), .b(16'h7), .eq(comparator_4_eq));  // open: gt, lt
  Hex_Digit_Display hex_digit_display_2 (.value(LedData[27:24]));  // open: dp
  Hex_Digit_Display hex_digit_display_3 (.value(LedData[23:20]));  // open: dp
  or or_1 (or_1_out, comparator_1_eq, comparator_2_eq);
  assign IRA = or_1_out ? ~CLK : 1'bz;  // Controlled_Inverter controlled_inverter_1
  assign IRB = comparator_3_eq ? ~CLK : 1'bz;  // Controlled_Inverter controlled_inverter_2
  assign IRC = comparator_4_eq ? ~CLK : 1'bz;  // Controlled_Inverter controlled_inverter_3
  Hex_Digit_Display hex_digit_display_4 (.value(LedData[19:16]));  // open: dp
  Hex_Digit_Display hex_digit_display_5 (.value(LedData[15:12]));  // open: dp
  Pull_Resistor #(.pull(0)) pull_resistor_1 (.node(IRA));
  Pull_Resistor #(.pull(0)) pull_resistor_2 (.node(IRB));
  Pull_Resistor #(.pull(0)) pull_resistor_3 (.node(IRC));
  Hex_Digit_Display hex_digit_display_6 (.value(LedData[11:8]));  // open: dp
  Hex_Digit_Display hex_digit_display_7 (.value(LedData[7:4]));  // open: dp
  // Probe on {3'b000, CNT_num}
  Hex_Digit_Display hex_digit_display_8 (.value(LedData[3:0]));  // open: dp
  Register #(.width(32), .trigger("rising"), .Select("low")) u_PC (
    .D(PCnew), .en(not_1_out), .Q(PC), .clk(CLK), .clr(RST));
  not not_1 (not_1_out, halt);
  Comparator #(.width(32), .mode("twosComplement")) comparator_5 (
    .a(R1), .b(32'h22), .eq(comparator_5_eq));  // open: gt, lt
  or or_2 (W1, IR1_q, d_ff_1_q);
  or or_3 (W2, IR2_q, d_ff_2_q);
  or or_4 (W3, IR3_q, d_ff_3_q);
  Adder #(.width(32)) adder_1 (.a(PC), .b(32'h4), .out(nextPC));  // open: cin, cout
  not not_2 (not_2_out, comparator_5_eq);
  and and_1 (and_1_out, comparator_5_eq, ecall);
  D_Flip_Flop #(.trigger("rising"), .Pre_Clr_Positions("LEGACY"), .NegatePresetClear("false"), .enable("true"), .NewFFLayout("false")) d_ff_1 (
    .clk(IR1_t), .D(1'b1), .Q(d_ff_1_q), .reset(IR1_q));  // open: Qn, preset, en
  D_Flip_Flop #(.trigger("rising"), .Pre_Clr_Positions("LEGACY"), .NegatePresetClear("false"), .enable("true"), .NewFFLayout("false")) d_ff_2 (
    .clk(IR2_t), .D(1'b1), .Q(d_ff_2_q), .reset(IR2_q));  // open: Qn, preset, en
  D_Flip_Flop #(.trigger("rising"), .Pre_Clr_Positions("LEGACY"), .NegatePresetClear("false"), .enable("true"), .NewFFLayout("false")) d_ff_3 (
    .clk(IR3_t), .D(1'b1), .Q(d_ff_3_q), .reset(IR3_q));  // open: Qn, preset, en
  or or_5 (IR1_t, IR1, IRA);
  // RiscV_Probe riscv_probe_1: pin names not known; wires that end beside it: IR
  and and_2 (and_2_out, ecall, not_2_out);
  Register #(.width(32), .trigger("rising"), .Select("low")) register_1 (
    .D(MDin), .en(and_1_out), .Q(LedData), .clk(CLK));  // open: clr
  Clock #(.highDuration(1), .lowDuration(1)) clock_1 (.out(clock_1_out));
  or or_6 (or_6_out, d_ff_1_q, IR1_q);
  and and_3 (and_3_out, or_6_out, not_3_out);
  not not_3 (not_3_out, IR1_reset);
  Clock #(.highDuration(1), .lowDuration(1)) clock_2 (.out(clock_2_out));
  or or_7 (or_7_out, d_ff_2_q, IR2_q);
  and and_4 (and_4_out, or_7_out, not_4_out);
  not not_4 (not_4_out, IR2_reset);
  Clock #(.highDuration(1), .lowDuration(1)) clock_3 (.out(clock_3_out));
  or or_8 (or_8_out, d_ff_3_q, IR3_q);
  and and_5 (and_5_out, or_8_out, not_5_out);
  not not_5 (not_5_out, IR3_reset);
  or or_9 (IR2_t, IR2, IRB);
  ROM #(.addrWidth(10), .dataWidth(32), .Select("high")) rom_1 (.addr(PC[11:2]), .data(IR));
  Multiplexer #(.select(1), .width(1), .disabled("Z"), .enable("false")) multiplexer_1 (
    .in0(and_2_out), .in1(1'b0), .out(halt), .sel(Go));
  D_Flip_Flop #(.trigger("rising"), .Pre_Clr_Positions("LEGACY"), .NegatePresetClear("false"), .enable("true"), .NewFFLayout("false")) u_IR1 (
    .clk(clock_1_out), .D(and_3_out), .Q(IR1_q));  // open: Qn, preset, en, reset
  D_Flip_Flop #(.trigger("rising"), .Pre_Clr_Positions("LEGACY"), .NegatePresetClear("false"), .enable("true"), .NewFFLayout("false")) u_IR2 (
    .clk(clock_2_out), .D(and_4_out), .Q(IR2_q));  // open: Qn, preset, en, reset
  D_Flip_Flop #(.trigger("rising"), .Pre_Clr_Positions("LEGACY"), .NegatePresetClear("false"), .enable("true"), .NewFFLayout("false")) u_IR3 (
    .clk(clock_3_out), .D(and_5_out), .Q(IR3_q));  // open: Qn, preset, en, reset
  or or_10 (IR3_t, IR3, IRC);
  \单周期硬布线控制器  \u_单周期硬布线控制器_1  (
    .Funct({IR[30], IR[25], IR[14:12]}), .OP(IR[6:2]), .ALU_OP(AluOP), .MemToReg(MemToReg),
    .MemWrite(MemWrite), .ALU_SRC(AluSrcB), .RegWrite(RegWrite), .ecall(ecall), .S_type(S_type), .Jalr(JALR),
    .Beq(BEQ), .JAL(JAL), .Bne(BNE), .in_3(IR[21]), .uret(URET), .CSR(CSR), .AUIPC(AUIPC), .LB(LB), .BGE(BGE));  // open: RSread, RTread
  Multiplexer #(.select(1), .width(5), .disabled("Z"), .enable("false")) multiplexer_2 (
    .in0(IR[19:15]), .in1(5'b10001), .out(multiplexer_2_out), .sel(ecall));
  Multiplexer #(.select(1), .width(5), .disabled("Z"), .enable("false")) multiplexer_3 (
    .in0(IR[24:20]), .in1(5'b01010), .out(multiplexer_3_out), .sel(ecall));
  Multiplexer #(.select(1), .width(12), .disabled("Z"), .enable("false")) multiplexer_4 (
    .in0(IR[31:20]), .in1({IR[31:25], IR[11:7]}), .out(multiplexer_4_out), .sel(S_type));
  Priority_Encoder #(.select(2), .disabled("Z")) priority_encoder_1 (
    .in1(IR1_q), .in2(IR2_q), .in3(IR3_q), .out(interrID), .gs(priority_encoder_1_gs));  // open: in0, en_out, en_in
  assign bit_extender_1_out = {{20{multiplexer_4_out[11]}}, multiplexer_4_out};  // Bit_Extender bit_extender_1
  assign bit_extender_2_out = {{20{IR[31]}}, {IR[31], IR[7], IR[30:25], IR[11:8]}};  // Bit_Extender bit_extender_2
  assign bit_extender_3_out = {{12{IR[31]}}, {IR[31], IR[19:12], IR[20], IR[30:21]}};  // Bit_Extender bit_extender_3
  and and_6 (interr, priority_encoder_1_gs, IE);
  Regifile regifile_1 (
    .Din(RDin), .Clk(CLK), .R1(R1), .R2(MDin), .WE(RegWrite), .W_num(IR[11:7]), .R1_num(multiplexer_2_out),
    .R2_num(multiplexer_3_out));
  Shifter #(.width(32), .shift("ll")) shifter_1 (.in(bit_extender_2_out), .\dist (5'b00001), .out(shifter_1_out));
  Shifter #(.width(32), .shift("ll")) shifter_2 (.in(bit_extender_3_out), .\dist (5'b00001), .out(shifter_2_out));
  ALU alu_1 (
    .X(R1), .Y(multiplexer_5_out), .AluOP(AluOP), .Equal(Aluequal), .Result(Alures), .out_4(Alugreatequal),
    .out_6(Aluless));  // open: Result_2
  Multiplexer #(.select(1), .width(32), .disabled("Z"), .enable("false")) multiplexer_5 (
    .in0(MDin), .in1(bit_extender_1_out), .out(multiplexer_5_out), .sel(AluSrcB));
  Adder #(.width(32)) adder_2 (.a(shifter_1_out), .b(PC), .out(BEaddr), .cin(1'b0));  // open: cout
  Adder #(.width(32)) adder_3 (.a(shifter_2_out), .b(PC), .out(JALaddr), .cin(1'b0));  // open: cout
  Comparator #(.width(16), .mode("twosComplement")) comparator_6 (
    .a({3'b000, CNT_num}), .b({16{1'b0}}), .eq(comparator_6_eq));  // open: gt, lt
  or or_11 (or_11_out, comparator_6_eq, URET, interr);
  not not_6 (not_6_out, interr);
  D_Flip_Flop #(.trigger("high"), .Pre_Clr_Positions("LEGACY"), .NegatePresetClear("false"), .enable("true"), .NewFFLayout("false")) d_ff_4 (.Q(d_ff_4_q));  // open: clk, D, Qn, preset, en, reset
  // Probe on 13'hc
  not not_7 (not_7_out, Aluequal);
  Multiplexer #(.select(1), .width(32), .disabled("Z"), .enable("false")) multiplexer_6 (
    .in0(nextPC), .in1(BEaddr), .out(multiplexer_6_out), .sel(BE));
  assign not_8_out = ~32'h1;  // NOT_Gate not_8, 32 bits wide
  Multiplexer #(.select(2), .width(32), .disabled("Z"), .enable("false")) multiplexer_7 (
    .in1(32'h30ac), .in2(32'h3150), .in3(32'h31f4), .out(multiplexer_7_out), .sel(interrID));  // open: in0
  Register #(.width(1), .trigger("rising"), .Select("low")) register_2 (
    .D(not_6_out), .en(or_11_out), .Q(IE), .clk(CLK), .clr(RST));
  Comparator #(.width(13), .mode("twosComplement")) comparator_7 (
    .a(CNT_num), .b(13'hc), .eq(comparator_7_eq), .lt(comparator_7_lt));  // open: gt
  Clock #(.highDuration(1), .lowDuration(1)) clock_4 (.out(clock_4_out));
  and and_7 (and_7_out, Aluequal, BEQ);
  and and_8 (and_8_out, not_7_out, BNE);
  and and_9 (and_9_out, Alugreatequal, BGE);
  RAM #(.addrWidth(10), .dataWidth(32), .bus("separate"), .Select("high")) ram_1 (
    .addr(Alures[11:2]), .din(MDin), .data(ram_1_data), .str(MemWrite), .clk(CLK));  // open: sel, ld, clr
  Multiplexer #(.select(1), .width(32), .disabled("Z"), .enable("false")) multiplexer_8 (
    .in0(multiplexer_6_out), .in1(JALaddr), .out(multiplexer_8_out), .sel(JAL));
  Multiplexer #(.select(1), .width(32), .disabled("Z"), .enable("false")) multiplexer_9 (
    .in0(multiplexer_8_out), .in1(and_10_out), .out(out_11), .sel(JALR));
  assign and_10_out = Alures & not_8_out;  // AND_Gate and_10, 32 bits wide
  Register #(.width(32), .trigger("rising"), .Select("low")) register_3 (
    .D(out_11), .en(interr), .Q(EPC), .clk(CLK), .clr(RST));
  Counter #(.width(13), .max('h1fff), .ongoal("stay"), .trigger("rising"), .behavior("old")) counter_1 (
    .count(comparator_7_lt), .Q(CNT_num), .clk(clock_4_out));  // open: load, D, carry, clr, preset
  or or_12 (BE, and_7_out, and_8_out, and_9_out);
  Multiplexer #(.select(2), .width(8), .disabled("Z"), .enable("false")) multiplexer_10 (
    .in0(ram_1_data[7:0]), .in1(ram_1_data[15:8]), .in2(ram_1_data[23:16]), .in3(ram_1_data[31:24]),
    .out(multiplexer_10_out), .sel(Alures[1:0]));
  Multiplexer #(.select(1), .width(32), .disabled("Z"), .enable("false")) multiplexer_11 (
    .in0(out_11), .in1(multiplexer_7_out), .out(multiplexer_11_out), .sel(interr));
  nand nand_1 (nand_1_out, d_ff_4_q, comparator_7_eq);
  assign bit_extender_4_out = {{24{multiplexer_10_out[7]}}, multiplexer_10_out};  // Bit_Extender bit_extender_4
  Multiplexer #(.select(1), .width(32), .disabled("Z"), .enable("false")) multiplexer_12 (
    .in0(multiplexer_11_out), .in1(EPC), .out(PCnew), .sel(URET));
  assign CLK = nand_1_out ? clock_4_out : 1'bz;  // Controlled_Buffer controlled_buffer_1
  Pull_Resistor #(.pull(1)) pull_resistor_4 (.node(CLK));
  Multiplexer #(.select(1), .width(32), .disabled("Z"), .enable("false")) multiplexer_13 (
    .in0(ram_1_data), .in1(bit_extender_4_out), .out(multiplexer_13_out), .sel(LB));
  Multiplexer #(.select(1), .width(32), .disabled("Z"), .enable("false")) multiplexer_14 (
    .in0(Alures), .in1(multiplexer_13_out), .out(multiplexer_14_out), .sel(MemToReg));
  or or_13 (or_13_out, JAL, JALR);
  Register #(.width(2), .trigger("rising"), .Select("low")) register_4 (
    .D(interrID), .en(interr), .Q(register_4_q), .clk(CLK));  // open: clr
  Demultiplexer #(.select(2), .width(1), .tristate("false"), .disabled("Z"), .enable("false")) demultiplexer_1 (
    .out1(IR1_reset), .out2(IR2_reset), .out3(IR3_reset), .in(URET), .sel(register_4_q));  // open: out0
  Multiplexer #(.select(1), .width(32), .disabled("Z"), .enable("false")) multiplexer_15 (
    .in0(multiplexer_14_out), .in1(nextPC), .out(RDin), .sel(or_13_out));

  // Other names for the same wires on the sheet: PCaddr[31:0] = out_11; R2[31:0] = MDin; 总周期数[12:0] = CNT_num

  // Notes on the sheet:
  //   中断源
  //   中断等待指示
  //   总复位信号应将除ROM以外所有存储组件全部清零
  //   单级中断测试信号模拟器
  //   数码管输出
  //   数码管输出应该用寄存器锁存，否则显示数据只能一闪而过
  //   指令探针
  //   指令存储器
  //   指令字
  //   contents of rom_1 (hex, n*v repeats v):
  //   7d000113 100413 1f41993 41f9d993 433 c00913 800b13 140413 f47413 800293 100313 499993 89e9b3 1300533
  //   2200893 73 406282b3 fe0294e3 140413 f00f93 1f47433 1c41413 800293 100313 49d993 89e9b3 1300533
  //   2200893 73 406282b3 fe0294e3 1c45413 406b0b33 b0463 f95ff06f 2b3 fff2c293 1029293 fff2e293 500533
  //   2200893 73 f5dff06f 1112023 410113 a12023 410113 812023 410113 1312023 410113 1412023 410113 1512023
  //   410113 1612023 410113 100b13 300a13 100a93 1600433 441413 14469b3 1300533 2200893 73 fe0416e3
  //   415a0a33 fe0a10e3 ffc10113 12b03 ffc10113 12a83 ffc10113 12a03 ffc10113 12983 ffc10113 12403
  //   ffc10113 12503 ffc10113 12883 200073 1112023 410113 a12023 410113 812023 410113 1312023 410113
  //   1412023 410113 1512023 410113 1612023 410113 200b13 300a13 100a93 1600433 441413 14469b3 1300533
  //   2200893 73 fe0416e3 415a0a33 fe0a10e3 ffc10113 12b03 ffc10113 12a83 ffc10113 12a03 ffc10113 12983
  //   ffc10113 12403 ffc10113 12503 ffc10113 12883 200073 1112023 410113 a12023 410113 812023 410113
  //   1312023 410113 1412023 410113 1512023 410113 1612023 410113 300b13 300a13 100a93 1600433 441413
  //   14469b3 1300533 2200893 73 fe0416e3 415a0a33 fe0a10e3 ffc10113 12b03 ffc10113 12a83 ffc10113 12a03
  //   ffc10113 12983 ffc10113 12403 ffc10113 12503 ffc10113 12883 200073
  //   JAL
  //   JALR
  //   URET
  //   Bne
  //   MemToReg
  //   MemWrite
  //   AluOP
  //   AluSrcB
  //   RegWrite
  //   为方便自动评测，需要输出PC，IR，寄存器堆写如数据RDin
  //   RAM写使能MemWrite、RAM写入数据MDin等信号
  //   数据存储器
  //   控制位
  //   暂停节拍，不能为0
  //   戳工具置1进入计数暂停模式，ctrl+k时钟自动运行到对应节拍暂停
  //   ctrl+k关闭时钟连续运行，将控制位置零，进入单步调试模式调试
  //   可计数暂停的时钟源
endmodule

module \单周期_多级中断  (
  input  IR1,
  input  IR2,
  input  IR3,
  output RegWrite,
  output MemWrite,
  output [31:0] PC,
  output [31:0] IR,
  output [31:0] RDin,
  output [31:0] MDin,
  output [31:0] LedData
);

  wire Aluequal, Alugreatequal, Aluless, AluSrcB, and_1_out, and_2_out, and_4_out, and_5_out, and_6_out,
       and_8_out, and_9_out, and_10_out, AUIPC, BE, BEQ, BGE, BNE, CLK, clock_1_out, clock_2_out,
       clock_3_out, clock_4_out, comparator_1_eq, comparator_2_eq, comparator_3_eq, comparator_4_eq,
       comparator_5_eq, comparator_6_eq, comparator_7_eq, comparator_7_lt, comparator_8_eq, CSR, d_ff_1_q,
       d_ff_2_q, d_ff_3_q, d_ff_4_q, demultiplexer_1_out1, demultiplexer_1_out2, demultiplexer_1_out3,
       demultiplexer_3_out1, demultiplexer_3_out2, demultiplexer_3_out3, ecall, Go, halt, IE, interr, IR1_q,
       IR1_reset, IR1_t, IR2_q, IR2_reset, IR2_t, IR3_q, IR3_reset, IR3_t, IRA, IRB, IRC, JAL, JALR, LB,
       MemToReg, multiplexer_4_out, nand_1_out, not_1_out, not_2_out, not_3_out, not_4_out, not_5_out,
       not_6_out, not_7_out, not_8_out, not_10_out, not_11_out, or_1_out, or_2_out, or_8_out, or_9_out,
       or_10_out, or_12_out, or_14_out, priority_encoder_1_gs, register_2_q, register_3_q, register_4_q, RST,
       S_type, URET, W1, W2, W3;
  wire [1:0] interrID, interrupting;
  wire [3:0] AluOP;
  wire [4:0] multiplexer_1_out, multiplexer_2_out;
  wire [7:0] multiplexer_9_out;
  wire [11:0] multiplexer_3_out;
  wire [12:0] CNT_num;
  wire [15:0] \总周期数 ;
  wire [31:0] Alures, and_11_out, BEaddr, bit_extender_1_out, bit_extender_2_out, bit_extender_3_out,
       bit_extender_4_out, EPC, JALaddr, multiplexer_5_out, multiplexer_6_out, multiplexer_7_out,
       multiplexer_8_out, multiplexer_11_out, multiplexer_12_out, multiplexer_14_out, nextPC, not_9_out,
       PCaddr, PCnew, R1, ram_1_data, register_6_q, register_7_q, register_8_q, shifter_1_out, shifter_2_out;

  Button \u_继续运行  (.out(Go));
  Button _1 (.out(IRA));
  Button _2 (.out(IRB));
  Button _3 (.out(IRC));
  LED #(.active("true")) led_1 (.in(W1));
  LED #(.active("true")) led_2 (.in(W2));
  LED #(.active("true")) led_3 (.in(W3));
  Hex_Digit_Display hex_digit_display_1 (.value(LedData[31:28]));  // open: dp
  Comparator #(.width(16), .mode("twosComplement")) comparator_1 (
    .a(\总周期数 ), .b(16'h7), .eq(comparator_1_eq));  // open: gt, lt
  Comparator #(.width(16), .mode("twosComplement")) comparator_2 (
    .a(\总周期数 ), .b(16'h241), .eq(comparator_2_eq));  // open: gt, lt
  Hex_Digit_Display hex_digit_display_2 (.value(LedData[27:24]));  // open: dp
  Hex_Digit_Display hex_digit_display_3 (.value(LedData[23:20]));  // open: dp
  Comparator #(.width(16), .mode("twosComplement")) comparator_3 (
    .a(16'h258), .b(\总周期数 ), .eq(comparator_3_eq));  // open: gt, lt
  or or_1 (or_1_out, comparator_3_eq, comparator_4_eq);
  Comparator #(.width(16), .mode("twosComplement")) comparator_4 (
    .a(\总周期数 ), .b(16'h1), .eq(comparator_4_eq));  // open: gt, lt
  Comparator #(.width(16), .mode("twosComplement")) comparator_5 (
    .a(\总周期数 ), .b(16'h4), .eq(comparator_5_eq));  // open: gt, lt
  or or_2 (or_2_out, comparator_1_eq, comparator_2_eq);
  Hex_Digit_Display hex_digit_display_4 (.value(LedData[15:12]));  // open: dp
  Hex_Digit_Display hex_digit_display_5 (.value(LedData[19:16]));  // open: dp
  Pull_Resistor #(.pull(0)) pull_resistor_1 (.node(IRA));
  assign IRA = or_1_out ? ~CLK : 1'bz;  // Controlled_Inverter controlled_inverter_1
  Pull_Resistor #(.pull(0)) pull_resistor_2 (.node(IRB));
  assign IRB = comparator_5_eq ? ~CLK : 1'bz;  // Controlled_Inverter controlled_inverter_2
  Pull_Resistor #(.pull(0)) pull_resistor_3 (.node(IRC));
  assign IRC = or_2_out ? ~CLK : 1'bz;  // Controlled_Inverter controlled_inverter_3
  Hex_Digit_Display hex_digit_display_6 (.value(LedData[11:8]));  // open: dp
  Hex_Digit_Display hex_digit_display_7 (.value(LedData[7:4]));  // open: dp
  // Probe on \总周期数 
  Hex_Digit_Display hex_digit_display_8 (.value(LedData[3:0]));  // open: dp
  not not_1 (not_1_out, halt);
  Counter #(.width(16), .max('hffff), .ongoal("wrap"), .trigger("rising"), .behavior("new")) counter_1 (
    .D({16{1'b0}}), .count(not_1_out), .Q(\总周期数 ), .clk(CLK));  // open: load, carry, clr, preset, down
  Register #(.width(32), .trigger("rising"), .Select("low")) u_PC (
    .D(PCnew), .en(not_2_out), .Q(PC), .clk(CLK), .clr(RST));
  not not_2 (not_2_out, halt);
  Comparator #(.width(32), .mode("twosComplement")) comparator_6 (
    .a(R1), .b(32'h22), .eq(comparator_6_eq));  // open: gt, lt
  or or_3 (W1, IR1_q, d_ff_1_q);
  or or_4 (W2, IR2_q, d_ff_2_q);
  or or_5 (W3, IR3_q, d_ff_3_q);
  or or_6 (IR1_t, IR1, IRA);
  not not_3 (not_3_out, comparator_6_eq);
  and and_1 (and_1_out, comparator_6_eq, ecall);
  D_Flip_Flop #(.trigger("rising"), .Pre_Clr_Positions("LEGACY"), .NegatePresetClear("false"), .enable("true"), .NewFFLayout("false")) d_ff_1 (
    .clk(IR1_t), .D(1'b1), .Q(d_ff_1_q), .reset(IR1_q));  // open: Qn, preset, en
  D_Flip_Flop #(.trigger("rising"), .Pre_Clr_Positions("LEGACY"), .NegatePresetClear("false"), .enable("true"), .NewFFLayout("false")) d_ff_2 (
    .clk(IR2_t), .D(1'b1), .Q(d_ff_2_q), .reset(IR2_q));  // open: Qn, preset, en
  D_Flip_Flop #(.trigger("rising"), .Pre_Clr_Positions("LEGACY"), .NegatePresetClear("false"), .enable("true"), .NewFFLayout("false")) d_ff_3 (
    .clk(IR3_t), .D(1'b1), .Q(d_ff_3_q), .reset(IR3_q));  // open: Qn, preset, en
  or or_7 (IR2_t, IR2, IRB);
  // RiscV_Probe riscv_probe_1: pin names not known; wires that end beside it: IR
  Adder #(.width(32)) adder_1 (.a(PC), .b(32'h4), .out(nextPC));  // open: cin, cout
  not not_4 (not_4_out, Go);
  and and_2 (and_2_out, ecall, not_3_out);
  Register #(.width(32), .trigger("rising"), .Select("low")) register_1 (
    .D(MDin), .en(and_1_out), .Q(LedData), .clk(CLK));  // open: clr
  Clock #(.highDuration(1), .lowDuration(1)) clock_1 (.out(clock_1_out));
  or or_8 (or_8_out, d_ff_1_q, IR1_q);
  not not_5 (not_5_out, IR1_reset);
  Clock #(.highDuration(1), .lowDuration(1)) clock_2 (.out(clock_2_out));
  or or_9 (or_9_out, d_ff_2_q, IR2_q);
  not not_6 (not_6_out, IR2_reset);
  Clock #(.highDuration(1), .lowDuration(1)) clock_3 (.out(clock_3_out));
  or or_10 (or_10_out, d_ff_3_q, IR3_q);
  not not_7 (not_7_out, IR3_reset);
  Demultiplexer #(.select(2), .width(1), .tristate("false"), .disabled("Z"), .enable("false")) demultiplexer_1 (
    .out1(demultiplexer_1_out1), .out2(demultiplexer_1_out2), .out3(demultiplexer_1_out3), .in(interr),
    .sel(interrID));  // open: out0
  ROM #(.addrWidth(10), .dataWidth(32), .Select("high")) rom_1 (.addr(PC[11:2]), .data(IR));
  and and_3 (halt, not_4_out, and_2_out);
  D_Flip_Flop #(.trigger("rising"), .Pre_Clr_Positions("LEGACY"), .NegatePresetClear("false"), .enable("true"), .NewFFLayout("false")) u_IR1 (
    .clk(clock_1_out), .D(and_4_out), .Q(IR1_q));  // open: Qn, preset, en, reset
  and and_4 (and_4_out, or_8_out, not_5_out);
  D_Flip_Flop #(.trigger("rising"), .Pre_Clr_Positions("LEGACY"), .NegatePresetClear("false"), .enable("true"), .NewFFLayout("false")) u_IR2 (
    .clk(clock_2_out), .D(and_5_out), .Q(IR2_q));  // open: Qn, preset, en, reset
  and and_5 (and_5_out, or_9_out, not_6_out);
  D_Flip_Flop #(.trigger("rising"), .Pre_Clr_Positions("LEGACY"), .NegatePresetClear("false"), .enable("true"), .NewFFLayout("false")) u_IR3 (
    .clk(clock_3_out), .D(and_6_out), .Q(IR3_q));  // open: Qn, preset, en, reset
  and and_6 (and_6_out, or_10_out, not_7_out);
  or or_11 (IR3_t, IR3, IRC);
  Register #(.width(1), .trigger("rising"), .Select("low")) register_2 (
    .D(1'b1), .en(demultiplexer_1_out1), .Q(register_2_q), .clk(CLK), .clr(IR1_reset));
  \单周期硬布线控制器  \u_单周期硬布线控制器_1  (
    .Funct({IR[30], IR[25], IR[14:12]}), .OP(IR[6:2]), .ALU_OP(AluOP), .MemToReg(MemToReg),
    .MemWrite(MemWrite), .ALU_SRC(AluSrcB), .RegWrite(RegWrite), .ecall(ecall), .S_type(S_type), .Jalr(JALR),
    .Beq(BEQ), .JAL(JAL), .Bne(BNE), .in_3(IR[21]), .uret(URET), .CSR(CSR), .AUIPC(AUIPC), .LB(LB), .BGE(BGE));  // open: RSread, RTread
  Multiplexer #(.select(1), .width(5), .disabled("Z"), .enable("false")) multiplexer_1 (
    .in0(IR[19:15]), .in1(5'b10001), .out(multiplexer_1_out), .sel(ecall));
  Multiplexer #(.select(1), .width(5), .disabled("Z"), .enable("false")) multiplexer_2 (
    .in0(IR[24:20]), .in1(5'b01010), .out(multiplexer_2_out), .sel(ecall));
  Multiplexer #(.select(1), .width(12), .disabled("Z"), .enable("false")) multiplexer_3 (
    .in0(IR[31:20]), .in1({IR[31:25], IR[11:7]}), .out(multiplexer_3_out), .sel(S_type));
  not not_8 (not_8_out, multiplexer_4_out);
  Multiplexer #(.select(2), .width(1), .disabled("Z"), .enable("false")) multiplexer_4 (
    .in0(1'b1), .in1(register_2_q), .in2(register_3_q), .in3(register_4_q), .out(multiplexer_4_out),
    .sel(interrID));
  Register #(.width(1), .trigger("rising"), .Select("low")) register_3 (
    .D(1'b1), .en(demultiplexer_1_out2), .Q(register_3_q), .clk(CLK), .clr(IR2_reset));
  assign bit_extender_1_out = {{20{IR[31]}}, {IR[31], IR[7], IR[30:25], IR[11:8]}};  // Bit_Extender bit_extender_1
  assign bit_extender_2_out = {{12{IR[31]}}, {IR[31], IR[19:12], IR[20], IR[30:21]}};  // Bit_Extender bit_extender_2
  Priority_Encoder #(.select(2), .disabled("Z")) priority_encoder_1 (
    .in0(1'b1), .in1(IR1_q), .in2(IR2_q), .in3(IR3_q), .out(interrID), .gs(priority_encoder_1_gs));  // open: en_out, en_in
  and and_7 (interr, priority_encoder_1_gs, not_8_out, IE);
  Register #(.width(1), .trigger("rising"), .Select("low")) register_4 (
    .D(1'b1), .en(demultiplexer_1_out3), .Q(register_4_q), .clk(CLK), .clr(IR3_reset));
  Regifile regifile_1 (
    .Din(RDin), .Clk(CLK), .R1(R1), .R2(MDin), .WE(RegWrite), .W_num(IR[11:7]), .R1_num(multiplexer_1_out),
    .R2_num(multiplexer_2_out));
  assign bit_extender_3_out = {{20{multiplexer_3_out[11]}}, multiplexer_3_out};  // Bit_Extender bit_extender_3
  Shifter #(.width(32), .shift("ll")) shifter_1 (.in(bit_extender_1_out), .\dist (5'b00001), .out(shifter_1_out));
  Shifter #(.width(32), .shift("ll")) shifter_2 (.in(bit_extender_2_out), .\dist (5'b00001), .out(shifter_2_out));
  or or_12 (or_12_out, CSR, URET, interr);
  Multiplexer #(.select(1), .width(32), .disabled("Z"), .enable("false")) multiplexer_5 (
    .in0(MDin), .in1(bit_extender_3_out), .out(multiplexer_5_out), .sel(AluSrcB));
  Adder #(.width(32)) adder_2 (.a(shifter_1_out), .b(PC), .out(BEaddr), .cin(1'b0));  // open: cout
  Adder #(.width(32)) adder_3 (.a(shifter_2_out), .b(PC), .out(JALaddr), .cin(1'b0));  // open: cout
  T_Flip_Flop #(.trigger("rising"), .Pre_Clr_Positions("ABOVE_BELOW"), .NegatePresetClear("false"), .enable("false"), .NewFFLayout("true")) t_ff_1 (
    .clk(CLK), .T(or_12_out), .Qn(IE));  // open: Q, preset, reset
  ALU alu_1 (
    .X(R1), .Y(multiplexer_5_out), .AluOP(AluOP), .Equal(Aluequal), .Result(Alures), .out_4(Alugreatequal),
    .out_6(Aluless));  // open: Result_2
  D_Flip_Flop #(.trigger("high"), .Pre_Clr_Positions("LEGACY"), .NegatePresetClear("false"), .enable("true"), .NewFFLayout("false")) d_ff_4 (.Q(d_ff_4_q));  // open: clk, D, Qn, preset, en, reset
  // Probe on 13'hcd
  Comparator #(.width(13), .mode("twosComplement")) comparator_7 (
    .a(CNT_num), .b(13'hcd), .eq(comparator_7_eq), .lt(comparator_7_lt));  // open: gt
  Clock #(.highDuration(1), .lowDuration(1)) clock_4 (.out(clock_4_out));
  Multiplexer #(.select(1), .width(32), .disabled("Z"), .enable("false")) multiplexer_6 (
    .in0(nextPC), .in1(BEaddr), .out(multiplexer_6_out), .sel(BE));
  assign not_9_out = ~32'h1;  // NOT_Gate not_9, 32 bits wide
  Multiplexer #(.select(2), .width(32), .disabled("Z"), .enable("false")) multiplexer_7 (
    .in1(32'h30ac), .in2(32'h3158), .in3(32'h3204), .out(multiplexer_7_out), .sel(interrID));  // open: in0
  Counter #(.width(13), .max('h1fff), .ongoal("stay"), .trigger("rising"), .behavior("old")) counter_2 (
    .count(comparator_7_lt), .Q(CNT_num), .clk(clock_4_out));  // open: load, D, carry, clr, preset
  and and_8 (and_8_out, Aluequal, BEQ);
  not not_10 (not_10_out, Aluequal);
  and and_9 (and_9_out, not_10_out, BNE);
  and and_10 (and_10_out, Alugreatequal, BGE);
  RAM #(.addrWidth(10), .dataWidth(32), .bus("separate"), .Select("high")) ram_1 (
    .addr(Alures[11:2]), .din(MDin), .data(ram_1_data), .str(MemWrite), .clk(CLK));  // open: sel, ld, clr
  Multiplexer #(.select(1), .width(32), .disabled("Z"), .enable("false")) multiplexer_8 (
    .in0(multiplexer_6_out), .in1(JALaddr), .out(multiplexer_8_out), .sel(JAL));
  assign and_11_out = Alures & not_9_out;  // AND_Gate and_11, 32 bits wide
  nand nand_1 (nand_1_out, d_ff_4_q, comparator_7_eq);
  or or_13 (BE, and_8_out, and_9_out, and_10_out);
  Multiplexer #(.select(2), .width(8), .disabled("Z"), .enable("false")) multiplexer_9 (
    .in0(ram_1_data[7:0]), .in1(ram_1_data[15:8]), .in2(ram_1_data[23:16]), .in3(ram_1_data[31:24]),
    .out(multiplexer_9_out), .sel(Alures[1:0]));
  Multiplexer #(.select(1), .width(32), .disabled("Z"), .enable("false")) multiplexer_10 (
    .in0(multiplexer_8_out), .in1(and_11_out), .out(PCaddr), .sel(JALR));
  Multiplexer #(.select(1), .width(32), .disabled("Z"), .enable("false")) multiplexer_11 (
    .in0(PCaddr), .in1(multiplexer_7_out), .out(multiplexer_11_out), .sel(interr));
  assign CLK = nand_1_out ? clock_4_out : 1'bz;  // Controlled_Buffer controlled_buffer_1
  Pull_Resistor #(.pull(1)) pull_resistor_4 (.node(CLK));
  assign bit_extender_4_out = {{24{multiplexer_9_out[7]}}, multiplexer_9_out};  // Bit_Extender bit_extender_4
  Multiplexer #(.select(1), .width(32), .disabled("Z"), .enable("false")) multiplexer_12 (
    .in0(ram_1_data), .in1(bit_extender_4_out), .out(multiplexer_12_out), .sel(LB));
  Comparator #(.width(2), .mode("twosComplement")) comparator_8 (
    .a(interrID), .b(interrupting), .eq(comparator_8_eq));  // open: gt, lt
  not not_11 (not_11_out, comparator_8_eq);
  Multiplexer #(.select(1), .width(32), .disabled("Z"), .enable("false")) multiplexer_13 (
    .in0(multiplexer_11_out), .in1(EPC), .out(PCnew), .sel(URET));
  Multiplexer #(.select(1), .width(32), .disabled("Z"), .enable("false")) multiplexer_14 (
    .in0(Alures), .in1(multiplexer_12_out), .out(multiplexer_14_out), .sel(MemToReg));
  or or_14 (or_14_out, JAL, JALR);
  Register #(.width(2), .trigger("rising"), .Select("low")) register_5 (
    .D(interrID), .en(not_11_out), .Q(interrupting), .clk(CLK));  // open: clr
  Demultiplexer #(.select(2), .width(1), .tristate("false"), .disabled("Z"), .enable("false")) demultiplexer_2 (
    .out1(IR1_reset), .out2(IR2_reset), .out3(IR3_reset), .in(URET), .sel(interrupting));  // open: out0
  Multiplexer #(.select(1), .width(32), .disabled("Z"), .enable("false")) multiplexer_15 (
    .in0(multiplexer_14_out), .in1(nextPC), .out(RDin), .sel(or_14_out));
  Demultiplexer #(.select(2), .width(1), .tristate("false"), .disabled("Z"), .enable("false")) demultiplexer_3 (
    .out1(demultiplexer_3_out1), .out2(demultiplexer_3_out2), .out3(demultiplexer_3_out3), .in(interr),
    .sel(interrID));  // open: out0
  Register #(.width(32), .trigger("rising"), .Select("low")) register_6 (
    .D(PCaddr), .en(demultiplexer_3_out1), .Q(register_6_q), .clk(CLK));  // open: clr
  Register #(.width(32), .trigger("rising"), .Select("low")) register_7 (
    .D(PCaddr), .en(demultiplexer_3_out2), .Q(register_7_q), .clk(CLK));  // open: clr
  Register #(.width(32), .trigger("rising"), .Select("low")) register_8 (
    .D(PCaddr), .en(demultiplexer_3_out3), .Q(register_8_q), .clk(CLK));  // open: clr
  Multiplexer #(.select(2), .width(32), .disabled("Z"), .enable("false")) multiplexer_16 (
    .in1(register_6_q), .in2(register_7_q), .in3(register_8_q), .out(EPC), .sel(interrID));  // open: in0

  // Other names for the same wires on the sheet: R2[31:0] = MDin

  // Notes on the sheet:
  //   中断源
  //   中断等待指示
  //   总复位信号应将除ROM以外所有存储组件全部清零
  //   多级中断测试信号模拟器
  //   数码管输出
  //   数码管输出应该用寄存器锁存，否则显示数据只能一闪而过
  //   指令探针
  //   指令存储器
  //   指令字
  //   contents of rom_1 (hex, n*v repeats v):
  //   100493 100006f 100493 200913 300993 100006f 100493 200913 300993 100006f 100493 200913 300993
  //   100006f 100493 200913 300993 40c000ef 100413 100493 1f49493 900533 2200893 73 24d493 48463 fedff06f
  //   900533 2200893 73 100493 249493 900533 2200893 73 48463 fedff06f 100493 1f49493 900533 2200893 73
  //   4034d493 900533 2200893 73 4044d493 900533 2200893 73 4044d493 900533 2200893 73 4044d493 900533
  //   2200893 73 4044d493 900533 2200893 73 4044d493 900533 2200893 73 4044d493 900533 2200893 73 4044d493
  //   900533 2200893 73 100413 1f41993 41f9d993 433 c00913 300b13 140413 f47413 800293 100313 499993
  //   89e9b3 1300533 2200893 73 406282b3 fe0294e3 140413 f00f93 1f47433 1c41413 800293 100313 49d993
  //   89e9b3 1300533 2200893 73 406282b3 fe0294e3 1c45413 406b0b33 b0463 f95ff06f 2b3 fff2c293 829293
  //   ff2e293 500533 2200893 73 fff00413 493 84a023 140413 448493 84a023 140413 448493 84a023 140413
  //   448493 84a023 140413 448493 84a023 140413 448493 84a023 140413 448493 84a023 140413 448493 84a023
  //   140413 448493 84a023 140413 448493 84a023 140413 448493 84a023 140413 448493 84a023 140413 448493
  //   84a023 140413 448493 84a023 140413 448493 84a023 140413 448493 84a023 140413 448493 140413 433
  //   3c00493 42983 4aa03 149a2b3 28663 134a023 1442023 ffc48493 fe9412e3 800533 2200893 73 440413 3c00493
  //   fc9416e3 a00893 73 fff00293 7700493 849493 7748493 900533 2200893 73 1000e13 54c4b3 900533 2200893
  //   73 fffe0e13 fe0e16e3 a00893 73 13 430497 900533 2200893 73 430497 900533 2200893 73 430497 900533
  //   2200893 73 430497 900533 2200893 73 430497 900533 2200893 73 430497 900533 2200893 73 430497 900533
  //   2200893 73 430497 900533 2200893 73 a00893 73 313 1000e13 13 8400493 849493 8348493 400913 891913
  //   490913 849493 8248493 849493 8148493 891913 490913 891913 490913 932023 12484b3 430313 fffe0e13
  //   fe0e18e3 2000e13 313 30483 900533 2200893 73 130313 fffe0e13 fe0e14e3 a00893 73 f00493 900533
  //   2200893 73 fff48493 fe04d8e3 a00893 73 413 140413 800533 2200893 73 240413 800533 2200893 73 340413
  //   800533 2200893 73 440413 800533 2200893 73 540413 800533 2200893 73 640413 800533 2200893 73 740413
  //   800533 2200893 73 840413 800533 2200893 2200893 73 8067
  //   JAL
  //   JALR
  //   URET
  //   Bne
  //   MemToReg
  //   MemWrite
  //   AluOP
  //   AluSrcB
  //   RegWrite
  //   为方便自动评测，需要输出PC，IR，寄存器堆写如数据RDin
  //   RAM写使能MemWrite、RAM写入数据MDin等信号
  //   控制位
  //   暂停节拍，不能为0
  //   数据存储器
  //   戳工具置1进入计数暂停模式，ctrl+k时钟自动运行到对应节拍暂停
  //   ctrl+k关闭时钟连续运行，将控制位置零，进入单步调试模式调试
  //   可计数暂停的时钟源
endmodule

module \封装正确性测试  (
);

  wire IR1, IR2, IR3, MemW, RegW;
  wire [31:0] EX_PC, ID_PC, IF_PC, IR, LED, MDin, MDinr, MEM_PC, PC, RDin, RDinr, WB_PC;

  \单周期RISC_V  \u_单周期risc_v_1  (
    .IR1(IR1), .IR2(IR2), .IR3(IR3), .RegWrite(RegW), .MemWrite(MemW), .PC(PC), .IR(IR), .RDin(RDin),
    .MDin(MDin), .LedData(LED));  // open: out_11
  \气泡流水线  \u_气泡流水线_1  (
    .RegWrite(RegW), .MemWrite(MemW), .IF_PC(IF_PC), .ID_PC(ID_PC), .EX_PC(EX_PC), .M_PC(MEM_PC),
    .WB_PC(WB_PC), .RDin(RDinr), .MDin(MDinr), .LedData(LED));
  \单周期_单级中断  \u_单周期_单级中断_1  (
    .IR1(IR1), .IR2(IR2), .IR3(IR3), .RegWrite(RegW), .MemWrite(MemW), .PC(PC), .IR(IR), .RDin(RDin),
    .MDin(MDin), .LedData(LED));  // open: out_11
  \理想流水线  \u_理想流水线_1  (
    .RegWrite(RegW), .MemWrite(MemW), .IF_PC(IF_PC), .ID_PC(ID_PC), .EX_PC(EX_PC), .M_PC(MEM_PC),
    .WB_PC(WB_PC), .RDin(RDinr), .MDin(MDinr), .LedData(LED));
  \重定向流水线  \u_重定向流水线_1  (
    .RegWrite(RegW), .MemWrite(MemW), .IF_PC(IF_PC), .ID_PC(ID_PC), .EX_PC(EX_PC), .M_PC(MEM_PC),
    .WB_PC(WB_PC), .RDin(RDinr), .MDin(MDinr), .LedData(LED));
  \单周期_多级中断  \u_单周期_多级中断_1  (
    .IR1(IR1), .IR2(IR2), .IR3(IR3), .RegWrite(RegW), .MemWrite(MemW), .PC(PC), .IR(IR), .RDin(RDin),
    .MDin(MDin), .LedData(LED));

  // Notes on the sheet:
  //   单周期封装测试
  //   气泡流水封装测试
  //   单周期+单级中断封装测试
  //   请检查上面封装有无位宽不匹配，引脚标签是否和连接的标签相对应，否则无法在educoder平台上正确测试
  //   理想流水封装测试
  //   重定向流水封装测试
  //   单周期+多级中断封装测试
endmodule

module IF_ID (
  input  [31:0] PCin,
  input  [31:0] nextPCin,
  input  [31:0] IRin,
  input  EN,
  input  CLK,
  input  RESET,
  output [31:0] PCout,
  output [31:0] nextPCout,
  output [31:0] IRout
);

  wire [31:0] multiplexer_1_out, multiplexer_2_out, multiplexer_3_out;

  Multiplexer #(.select(1), .width(32), .disabled("Z"), .enable("false")) multiplexer_1 (
    .in0(PCin), .in1({32{1'b0}}), .out(multiplexer_1_out), .sel(RESET));
  Multiplexer #(.select(1), .width(32), .disabled("Z"), .enable("false")) multiplexer_2 (
    .in0(nextPCin), .in1({32{1'b0}}), .out(multiplexer_2_out), .sel(RESET));
  Multiplexer #(.select(1), .width(32), .disabled("Z"), .enable("false")) multiplexer_3 (
    .in0(IRin), .in1({32{1'b0}}), .out(multiplexer_3_out), .sel(RESET));
  Register #(.width(32), .trigger("rising"), .Select("low")) register_1 (
    .D(multiplexer_1_out), .en(EN), .Q(PCout), .clk(CLK));  // open: clr
  Register #(.width(32), .trigger("rising"), .Select("low")) register_2 (
    .D(multiplexer_2_out), .en(EN), .Q(nextPCout), .clk(CLK));  // open: clr
  Register #(.width(32), .trigger("rising"), .Select("low")) register_3 (
    .D(multiplexer_3_out), .en(EN), .Q(IRout), .clk(CLK));  // open: clr
endmodule

module ID_EX (
  input  RegWritein,
  input  MemToRegin,
  input  MemWritein,
  input  [3:0] ALUOPin,
  input  ALUSrcin,
  input  ecallin,
  input  S_typein,
  input  BEQin,
  input  BNEin,
  input  JALin,
  input  JALRin,
  input  AUIPCin,
  input  LBin,
  input  BGEin,
  input  [31:0] R1in,
  input  [31:0] R2in,
  input  [4:0] W_in,
  input  [31:0] immin,
  input  [31:0] BEaddrin,
  input  [31:0] PCin,
  input  [31:0] nextPCin,
  input  [31:0] JALaddrin,
  input  [31:0] IRin,
  input  [1:0] RS_Fin,
  input  [1:0] RT_Fin,
  input  [31:0] AUIPCresin,
  input  RESET,
  input  EN,
  input  CLK,
  output RegWriteout,
  output MemToRegout,
  output MemWriteout,
  output [3:0] ALUOPout,
  output ALUSrcout,
  output ecallout,
  output S_typeout,
  output BEQout,
  output BNEout,
  output JALout,
  output JALRout,
  output AUIPCout,
  output LBout,
  output BGEout,
  output [31:0] R1out,
  output [31:0] R2out,
  output [4:0] W_out,
  output [31:0] immout,
  output [31:0] BEaddrout,
  output [31:0] PCout,
  output [31:0] nextPCout,
  output [31:0] JALaddrout,
  output [31:0] IRout,
  output [1:0] RS_Fout,
  output [1:0] RT_Fout,
  output [31:0] AUIPCresout
);

  wire multiplexer_1_out, multiplexer_2_out, multiplexer_3_out, multiplexer_5_out, multiplexer_6_out,
       multiplexer_7_out, multiplexer_8_out, multiplexer_9_out, multiplexer_10_out, multiplexer_11_out,
       multiplexer_12_out, multiplexer_13_out, multiplexer_14_out;
  wire [1:0] multiplexer_24_out, multiplexer_25_out;
  wire [3:0] multiplexer_4_out;
  wire [4:0] multiplexer_17_out;
  wire [31:0] multiplexer_15_out, multiplexer_16_out, multiplexer_18_out, multiplexer_19_out,
       multiplexer_20_out, multiplexer_21_out, multiplexer_22_out, multiplexer_23_out, multiplexer_26_out;

  Multiplexer #(.select(1), .width(1), .disabled("Z"), .enable("false")) multiplexer_1 (
    .in0(RegWritein), .in1(1'b0), .out(multiplexer_1_out), .sel(RESET));
  Multiplexer #(.select(1), .width(1), .disabled("Z"), .enable("false")) multiplexer_2 (
    .in0(MemToRegin), .in1(1'b0), .out(multiplexer_2_out), .sel(RESET));
  Multiplexer #(.select(1), .width(1), .disabled("Z"), .enable("false")) multiplexer_3 (
    .in0(MemWritein), .in1(1'b0), .out(multiplexer_3_out), .sel(RESET));
  Multiplexer #(.select(1), .width(4), .disabled("Z"), .enable("false")) multiplexer_4 (
    .in0(ALUOPin), .in1(4'b0000), .out(multiplexer_4_out), .sel(RESET));
  Multiplexer #(.select(1), .width(1), .disabled("Z"), .enable("false")) multiplexer_5 (
    .in0(ALUSrcin), .in1(1'b0), .out(multiplexer_5_out), .sel(RESET));
  Multiplexer #(.select(1), .width(1), .disabled("Z"), .enable("false")) multiplexer_6 (
    .in0(ecallin), .in1(1'b0), .out(multiplexer_6_out), .sel(RESET));
  Multiplexer #(.select(1), .width(1), .disabled("Z"), .enable("false")) multiplexer_7 (
    .in0(S_typein), .in1(1'b0), .out(multiplexer_7_out), .sel(RESET));
  Multiplexer #(.select(1), .width(1), .disabled("Z"), .enable("false")) multiplexer_8 (
    .in0(BEQin), .in1(1'b0), .out(multiplexer_8_out), .sel(RESET));
  Multiplexer #(.select(1), .width(1), .disabled("Z"), .enable("false")) multiplexer_9 (
    .in0(BNEin), .in1(1'b0), .out(multiplexer_9_out), .sel(RESET));
  Multiplexer #(.select(1), .width(1), .disabled("Z"), .enable("false")) multiplexer_10 (
    .in0(JALin), .in1(1'b0), .out(multiplexer_10_out), .sel(RESET));
  Multiplexer #(.select(1), .width(1), .disabled("Z"), .enable("false")) multiplexer_11 (
    .in0(JALRin), .in1(1'b0), .out(multiplexer_11_out), .sel(RESET));
  Multiplexer #(.select(1), .width(1), .disabled("Z"), .enable("false")) multiplexer_12 (
    .in0(AUIPCin), .in1(1'b0), .out(multiplexer_12_out), .sel(RESET));
  Multiplexer #(.select(1), .width(1), .disabled("Z"), .enable("false")) multiplexer_13 (
    .in0(LBin), .in1(1'b0), .out(multiplexer_13_out), .sel(RESET));
  Multiplexer #(.select(1), .width(1), .disabled("Z"), .enable("false")) multiplexer_14 (
    .in0(BGEin), .in1(1'b0), .out(multiplexer_14_out), .sel(RESET));
  Multiplexer #(.select(1), .width(32), .disabled("Z"), .enable("false")) multiplexer_15 (
    .in0(R1in), .in1({32{1'b0}}), .out(multiplexer_15_out), .sel(RESET));
  Multiplexer #(.select(1), .width(32), .disabled("Z"), .enable("false")) multiplexer_16 (
    .in0(R2in), .in1({32{1'b0}}), .out(multiplexer_16_out), .sel(RESET));
  Multiplexer #(.select(1), .width(5), .disabled("Z"), .enable("false")) multiplexer_17 (
    .in0(W_in), .in1({5{1'b0}}), .out(multiplexer_17_out), .sel(RESET));
  Multiplexer #(.select(1), .width(32), .disabled("Z"), .enable("false")) multiplexer_18 (
    .in0(immin), .in1({32{1'b0}}), .out(multiplexer_18_out), .sel(RESET));
  Multiplexer #(.select(1), .width(32), .disabled("Z"), .enable("false")) multiplexer_19 (
    .in0(BEaddrin), .in1({32{1'b0}}), .out(multiplexer_19_out), .sel(RESET));
  Multiplexer #(.select(1), .width(32), .disabled("Z"), .enable("false")) multiplexer_20 (
    .in0(PCin), .in1({32{1'b0}}), .out(multiplexer_20_out), .sel(RESET));
  Multiplexer #(.select(1), .width(32), .disabled("Z"), .enable("false")) multiplexer_21 (
    .in0(nextPCin), .in1({32{1'b0}}), .out(multiplexer_21_out), .sel(RESET));
  Multiplexer #(.select(1), .width(32), .disabled("Z"), .enable("false")) multiplexer_22 (
    .in0(JALaddrin), .in1({32{1'b0}}), .out(multiplexer_22_out), .sel(RESET));
  Multiplexer #(.select(1), .width(32), .disabled("Z"), .enable("false")) multiplexer_23 (
    .in0(IRin), .in1({32{1'b0}}), .out(multiplexer_23_out), .sel(RESET));
  Multiplexer #(.select(1), .width(2), .disabled("Z"), .enable("false")) multiplexer_24 (
    .in0(RS_Fin), .in1(2'b00), .out(multiplexer_24_out), .sel(RESET));
  Multiplexer #(.select(1), .width(2), .disabled("Z"), .enable("false")) multiplexer_25 (
    .in0(RT_Fin), .in1(2'b00), .out(multiplexer_25_out), .sel(RESET));
  Multiplexer #(.select(1), .width(32), .disabled("Z"), .enable("false")) multiplexer_26 (
    .in0(AUIPCresin), .in1({32{1'b0}}), .out(multiplexer_26_out), .sel(RESET));
  Register #(.width(1), .trigger("rising"), .Select("low")) register_1 (
    .D(multiplexer_1_out), .en(EN), .Q(RegWriteout), .clk(CLK));  // open: clr
  Register #(.width(1), .trigger("rising"), .Select("low")) register_2 (
    .D(multiplexer_2_out), .en(EN), .Q(MemToRegout), .clk(CLK));  // open: clr
  Register #(.width(1), .trigger("rising"), .Select("low")) register_3 (
    .D(multiplexer_3_out), .en(EN), .Q(MemWriteout), .clk(CLK));  // open: clr
  Register #(.width(4), .trigger("rising"), .Select("low")) register_4 (
    .D(multiplexer_4_out), .en(EN), .Q(ALUOPout), .clk(CLK));  // open: clr
  Register #(.width(1), .trigger("rising"), .Select("low")) register_5 (
    .D(multiplexer_5_out), .en(EN), .Q(ALUSrcout), .clk(CLK));  // open: clr
  Register #(.width(1), .trigger("rising"), .Select("low")) register_6 (
    .D(multiplexer_6_out), .en(EN), .Q(ecallout), .clk(CLK));  // open: clr
  Register #(.width(1), .trigger("rising"), .Select("low")) register_7 (
    .D(multiplexer_7_out), .en(EN), .Q(S_typeout), .clk(CLK));  // open: clr
  Register #(.width(1), .trigger("rising"), .Select("low")) register_8 (
    .D(multiplexer_8_out), .en(EN), .Q(BEQout), .clk(CLK));  // open: clr
  Register #(.width(1), .trigger("rising"), .Select("low")) register_9 (
    .D(multiplexer_9_out), .en(EN), .Q(BNEout), .clk(CLK));  // open: clr
  Register #(.width(1), .trigger("rising"), .Select("low")) register_10 (
    .D(multiplexer_10_out), .en(EN), .Q(JALout), .clk(CLK));  // open: clr
  Register #(.width(1), .trigger("rising"), .Select("low")) register_11 (
    .D(multiplexer_11_out), .en(EN), .Q(JALRout), .clk(CLK));  // open: clr
  Register #(.width(1), .trigger("rising"), .Select("low")) register_12 (
    .D(multiplexer_12_out), .en(EN), .Q(AUIPCout), .clk(CLK));  // open: clr
  Register #(.width(1), .trigger("rising"), .Select("low")) register_13 (
    .D(multiplexer_13_out), .en(EN), .Q(LBout), .clk(CLK));  // open: clr
  Register #(.width(1), .trigger("rising"), .Select("low")) register_14 (
    .D(multiplexer_14_out), .en(EN), .Q(BGEout), .clk(CLK));  // open: clr
  Register #(.width(32), .trigger("rising"), .Select("low")) register_15 (
    .D(multiplexer_15_out), .en(EN), .Q(R1out), .clk(CLK));  // open: clr
  Register #(.width(32), .trigger("rising"), .Select("low")) register_16 (
    .D(multiplexer_16_out), .en(EN), .Q(R2out), .clk(CLK));  // open: clr
  Register #(.width(5), .trigger("rising"), .Select("low")) register_17 (
    .D(multiplexer_17_out), .en(EN), .Q(W_out), .clk(CLK));  // open: clr
  Register #(.width(32), .trigger("rising"), .Select("low")) register_18 (
    .D(multiplexer_18_out), .en(EN), .Q(immout), .clk(CLK));  // open: clr
  Register #(.width(32), .trigger("rising"), .Select("low")) register_19 (
    .D(multiplexer_19_out), .en(EN), .Q(BEaddrout), .clk(CLK));  // open: clr
  Register #(.width(32), .trigger("rising"), .Select("low")) register_20 (
    .D(multiplexer_20_out), .en(EN), .Q(PCout), .clk(CLK));  // open: clr
  Register #(.width(32), .trigger("rising"), .Select("low")) register_21 (
    .D(multiplexer_21_out), .en(EN), .Q(nextPCout), .clk(CLK));  // open: clr
  Register #(.width(32), .trigger("rising"), .Select("low")) register_22 (
    .D(multiplexer_22_out), .en(EN), .Q(JALaddrout), .clk(CLK));  // open: clr
  Register #(.width(32), .trigger("rising"), .Select("low")) register_23 (
    .D(multiplexer_23_out), .en(EN), .Q(IRout), .clk(CLK));  // open: clr
  Register #(.width(2), .trigger("rising"), .Select("low")) register_24 (
    .D(multiplexer_24_out), .en(EN), .Q(RS_Fout), .clk(CLK));  // open: clr
  Register #(.width(2), .trigger("rising"), .Select("low")) register_25 (
    .D(multiplexer_25_out), .en(EN), .Q(RT_Fout), .clk(CLK));  // open: clr
  Register #(.width(32), .trigger("rising"), .Select("low")) register_26 (
    .D(multiplexer_26_out), .en(EN), .Q(AUIPCresout), .clk(CLK));  // open: clr
endmodule

module EX_MEM (
  input  RegWritein,
  input  MemToRegin,
  input  MemWritein,
  input  [3:0] ALUOPin,
  input  ALUSrcin,
  input  ecallin,
  input  S_typein,
  input  BEQin,
  input  BNEin,
  input  JALin,
  input  JALRin,
  input  AUIPCin,
  input  LBin,
  input  BGEin,
  input  [31:0] R1in,
  input  [31:0] R2in,
  input  [4:0] W_in,
  input  [31:0] immin,
  input  [31:0] BEaddrin,
  input  [31:0] PCin,
  input  [31:0] nextPCin,
  input  [31:0] JALaddrin,
  input  [31:0] IRin,
  input  BEin,
  input  [31:0] ALUResultin,
  input  RESET,
  input  EN,
  input  CLK,
  output RegWriteout,
  output MemToRegout,
  output MemWriteout,
  output [3:0] ALUOPout,
  output ALUSrcout,
  output ecallout,
  output S_typeout,
  output BEQout,
  output BNEout,
  output JALout,
  output JALRout,
  output AUIPCout,
  output LBout,
  output BGEout,
  output [31:0] R1out,
  output [31:0] R2out,
  output [4:0] W_out,
  output [31:0] immout,
  output [31:0] BEaddrout,
  output [31:0] PCout,
  output [31:0] nextPCout,
  output [31:0] JALaddrout,
  output [31:0] IRout,
  output BEout,
  output [31:0] ALUResultout
);

  wire multiplexer_1_out, multiplexer_2_out, multiplexer_3_out, multiplexer_5_out, multiplexer_6_out,
       multiplexer_7_out, multiplexer_8_out, multiplexer_9_out, multiplexer_10_out, multiplexer_11_out,
       multiplexer_12_out, multiplexer_13_out, multiplexer_14_out, multiplexer_24_out;
  wire [3:0] multiplexer_4_out;
  wire [4:0] multiplexer_17_out;
  wire [31:0] multiplexer_15_out, multiplexer_16_out, multiplexer_18_out, multiplexer_19_out,
       multiplexer_20_out, multiplexer_21_out, multiplexer_22_out, multiplexer_23_out, multiplexer_25_out;

  Multiplexer #(.select(1), .width(1), .disabled("Z"), .enable("false")) multiplexer_1 (
    .in0(RegWritein), .in1(1'b0), .out(multiplexer_1_out), .sel(RESET));
  Multiplexer #(.select(1), .width(1), .disabled("Z"), .enable("false")) multiplexer_2 (
    .in0(MemToRegin), .in1(1'b0), .out(multiplexer_2_out), .sel(RESET));
  Multiplexer #(.select(1), .width(1), .disabled("Z"), .enable("false")) multiplexer_3 (
    .in0(MemWritein), .in1(1'b0), .out(multiplexer_3_out), .sel(RESET));
  Multiplexer #(.select(1), .width(4), .disabled("Z"), .enable("false")) multiplexer_4 (
    .in0(ALUOPin), .in1(4'b0000), .out(multiplexer_4_out), .sel(RESET));
  Multiplexer #(.select(1), .width(1), .disabled("Z"), .enable("false")) multiplexer_5 (
    .in0(ALUSrcin), .in1(1'b0), .out(multiplexer_5_out), .sel(RESET));
  Multiplexer #(.select(1), .width(1), .disabled("Z"), .enable("false")) multiplexer_6 (
    .in0(ecallin), .in1(1'b0), .out(multiplexer_6_out), .sel(RESET));
  Multiplexer #(.select(1), .width(1), .disabled("Z"), .enable("false")) multiplexer_7 (
    .in0(S_typein), .in1(1'b0), .out(multiplexer_7_out), .sel(RESET));
  Multiplexer #(.select(1), .width(1), .disabled("Z"), .enable("false")) multiplexer_8 (
    .in0(BEQin), .in1(1'b0), .out(multiplexer_8_out), .sel(RESET));
  Multiplexer #(.select(1), .width(1), .disabled("Z"), .enable("false")) multiplexer_9 (
    .in0(BNEin), .in1(1'b0), .out(multiplexer_9_out), .sel(RESET));
  Multiplexer #(.select(1), .width(1), .disabled("Z"), .enable("false")) multiplexer_10 (
    .in0(JALin), .in1(1'b0), .out(multiplexer_10_out), .sel(RESET));
  Multiplexer #(.select(1), .width(1), .disabled("Z"), .enable("false")) multiplexer_11 (
    .in0(JALRin), .in1(1'b0), .out(multiplexer_11_out), .sel(RESET));
  Multiplexer #(.select(1), .width(1), .disabled("Z"), .enable("false")) multiplexer_12 (
    .in0(AUIPCin), .in1(1'b0), .out(multiplexer_12_out), .sel(RESET));
  Multiplexer #(.select(1), .width(1), .disabled("Z"), .enable("false")) multiplexer_13 (
    .in0(LBin), .in1(1'b0), .out(multiplexer_13_out), .sel(RESET));
  Multiplexer #(.select(1), .width(1), .disabled("Z"), .enable("false")) multiplexer_14 (
    .in0(BGEin), .in1(1'b0), .out(multiplexer_14_out), .sel(RESET));
  Multiplexer #(.select(1), .width(32), .disabled("Z"), .enable("false")) multiplexer_15 (
    .in0(R1in), .in1({32{1'b0}}), .out(multiplexer_15_out), .sel(RESET));
  Multiplexer #(.select(1), .width(32), .disabled("Z"), .enable("false")) multiplexer_16 (
    .in0(R2in), .in1({32{1'b0}}), .out(multiplexer_16_out), .sel(RESET));
  Multiplexer #(.select(1), .width(5), .disabled("Z"), .enable("false")) multiplexer_17 (
    .in0(W_in), .in1({5{1'b0}}), .out(multiplexer_17_out), .sel(RESET));
  Multiplexer #(.select(1), .width(32), .disabled("Z"), .enable("false")) multiplexer_18 (
    .in0(immin), .in1({32{1'b0}}), .out(multiplexer_18_out), .sel(RESET));
  Multiplexer #(.select(1), .width(32), .disabled("Z"), .enable("false")) multiplexer_19 (
    .in0(BEaddrin), .in1({32{1'b0}}), .out(multiplexer_19_out), .sel(RESET));
  Multiplexer #(.select(1), .width(32), .disabled("Z"), .enable("false")) multiplexer_20 (
    .in0(PCin), .in1({32{1'b0}}), .out(multiplexer_20_out), .sel(RESET));
  Multiplexer #(.select(1), .width(32), .disabled("Z"), .enable("false")) multiplexer_21 (
    .in0(nextPCin), .in1({32{1'b0}}), .out(multiplexer_21_out), .sel(RESET));
  Multiplexer #(.select(1), .width(32), .disabled("Z"), .enable("false")) multiplexer_22 (
    .in0(JALaddrin), .in1({32{1'b0}}), .out(multiplexer_22_out), .sel(RESET));
  Multiplexer #(.select(1), .width(32), .disabled("Z"), .enable("false")) multiplexer_23 (
    .in0(IRin), .in1({32{1'b0}}), .out(multiplexer_23_out), .sel(RESET));
  Multiplexer #(.select(1), .width(1), .disabled("Z"), .enable("false")) multiplexer_24 (
    .in0(BEin), .in1(1'b0), .out(multiplexer_24_out), .sel(RESET));
  Multiplexer #(.select(1), .width(32), .disabled("Z"), .enable("false")) multiplexer_25 (
    .in0(ALUResultin), .in1({32{1'b0}}), .out(multiplexer_25_out), .sel(RESET));
  Register #(.width(1), .trigger("rising"), .Select("low")) register_1 (
    .D(multiplexer_1_out), .en(EN), .Q(RegWriteout), .clk(CLK));  // open: clr
  Register #(.width(1), .trigger("rising"), .Select("low")) register_2 (
    .D(multiplexer_2_out), .en(EN), .Q(MemToRegout), .clk(CLK));  // open: clr
  Register #(.width(1), .trigger("rising"), .Select("low")) register_3 (
    .D(multiplexer_3_out), .en(EN), .Q(MemWriteout), .clk(CLK));  // open: clr
  Register #(.width(4), .trigger("rising"), .Select("low")) register_4 (
    .D(multiplexer_4_out), .en(EN), .Q(ALUOPout), .clk(CLK));  // open: clr
  Register #(.width(1), .trigger("rising"), .Select("low")) register_5 (
    .D(multiplexer_5_out), .en(EN), .Q(ALUSrcout), .clk(CLK));  // open: clr
  Register #(.width(1), .trigger("rising"), .Select("low")) register_6 (
    .D(multiplexer_6_out), .en(EN), .Q(ecallout), .clk(CLK));  // open: clr
  Register #(.width(1), .trigger("rising"), .Select("low")) register_7 (
    .D(multiplexer_7_out), .en(EN), .Q(S_typeout), .clk(CLK));  // open: clr
  Register #(.width(1), .trigger("rising"), .Select("low")) register_8 (
    .D(multiplexer_8_out), .en(EN), .Q(BEQout), .clk(CLK));  // open: clr
  Register #(.width(1), .trigger("rising"), .Select("low")) register_9 (
    .D(multiplexer_9_out), .en(EN), .Q(BNEout), .clk(CLK));  // open: clr
  Register #(.width(1), .trigger("rising"), .Select("low")) register_10 (
    .D(multiplexer_10_out), .en(EN), .Q(JALout), .clk(CLK));  // open: clr
  Register #(.width(1), .trigger("rising"), .Select("low")) register_11 (
    .D(multiplexer_11_out), .en(EN), .Q(JALRout), .clk(CLK));  // open: clr
  Register #(.width(1), .trigger("rising"), .Select("low")) register_12 (
    .D(multiplexer_12_out), .en(EN), .Q(AUIPCout), .clk(CLK));  // open: clr
  Register #(.width(1), .trigger("rising"), .Select("low")) register_13 (
    .D(multiplexer_13_out), .en(EN), .Q(LBout), .clk(CLK));  // open: clr
  Register #(.width(1), .trigger("rising"), .Select("low")) register_14 (
    .D(multiplexer_14_out), .en(EN), .Q(BGEout), .clk(CLK));  // open: clr
  Register #(.width(32), .trigger("rising"), .Select("low")) register_15 (
    .D(multiplexer_15_out), .en(EN), .Q(R1out), .clk(CLK));  // open: clr
  Register #(.width(32), .trigger("rising"), .Select("low")) register_16 (
    .D(multiplexer_16_out), .en(EN), .Q(R2out), .clk(CLK));  // open: clr
  Register #(.width(5), .trigger("rising"), .Select("low")) register_17 (
    .D(multiplexer_17_out), .en(EN), .Q(W_out), .clk(CLK));  // open: clr
  Register #(.width(32), .trigger("rising"), .Select("low")) register_18 (
    .D(multiplexer_18_out), .en(EN), .Q(immout), .clk(CLK));  // open: clr
  Register #(.width(32), .trigger("rising"), .Select("low")) register_19 (
    .D(multiplexer_19_out), .en(EN), .Q(BEaddrout), .clk(CLK));  // open: clr
  Register #(.width(32), .trigger("rising"), .Select("low")) register_20 (
    .D(multiplexer_20_out), .en(EN), .Q(PCout), .clk(CLK));  // open: clr
  Register #(.width(32), .trigger("rising"), .Select("low")) register_21 (
    .D(multiplexer_21_out), .en(EN), .Q(nextPCout), .clk(CLK));  // open: clr
  Register #(.width(32), .trigger("rising"), .Select("low")) register_22 (
    .D(multiplexer_22_out), .en(EN), .Q(JALaddrout), .clk(CLK));  // open: clr
  Register #(.width(32), .trigger("rising"), .Select("low")) register_23 (
    .D(multiplexer_23_out), .en(EN), .Q(IRout), .clk(CLK));  // open: clr
  Register #(.width(1), .trigger("rising"), .Select("low")) register_24 (
    .D(multiplexer_24_out), .en(EN), .Q(BEout), .clk(CLK));  // open: clr
  Register #(.width(32), .trigger("rising"), .Select("low")) register_25 (
    .D(multiplexer_25_out), .en(EN), .Q(ALUResultout), .clk(CLK));  // open: clr
endmodule

module MEM_WB (
  input  RegWritein,
  input  MemToRegin,
  input  MemWritein,
  input  [3:0] ALUOPin,
  input  ALUSrcin,
  input  ecallin,
  input  S_typein,
  input  BEQin,
  input  BNEin,
  input  JALin,
  input  JALRin,
  input  AUIPCin,
  input  LBin,
  input  BGEin,
  input  [31:0] Memin,
  input  [4:0] W_in,
  input  [31:0] immin,
  input  [31:0] BEaddrin,
  input  [31:0] PCin,
  input  [31:0] nextPCin,
  input  [31:0] JALaddrin,
  input  [31:0] IRin,
  input  BEin,
  input  [31:0] ALUResultin,
  input  [31:0] R1in,
  input  [31:0] R2in,
  input  RESET,
  input  EN,
  input  CLK,
  output RegWriteout,
  output MemToRegout,
  output MemWriteout,
  output [3:0] ALUOPout,
  output ALUSrcout,
  output ecallout,
  output S_typeout,
  output BEQout,
  output BNEout,
  output JALout,
  output JALRout,
  output AUIPCout,
  output LBout,
  output BGEout,
  output [31:0] Memout,
  output [4:0] W_out,
  output [31:0] immout,
  output [31:0] BEaddrout,
  output [31:0] PCout,
  output [31:0] nextPCout,
  output [31:0] JALaddrout,
  output [31:0] IRout,
  output BEout,
  output [31:0] ALUResultout,
  output [31:0] R1out,
  output [31:0] R2out
);

  wire multiplexer_1_out, multiplexer_2_out, multiplexer_3_out, multiplexer_5_out, multiplexer_6_out,
       multiplexer_7_out, multiplexer_8_out, multiplexer_9_out, multiplexer_10_out, multiplexer_11_out,
       multiplexer_12_out, multiplexer_13_out, multiplexer_14_out, multiplexer_23_out;
  wire [3:0] multiplexer_4_out;
  wire [4:0] multiplexer_16_out;
  wire [31:0] multiplexer_15_out, multiplexer_17_out, multiplexer_18_out, multiplexer_19_out,
       multiplexer_20_out, multiplexer_21_out, multiplexer_22_out, multiplexer_24_out, multiplexer_25_out,
       multiplexer_26_out;

  Multiplexer #(.select(1), .width(1), .disabled("Z"), .enable("false")) multiplexer_1 (
    .in0(RegWritein), .in1(1'b0), .out(multiplexer_1_out), .sel(RESET));
  Multiplexer #(.select(1), .width(1), .disabled("Z"), .enable("false")) multiplexer_2 (
    .in0(MemToRegin), .in1(1'b0), .out(multiplexer_2_out), .sel(RESET));
  Multiplexer #(.select(1), .width(1), .disabled("Z"), .enable("false")) multiplexer_3 (
    .in0(MemWritein), .in1(1'b0), .out(multiplexer_3_out), .sel(RESET));
  Multiplexer #(.select(1), .width(4), .disabled("Z"), .enable("false")) multiplexer_4 (
    .in0(ALUOPin), .in1(4'b0000), .out(multiplexer_4_out), .sel(RESET));
  Multiplexer #(.select(1), .width(1), .disabled("Z"), .enable("false")) multiplexer_5 (
    .in0(ALUSrcin), .in1(1'b0), .out(multiplexer_5_out), .sel(RESET));
  Multiplexer #(.select(1), .width(1), .disabled("Z"), .enable("false")) multiplexer_6 (
    .in0(ecallin), .in1(1'b0), .out(multiplexer_6_out), .sel(RESET));
  Multiplexer #(.select(1), .width(1), .disabled("Z"), .enable("false")) multiplexer_7 (
    .in0(S_typein), .in1(1'b0), .out(multiplexer_7_out), .sel(RESET));
  Multiplexer #(.select(1), .width(1), .disabled("Z"), .enable("false")) multiplexer_8 (
    .in0(BEQin), .in1(1'b0), .out(multiplexer_8_out), .sel(RESET));
  Multiplexer #(.select(1), .width(1), .disabled("Z"), .enable("false")) multiplexer_9 (
    .in0(BNEin), .in1(1'b0), .out(multiplexer_9_out), .sel(RESET));
  Multiplexer #(.select(1), .width(1), .disabled("Z"), .enable("false")) multiplexer_10 (
    .in0(JALin), .in1(1'b0), .out(multiplexer_10_out), .sel(RESET));
  Multiplexer #(.select(1), .width(1), .disabled("Z"), .enable("false")) multiplexer_11 (
    .in0(JALRin), .in1(1'b0), .out(multiplexer_11_out), .sel(RESET));
  Multiplexer #(.select(1), .width(1), .disabled("Z"), .enable("false")) multiplexer_12 (
    .in0(AUIPCin), .in1(1'b0), .out(multiplexer_12_out), .sel(RESET));
  Multiplexer #(.select(1), .width(1), .disabled("Z"), .enable("false")) multiplexer_13 (
    .in0(LBin), .in1(1'b0), .out(multiplexer_13_out), .sel(RESET));
  Multiplexer #(.select(1), .width(1), .disabled("Z"), .enable("false")) multiplexer_14 (
    .in0(BGEin), .in1(1'b0), .out(multiplexer_14_out), .sel(RESET));
  Multiplexer #(.select(1), .width(32), .disabled("Z"), .enable("false")) multiplexer_15 (
    .in0(Memin), .in1({32{1'b0}}), .out(multiplexer_15_out), .sel(RESET));
  Multiplexer #(.select(1), .width(5), .disabled("Z"), .enable("false")) multiplexer_16 (
    .in0(W_in), .in1({5{1'b0}}), .out(multiplexer_16_out), .sel(RESET));
  Multiplexer #(.select(1), .width(32), .disabled("Z"), .enable("false")) multiplexer_17 (
    .in0(immin), .in1({32{1'b0}}), .out(multiplexer_17_out), .sel(RESET));
  Multiplexer #(.select(1), .width(32), .disabled("Z"), .enable("false")) multiplexer_18 (
    .in0(BEaddrin), .in1({32{1'b0}}), .out(multiplexer_18_out), .sel(RESET));
  Multiplexer #(.select(1), .width(32), .disabled("Z"), .enable("false")) multiplexer_19 (
    .in0(PCin), .in1({32{1'b0}}), .out(multiplexer_19_out), .sel(RESET));
  Multiplexer #(.select(1), .width(32), .disabled("Z"), .enable("false")) multiplexer_20 (
    .in0(nextPCin), .in1({32{1'b0}}), .out(multiplexer_20_out), .sel(RESET));
  Multiplexer #(.select(1), .width(32), .disabled("Z"), .enable("false")) multiplexer_21 (
    .in0(JALaddrin), .in1({32{1'b0}}), .out(multiplexer_21_out), .sel(RESET));
  Multiplexer #(.select(1), .width(32), .disabled("Z"), .enable("false")) multiplexer_22 (
    .in0(IRin), .in1({32{1'b0}}), .out(multiplexer_22_out), .sel(RESET));
  Multiplexer #(.select(1), .width(1), .disabled("Z"), .enable("false")) multiplexer_23 (
    .in0(BEin), .in1(1'b0), .out(multiplexer_23_out), .sel(RESET));
  Multiplexer #(.select(1), .width(32), .disabled("Z"), .enable("false")) multiplexer_24 (
    .in0(ALUResultin), .in1({32{1'b0}}), .out(multiplexer_24_out), .sel(RESET));
  Multiplexer #(.select(1), .width(32), .disabled("Z"), .enable("false")) multiplexer_25 (
    .in0(R1in), .in1({32{1'b0}}), .out(multiplexer_25_out), .sel(RESET));
  Multiplexer #(.select(1), .width(32), .disabled("Z"), .enable("false")) multiplexer_26 (
    .in0(R2in), .in1({32{1'b0}}), .out(multiplexer_26_out), .sel(RESET));
  Register #(.width(1), .trigger("rising"), .Select("low")) register_1 (
    .D(multiplexer_1_out), .en(EN), .Q(RegWriteout), .clk(CLK));  // open: clr
  Register #(.width(1), .trigger("rising"), .Select("low")) register_2 (
    .D(multiplexer_2_out), .en(EN), .Q(MemToRegout), .clk(CLK));  // open: clr
  Register #(.width(1), .trigger("rising"), .Select("low")) register_3 (
    .D(multiplexer_3_out), .en(EN), .Q(MemWriteout), .clk(CLK));  // open: clr
  Register #(.width(4), .trigger("rising"), .Select("low")) register_4 (
    .D(multiplexer_4_out), .en(EN), .Q(ALUOPout), .clk(CLK));  // open: clr
  Register #(.width(1), .trigger("rising"), .Select("low")) register_5 (
    .D(multiplexer_5_out), .en(EN), .Q(ALUSrcout), .clk(CLK));  // open: clr
  Register #(.width(1), .trigger("rising"), .Select("low")) register_6 (
    .D(multiplexer_6_out), .en(EN), .Q(ecallout), .clk(CLK));  // open: clr
  Register #(.width(1), .trigger("rising"), .Select("low")) register_7 (
    .D(multiplexer_7_out), .en(EN), .Q(S_typeout), .clk(CLK));  // open: clr
  Register #(.width(1), .trigger("rising"), .Select("low")) register_8 (
    .D(multiplexer_8_out), .en(EN), .Q(BEQout), .clk(CLK));  // open: clr
  Register #(.width(1), .trigger("rising"), .Select("low")) register_9 (
    .D(multiplexer_9_out), .en(EN), .Q(BNEout), .clk(CLK));  // open: clr
  Register #(.width(1), .trigger("rising"), .Select("low")) register_10 (
    .D(multiplexer_10_out), .en(EN), .Q(JALout), .clk(CLK));  // open: clr
  Register #(.width(1), .trigger("rising"), .Select("low")) register_11 (
    .D(multiplexer_11_out), .en(EN), .Q(JALRout), .clk(CLK));  // open: clr
  Register #(.width(1), .trigger("rising"), .Select("low")) register_12 (
    .D(multiplexer_12_out), .en(EN), .Q(AUIPCout), .clk(CLK));  // open: clr
  Register #(.width(1), .trigger("rising"), .Select("low")) register_13 (
    .D(multiplexer_13_out), .en(EN), .Q(LBout), .clk(CLK));  // open: clr
  Register #(.width(1), .trigger("rising"), .Select("low")) register_14 (
    .D(multiplexer_14_out), .en(EN), .Q(BGEout), .clk(CLK));  // open: clr
  Register #(.width(32), .trigger("rising"), .Select("low")) register_15 (
    .D(multiplexer_15_out), .en(EN), .Q(Memout), .clk(CLK));  // open: clr
  Register #(.width(5), .trigger("rising"), .Select("low")) register_16 (
    .D(multiplexer_16_out), .en(EN), .Q(W_out), .clk(CLK));  // open: clr
  Register #(.width(32), .trigger("rising"), .Select("low")) register_17 (
    .D(multiplexer_17_out), .en(EN), .Q(immout), .clk(CLK));  // open: clr
  Register #(.width(32), .trigger("rising"), .Select("low")) register_18 (
    .D(multiplexer_18_out), .en(EN), .Q(BEaddrout), .clk(CLK));  // open: clr
  Register #(.width(32), .trigger("rising"), .Select("low")) register_19 (
    .D(multiplexer_19_out), .en(EN), .Q(PCout), .clk(CLK));  // open: clr
  Register #(.width(32), .trigger("rising"), .Select("low")) register_20 (
    .D(multiplexer_20_out), .en(EN), .Q(nextPCout), .clk(CLK));  // open: clr
  Register #(.width(32), .trigger("rising"), .Select("low")) register_21 (
    .D(multiplexer_21_out), .en(EN), .Q(JALaddrout), .clk(CLK));  // open: clr
  Register #(.width(32), .trigger("rising"), .Select("low")) register_22 (
    .D(multiplexer_22_out), .en(EN), .Q(IRout), .clk(CLK));  // open: clr
  Register #(.width(1), .trigger("rising"), .Select("low")) register_23 (
    .D(multiplexer_23_out), .en(EN), .Q(BEout), .clk(CLK));  // open: clr
  Register #(.width(32), .trigger("rising"), .Select("low")) register_24 (
    .D(multiplexer_24_out), .en(EN), .Q(ALUResultout), .clk(CLK));  // open: clr
  Register #(.width(32), .trigger("rising"), .Select("low")) register_25 (
    .D(multiplexer_25_out), .en(EN), .Q(R1out), .clk(CLK));  // open: clr
  Register #(.width(32), .trigger("rising"), .Select("low")) register_26 (
    .D(multiplexer_26_out), .en(EN), .Q(R2out), .clk(CLK));  // open: clr
endmodule

module bubble_judge (
  input  RSin,
  input  RTin,
  input  [4:0] RSid,
  input  [4:0] RTid,
  input  EX_Regwrite,
  input  MEM_Regwrite,
  input  [4:0] EX_Wid,
  input  [4:0] MEM_Wid,
  output bubble
);

  wire and_1_out, and_2_out, and_3_out, and_4_out, comparator_1_eq, comparator_2_eq, comparator_3_eq,
       comparator_4_eq, comparator_5_eq, comparator_6_eq, comparator_7_eq, comparator_8_eq, not_1_out,
       not_2_out, not_3_out, not_4_out;

  Comparator #(.width(5), .mode("twosComplement")) comparator_1 (
    .a(RSid), .b({5{1'b0}}), .eq(comparator_1_eq));  // open: gt, lt
  Comparator #(.width(5), .mode("twosComplement")) comparator_2 (
    .a(RSid), .b(EX_Wid), .eq(comparator_2_eq));  // open: gt, lt
  Comparator #(.width(5), .mode("twosComplement")) comparator_3 (
    .a(RTid), .b({5{1'b0}}), .eq(comparator_3_eq));  // open: gt, lt
  Comparator #(.width(5), .mode("twosComplement")) comparator_4 (
    .a(RTid), .b(EX_Wid), .eq(comparator_4_eq));  // open: gt, lt
  Comparator #(.width(5), .mode("twosComplement")) comparator_5 (
    .a(RSid), .b({5{1'b0}}), .eq(comparator_5_eq));  // open: gt, lt
  Comparator #(.width(5), .mode("twosComplement")) comparator_6 (
    .a(RSid), .b(MEM_Wid), .eq(comparator_6_eq));  // open: gt, lt
  Comparator #(.width(5), .mode("twosComplement")) comparator_7 (
    .a(RTid), .b({5{1'b0}}), .eq(comparator_7_eq));  // open: gt, lt
  Comparator #(.width(5), .mode("twosComplement")) comparator_8 (
    .a(RTid), .b(MEM_Wid), .eq(comparator_8_eq));  // open: gt, lt
  not not_1 (not_1_out, comparator_1_eq);
  not not_2 (not_2_out, comparator_3_eq);
  not not_3 (not_3_out, comparator_5_eq);
  not not_4 (not_4_out, comparator_7_eq);
  and and_1 (and_1_out, RSin, not_1_out, EX_Regwrite, comparator_2_eq);
  and and_2 (and_2_out, RTin, not_2_out, EX_Regwrite, comparator_4_eq);
  and and_3 (and_3_out, RSin, not_3_out, MEM_Regwrite, comparator_6_eq);
  and and_4 (and_4_out, RTin, not_4_out, MEM_Regwrite, comparator_8_eq);
  or or_1 (bubble, and_1_out, and_2_out, and_3_out, and_4_out);

  // Other names for the same wires on the sheet: EX_Reg = EX_Regwrite; EX_W_num[4:0] = EX_Wid; MEM_Reg = MEM_Regwrite;
  //   MEM_W_num[4:0] = MEM_Wid; RS[4:0] = RSid; RSread = RSin; RT[4:0] = RTid; RTread = RTin
endmodule

module load_judge (
  input  RSin,
  input  RTin,
  input  [4:0] RSid,
  input  [4:0] RTid,
  input  EX_Regwrite,
  input  MEM_Regwrite,
  input  [4:0] EX_Wid,
  input  [4:0] MEM_Wid,
  input  EX_MemToReg,
  output [1:0] RS_F,
  output [1:0] RT_F,
  output load
);

  wire and_1_out, and_2_out, and_3_out, and_4_out, and_5_out, and_6_out, comparator_1_eq, comparator_2_eq,
       comparator_3_eq, comparator_4_eq, comparator_5_eq, comparator_6_eq, comparator_7_eq, comparator_8_eq,
       comparator_9_eq, comparator_10_eq, comparator_11_eq, comparator_12_eq, not_1_out, not_2_out,
       not_3_out, not_4_out, not_5_out, not_6_out;
  wire [1:0] multiplexer_1_out, multiplexer_2_out;

  Comparator #(.width(5), .mode("twosComplement")) comparator_1 (
    .a(RSid), .b({5{1'b0}}), .eq(comparator_1_eq));  // open: gt, lt
  Comparator #(.width(5), .mode("twosComplement")) comparator_2 (
    .a(RSid), .b(EX_Wid), .eq(comparator_2_eq));  // open: gt, lt
  Comparator #(.width(5), .mode("twosComplement")) comparator_3 (
    .a(RTid), .b({5{1'b0}}), .eq(comparator_3_eq));  // open: gt, lt
  Comparator #(.width(5), .mode("twosComplement")) comparator_4 (
    .a(RTid), .b(EX_Wid), .eq(comparator_4_eq));  // open: gt, lt
  not not_1 (not_1_out, comparator_1_eq);
  not not_2 (not_2_out, comparator_3_eq);
  and and_1 (and_1_out, RSin, not_1_out, EX_MemToReg, comparator_2_eq);
  and and_2 (and_2_out, RTin, not_2_out, EX_MemToReg, comparator_4_eq);
  or or_1 (load, and_1_out, and_2_out);
  Comparator #(.width(5), .mode("twosComplement")) comparator_5 (
    .a(RSid), .b({5{1'b0}}), .eq(comparator_5_eq));  // open: gt, lt
  Comparator #(.width(5), .mode("twosComplement")) comparator_6 (
    .a(RSid), .b(EX_Wid), .eq(comparator_6_eq));  // open: gt, lt
  Comparator #(.width(5), .mode("twosComplement")) comparator_7 (
    .a(RSid), .b({5{1'b0}}), .eq(comparator_7_eq));  // open: gt, lt
  Comparator #(.width(5), .mode("twosComplement")) comparator_8 (
    .a(RSid), .b(MEM_Wid), .eq(comparator_8_eq));  // open: gt, lt
  Comparator #(.width(5), .mode("twosComplement")) comparator_9 (
    .a(RTid), .b({5{1'b0}}), .eq(comparator_9_eq));  // open: gt, lt
  Comparator #(.width(5), .mode("twosComplement")) comparator_10 (
    .a(RTid), .b(EX_Wid), .eq(comparator_10_eq));  // open: gt, lt
  Comparator #(.width(5), .mode("twosComplement")) comparator_11 (
    .a(RTid), .b({5{1'b0}}), .eq(comparator_11_eq));  // open: gt, lt
  Comparator #(.width(5), .mode("twosComplement")) comparator_12 (
    .a(RTid), .b(MEM_Wid), .eq(comparator_12_eq));  // open: gt, lt
  not not_3 (not_3_out, comparator_5_eq);
  not not_4 (not_4_out, comparator_7_eq);
  not not_5 (not_5_out, comparator_9_eq);
  not not_6 (not_6_out, comparator_11_eq);
  and and_3 (and_3_out, RSin, not_3_out, EX_Regwrite, comparator_6_eq);
  and and_4 (and_4_out, RSin, not_4_out, MEM_Regwrite, comparator_8_eq);
  and and_5 (and_5_out, RTin, not_5_out, EX_Regwrite, comparator_10_eq);
  and and_6 (and_6_out, RTin, not_6_out, MEM_Regwrite, comparator_12_eq);
  Multiplexer #(.select(1), .width(2), .disabled("Z"), .enable("false")) multiplexer_1 (
    .in0(2'b00), .in1(2'b01), .out(multiplexer_1_out), .sel(and_4_out));
  Multiplexer #(.select(1), .width(2), .disabled("Z"), .enable("false")) multiplexer_2 (
    .in0(2'b00), .in1(2'b01), .out(multiplexer_2_out), .sel(and_6_out));
  Multiplexer #(.select(1), .width(2), .disabled("Z"), .enable("false")) multiplexer_3 (
    .in0(multiplexer_1_out), .in1(2'b10), .out(RS_F), .sel(and_3_out));
  Multiplexer #(.select(1), .width(2), .disabled("Z"), .enable("false")) multiplexer_4 (
    .in0(multiplexer_2_out), .in1(2'b10), .out(RT_F), .sel(and_5_out));

  // Other names for the same wires on the sheet: EX_MTR = EX_MemToReg; EX_Reg = EX_Regwrite; EX_W_num[4:0] = EX_Wid;
  //   MEM_Reg = MEM_Regwrite; MEM_W_num[4:0] = MEM_Wid; RS[4:0] = RSid; RSread = RSin; RT[4:0] = RTid; RTread = RTin
endmodule

module \双位预测状态转换  (
  input  P1,
  input  P0,
  input  IsJump,
  output S1,
  output S0
);

  wire and_1_out, and_2_out, and_3_out, and_4_out, not_1_out, not_2_out, not_3_out, not_4_out, not_5_out;

  not not_1 (not_1_out, P0);
  not not_2 (not_2_out, P1);
  not not_3 (not_3_out, P0);
  not not_4 (not_4_out, P0);
  not not_5 (not_5_out, IsJump);
  and and_1 (and_1_out, P0, IsJump);
  and and_2 (and_2_out, P1, not_1_out);
  and and_3 (and_3_out, not_2_out, not_3_out, IsJump);
  and and_4 (and_4_out, P1, not_4_out, not_5_out);
  or or_1 (S1, and_1_out, and_2_out);
  or or_2 (S0, and_3_out, and_4_out);
endmodule
module \动态预测  (
  output RegWrite,
  output MemWrite,
  output [31:0] IF_PC,
  output [31:0] ID_PC,
  output [31:0] EX_PC,
  output [31:0] M_PC,
  output [31:0] WB_PC,
  output [31:0] RDin,
  output [31:0] MDin,
  output [31:0] LedData
);

  wire and_1_out, and_2_out, and_3_out, and_4_out, and_6_out, and_7_out, and_9_out, and_10_out, and_11_out,
       CLK, clock_1_out, comparator_1_eq, comparator_1_lt, comparator_2_eq, comparator_3_eq, d_ff_1_q, EN,
       EX_Aluequal, EX_Alugreatequal, EX_Aluless, EX_AluSrcB, EX_AUIPC, EX_BE, EX_BEQ, EX_BGE, EX_BNE,
       EX_Branch, EX_ecall, EX_isBranchIR, EX_JAL, EX_JALR, EX_JUMP, EX_LB, EX_MemToReg, EX_MemWrite,
       EX_PredictErr, EX_RegWrite, EX_S_type, Go, halt, ID_AluSrcB, ID_AUIPC, ID_BEQ, ID_BGE, ID_BNE, ID_CSR,
       ID_ecall, ID_JAL, ID_JALR, ID_LB, ID_MemToReg, ID_MemWrite, ID_RegWrite, ID_S_type, ID_URET, IR1, IR2,
       IR3, load, locker_1_out, locker_2_out, MEM_AluSrcB, MEM_AUIPC, MEM_BE, MEM_BEQ, MEM_BGE, MEM_BNE,
       MEM_ecall, MEM_JAL, MEM_JALR, MEM_LB, MEM_MemToReg, MEM_RegWrite, MEM_S_type, nand_1_out, nor_1_out,
       nor_2_out, nor_3_out, not_2_out, not_3_out, not_4_out, not_5_out, not_6_out, not_7_out, or_1_out,
       or_2_out, or_3_out, or_8_out, PredictJump, RST, W1, W2, W3, WB_AluSrcB, WB_AUIPC, WB_BE, WB_BEQ,
       WB_BGE, WB_BNE, WB_ecall, WB_JAL, WB_JALR, WB_LB, WB_MemToReg, WB_MemWrite, WB_S_type,
       \单周期硬布线控制器_1_rsread , \单周期硬布线控制器_1_rtread ;
  wire [1:0] EX_RS_F, EX_RT_F, ID_RS_F, ID_RT_F;
  wire [3:0] EX_AluOP, ID_AluOP, MEM_AluOP, WB_AluOP;
  wire [4:0] EX_W_num, funct, MEM_W_num, RSid, RTid, WB_W_num;
  wire [7:0] multiplexer_14_out;
  wire [11:0] multiplexer_7_out;
  wire [12:0] CNT_num;
  wire [15:0] \LoadUse次数 , \总周期数 , \插入气泡数 , \无条件分支数 , \条件分支成功数 ;
  wire [31:0] and_8_out, bit_extender_1_out, bit_extender_2_out, bit_extender_4_out, EX_AUIPCresult,
       EX_BEaddr, EX_Branchaddr, EX_imm, EX_IR, EX_JALaddr, EX_nextPC, EX_R1, EX_R2, EX_Result,
       ID_AUIPCresult, ID_BEaddr, id_ex_1_r1out, id_ex_1_r2out, ID_imm, ID_IR, ID_JALaddr, ID_nextPC, ID_R1,
       ID_R2, IF_IR, IF_nextPC, Jumpaddr, MEM_ALUout, MEM_BEaddr, MEM_imm, MEM_IR, MEM_JALaddr, MEM_nextPC,
       MEM_R1, mem_wb_1_aluresultout, mem_wb_1_memout, multiplexer_1_out, multiplexer_2_out,
       multiplexer_10_out, multiplexer_11_out, multiplexer_13_out, multiplexer_15_out, multiplexer_16_out,
       not_8_out, PCaddr, ram_1_data, shifter_1_out, shifter_2_out, WB_BEaddr, WB_imm, WB_IR, WB_JALaddr,
       WB_nextPC, WB_R1, WB_R2;

  Button \u_总复位  (.out(RST));
  Button _1 (.out(IR1));
  Button _2 (.out(IR2));
  Button _3 (.out(IR3));
  // Probe on \总周期数 
  // Probe on \总周期数 
  Button \u_继续运行  (.out(Go));
  LED #(.active("true")) led_1 (.in(W1));
  LED #(.active("true")) led_2 (.in(W2));
  LED #(.active("true")) led_3 (.in(W3));
  Hex_Digit_Display hex_digit_display_1 (.value(LedData[31:28]));  // open: dp
  // Probe on IF_PC[19:0]
  // RiscV_Probe riscv_probe_1: pin names not known; wires that end beside it: IF_IR
  Register #(.width(32), .trigger("rising"), .Select("low")) PC (
    .D(PCaddr), .en(nor_1_out), .Q(IF_PC), .clk(CLK), .clr(RST));
  nor nor_1 (nor_1_out, halt, load);
  Hex_Digit_Display hex_digit_display_2 (.value(LedData[23:20]));  // open: dp
  Hex_Digit_Display hex_digit_display_3 (.value(LedData[27:24]));  // open: dp
  // Probe on ID_PC[19:0]
  // RiscV_Probe riscv_probe_2: pin names not known; wires that end beside it: {ID_IR[31], funct[4], ID_IR[29:26], funct[3], ID_IR[24:15], funct[2], ID_IR[13:0]}
  not not_1 (EN, halt);
  Counter #(.width(16), .max('hffff), .ongoal("wrap"), .trigger("rising"), .behavior("new")) counter_1 (
    .D({16{1'b0}}), .Q(\总周期数 ), .clk(and_1_out));  // open: load, count, carry, clr, preset, down
  and and_1 (and_1_out, CLK, not_2_out);
  not not_2 (not_2_out, WB_ecall);
  Hex_Digit_Display hex_digit_display_4 (.value(LedData[15:12]));  // open: dp
  Hex_Digit_Display hex_digit_display_5 (.value(LedData[19:16]));  // open: dp
  Adder #(.width(32)) adder_1 (.a(IF_PC), .b(32'h4), .out(IF_nextPC));  // open: cin, cout
  Hex_Digit_Display hex_digit_display_6 (.value(LedData[11:8]));  // open: dp
  Hex_Digit_Display hex_digit_display_7 (.value(LedData[7:4]));  // open: dp
  // Probe on EX_PC[19:0]
  // RiscV_Probe riscv_probe_3: pin names not known; wires that end beside it: EX_IR
  ROM #(.addrWidth(10), .dataWidth(32), .Select("high")) \u_指令存储器  (.addr(IF_PC[11:2]), .data(IF_IR));
  Hex_Digit_Display hex_digit_display_8 (.value(LedData[3:0]));  // open: dp
  // RiscV_Probe riscv_probe_4: pin names not known; wires that end beside it: IF_IR
  nor nor_2 (nor_2_out, halt, load);
  Multiplexer #(.select(1), .width(32), .disabled("Z"), .enable("false")) multiplexer_1 (
    .in0(EX_nextPC), .in1(EX_Branchaddr), .out(multiplexer_1_out), .sel(EX_Branch));
  // Probe on \总周期数 
  // Probe on M_PC[19:0]
  // RiscV_Probe riscv_probe_5: pin names not known; wires that end beside it: MEM_IR
  BTB btb_1 (
    .CLK(CLK), .EX_isBranchIR(EX_isBranchIR), .EX_BranchTaken(EX_Branch), .PC(IF_PC), .EX_PC(EX_PC),
    .EX_Branchaddr(EX_Branchaddr), .PredictJump(PredictJump), .Jumpaddr(Jumpaddr));
  Multiplexer #(.select(1), .width(32), .disabled("Z"), .enable("false")) multiplexer_2 (
    .in0(IF_nextPC), .in1(Jumpaddr), .out(multiplexer_2_out), .sel(PredictJump));
  // Probe on \总周期数 
  // Probe on \无条件分支数 
  // Probe on \条件分支成功数 
  // Probe on \插入气泡数 
  // Probe on \LoadUse次数 
  IF_ID if_id_1 (
    .PCin(IF_PC), .nextPCin(IF_nextPC), .IRin(IF_IR), .EN(nor_2_out), .CLK(CLK), .RESET(EX_PredictErr),
    .PCout(ID_PC), .nextPCout(ID_nextPC),
    .IRout({ID_IR[31], funct[4], ID_IR[29:26], funct[3], ID_IR[24:15], funct[2], ID_IR[13:0]}));
  locker locker_1 (.in(PredictJump), .CLK(CLK), .EN(nor_2_out), .RST(EX_PredictErr), .out(locker_1_out));
  Multiplexer #(.select(1), .width(32), .disabled("Z"), .enable("false")) multiplexer_3 (
    .in0(multiplexer_2_out), .in1(multiplexer_1_out), .out(PCaddr), .sel(EX_PredictErr));
  // Probe on IF_PC[11:0]
  // Probe on WB_PC[19:0]
  // RiscV_Probe riscv_probe_6: pin names not known; wires that end beside it: WB_IR
  // RiscV_Probe riscv_probe_7: pin names not known; wires that end beside it: {ID_IR[31], funct[4], ID_IR[29:26], funct[3], ID_IR[24:15], funct[2], ID_IR[13:0]}
  not not_3 (not_3_out, ID_IR[0]);
  not not_4 (not_4_out, ID_IR[1]);
  // Probe on ID_PC[11:0]
  // Probe on EX_PC[11:0]
  and and_2 (and_2_out, not_3_out, not_4_out);
  // Probe on M_PC[11:0]
  D_Flip_Flop #(.trigger("high"), .Pre_Clr_Positions("LEGACY"), .NegatePresetClear("false"), .enable("true"), .NewFFLayout("false")) d_ff_1 (.Q(d_ff_1_q));  // open: clk, D, Qn, preset, en, reset
  // Probe on 13'h1c
  Multiplexer #(.select(1), .width(2), .disabled("Z"), .enable("false")) multiplexer_4 (
    .in0(ID_IR[13:12]), .in1(2'b11), .out(funct[1:0]), .sel(and_2_out));
  // Probe on WB_PC[11:0]
  Comparator #(.width(13), .mode("twosComplement")) comparator_1 (
    .a(CNT_num), .b(13'h1c), .eq(comparator_1_eq), .lt(comparator_1_lt));  // open: gt
  Clock #(.highDuration(1), .lowDuration(1)) clock_1 (.out(clock_1_out));
  Counter #(.width(16), .max('hffff), .ongoal("wrap"), .trigger("rising"), .behavior("new")) counter_2 (
    .D({16{1'b0}}), .count(load), .Q(\LoadUse次数 ), .clk(CLK), .clr(RST));  // open: load, carry, preset, down
  nand nand_1 (nand_1_out, d_ff_1_q, comparator_1_eq);
  Counter #(.width(13), .max('h1fff), .ongoal("stay"), .trigger("rising"), .behavior("old")) counter_3 (
    .count(comparator_1_lt), .Q(CNT_num), .clk(clock_1_out));  // open: load, D, carry, clr, preset
  assign CLK = nand_1_out ? clock_1_out : 1'bz;  // Controlled_Buffer controlled_buffer_1
  \单周期硬布线控制器  \u_单周期硬布线控制器_1  (
    .Funct(funct), .OP(ID_IR[6:2]), .ALU_OP(ID_AluOP), .MemToReg(ID_MemToReg), .MemWrite(ID_MemWrite),
    .ALU_SRC(ID_AluSrcB), .RegWrite(ID_RegWrite), .ecall(ID_ecall), .S_type(ID_S_type), .Jalr(ID_JALR),
    .Beq(ID_BEQ), .JAL(ID_JAL), .Bne(ID_BNE), .in_3(ID_IR[21]), .uret(ID_URET), .CSR(ID_CSR),
    .AUIPC(ID_AUIPC), .LB(ID_LB), .BGE(ID_BGE), .RSread(\单周期硬布线控制器_1_rsread ), .RTread(\单周期硬布线控制器_1_rtread ));
  Multiplexer #(.select(1), .width(5), .disabled("Z"), .enable("false")) multiplexer_5 (
    .in0(ID_IR[19:15]), .in1(5'b10001), .out(RSid), .sel(ID_ecall));
  Multiplexer #(.select(1), .width(5), .disabled("Z"), .enable("false")) multiplexer_6 (
    .in0(ID_IR[24:20]), .in1(5'b01010), .out(RTid), .sel(ID_ecall));
  Multiplexer #(.select(1), .width(12), .disabled("Z"), .enable("false")) multiplexer_7 (
    .in0({ID_IR[31], funct[4], ID_IR[29:26], funct[3], ID_IR[24:20]}),
    .in1({ID_IR[31], funct[4], ID_IR[29:26], funct[3], ID_IR[11:7]}), .out(multiplexer_7_out), .sel(ID_S_type));
  Comparator #(.width(32), .mode("twosComplement")) comparator_2 (
    .a(WB_R1), .b(32'h22), .eq(comparator_2_eq));  // open: gt, lt
  or or_1 (or_1_out, EX_JAL, EX_JALR);
  Pull_Resistor #(.pull(1)) pull_resistor_1 (.node(CLK));
  assign bit_extender_1_out = {{20{ID_IR[31]}}, {ID_IR[31], ID_IR[7], funct[4], ID_IR[29:26], funct[3], ID_IR[11:8]}};  // Bit_Extender bit_extender_1
  assign bit_extender_2_out = {{12{ID_IR[31]}}, {ID_IR[31], ID_IR[19:15], funct[2], ID_IR[13:12], ID_IR[20], funct[4], ID_IR[29:26], funct[3], ID_IR[24:21]}};  // Bit_Extender bit_extender_2
  not not_5 (not_5_out, comparator_2_eq);
  and and_3 (and_3_out, comparator_2_eq, WB_ecall);
  Counter #(.width(16), .max('hffff), .ongoal("wrap"), .trigger("rising"), .behavior("new")) counter_4 (
    .D({16{1'b0}}), .count(or_1_out), .Q(\无条件分支数 ), .clk(CLK), .clr(RST));  // open: load, carry, preset, down
  Regifile regifile_1 (
    .Din(RDin), .Clk(CLK), .R1(ID_R1), .R2(ID_R2), .WE(RegWrite), .W_num(WB_W_num), .R1_num(RSid),
    .R2_num(RTid));
  assign ID_imm = {{20{multiplexer_7_out[11]}}, multiplexer_7_out};  // Bit_Extender bit_extender_3
  and and_4 (and_4_out, WB_ecall, not_5_out);
  Register #(.width(32), .trigger("rising"), .Select("low")) register_1 (
    .D(WB_R2), .en(and_3_out), .Q(LedData), .clk(CLK));  // open: clr
  load_judge load_judge_1 (
    .RSin(\单周期硬布线控制器_1_rsread ), .RTin(\单周期硬布线控制器_1_rtread ), .RSid(RSid), .RTid(RTid),
    .EX_Regwrite(EX_RegWrite), .MEM_Regwrite(MEM_RegWrite), .EX_Wid(EX_W_num), .MEM_Wid(MEM_W_num),
    .EX_MemToReg(EX_MemToReg), .RS_F(ID_RS_F), .RT_F(ID_RT_F), .load(load));
  Shifter #(.width(32), .shift("ll")) shifter_1 (.in(bit_extender_1_out), .\dist (5'b00001), .out(shifter_1_out));
  Shifter #(.width(32), .shift("ll")) shifter_2 (.in(bit_extender_2_out), .\dist (5'b00001), .out(shifter_2_out));
  not not_6 (not_6_out, Go);
  and and_5 (halt, not_6_out, and_4_out);
  Adder #(.width(32)) adder_2 (.a(shifter_1_out), .b(ID_PC), .out(ID_BEaddr), .cin(1'b0));  // open: cout
  Adder #(.width(32)) adder_3 (.a(shifter_2_out), .b(ID_PC), .out(ID_JALaddr), .cin(1'b0));  // open: cout
  Adder #(.width(32)) adder_4 (
    .a({ID_IR[31], funct[4], ID_IR[29:26], funct[3], ID_IR[24:15], funct[2], ID_IR[13:12], {12{1'b0}}}),
    .b(ID_PC), .out(ID_AUIPCresult), .cin(1'b0));  // open: cout
  and and_6 (and_6_out, EX_Branch, nor_3_out);
  nor nor_3 (nor_3_out, EX_JAL, EX_JALR);
  Counter #(.width(16), .max('hffff), .ongoal("wrap"), .trigger("rising"), .behavior("new")) counter_5 (
    .D({16{1'b0}}), .count(and_6_out), .Q(\条件分支成功数 ), .clk(CLK), .clr(RST));  // open: load, carry, preset, down
  or or_2 (or_2_out, EX_PredictErr, load);
  and and_7 (and_7_out, EX_isBranchIR, EX_PredictErr);
  ID_EX id_ex_1 (
    .RegWritein(ID_RegWrite), .MemToRegin(ID_MemToReg), .MemWritein(ID_MemWrite), .ALUOPin(ID_AluOP),
    .ALUSrcin(ID_AluSrcB), .ecallin(ID_ecall), .S_typein(ID_S_type), .BEQin(ID_BEQ), .BNEin(ID_BNE),
    .JALin(ID_JAL), .JALRin(ID_JALR), .AUIPCin(ID_AUIPC), .LBin(ID_LB), .BGEin(ID_BGE), .R1in(ID_R1),
    .R2in(ID_R2), .W_in(ID_IR[11:7]), .immin(ID_imm), .BEaddrin(ID_BEaddr), .PCin(ID_PC),
    .nextPCin(ID_nextPC), .JALaddrin(ID_JALaddr),
    .IRin({ID_IR[31], funct[4], ID_IR[29:26], funct[3], ID_IR[24:15], funct[2], ID_IR[13:0]}),
    .RESET(or_2_out), .EN(EN), .CLK(CLK), .RegWriteout(EX_RegWrite), .MemToRegout(EX_MemToReg),
    .MemWriteout(EX_MemWrite), .ALUOPout(EX_AluOP), .ALUSrcout(EX_AluSrcB), .ecallout(EX_ecall),
    .S_typeout(EX_S_type), .BEQout(EX_BEQ), .BNEout(EX_BNE), .JALout(EX_JAL), .JALRout(EX_JALR),
    .AUIPCout(EX_AUIPC), .LBout(EX_LB), .BGEout(EX_BGE), .R1out(id_ex_1_r1out), .R2out(id_ex_1_r2out),
    .W_out(EX_W_num), .immout(EX_imm), .BEaddrout(EX_BEaddr), .PCout(EX_PC), .nextPCout(EX_nextPC),
    .JALaddrout(EX_JALaddr), .IRout(EX_IR), .RS_Fin(ID_RS_F), .RS_Fout(EX_RS_F), .RT_Fin(ID_RT_F),
    .RT_Fout(EX_RT_F), .AUIPCresin(ID_AUIPCresult), .AUIPCresout(EX_AUIPCresult));
  or or_3 (or_3_out, and_7_out, load);
  Counter #(.width(16), .max('hffff), .ongoal("wrap"), .trigger("rising"), .behavior("new")) counter_6 (
    .D({16{1'b0}}), .count(or_3_out), .Q(\插入气泡数 ), .clk(CLK), .clr(RST));  // open: load, carry, preset, down
  locker locker_2 (.in(locker_1_out), .CLK(CLK), .EN(EN), .RST(or_2_out), .out(locker_2_out));
  Multiplexer #(.select(2), .width(32), .disabled("Z"), .enable("false")) multiplexer_8 (
    .in0(id_ex_1_r1out), .in1(RDin), .in2(MEM_ALUout), .out(EX_R1), .sel(EX_RS_F));  // open: in3
  Multiplexer #(.select(2), .width(32), .disabled("Z"), .enable("false")) multiplexer_9 (
    .in0(id_ex_1_r2out), .in1(RDin), .in2(MEM_ALUout), .out(EX_R2), .sel(EX_RT_F));  // open: in3
  or or_4 (EX_isBranchIR, EX_BEQ, EX_BNE, EX_JAL, EX_JALR, EX_BGE);
  not not_7 (not_7_out, EX_Aluequal);
  Multiplexer #(.select(1), .width(32), .disabled("Z"), .enable("false")) multiplexer_10 (
    .in0(EX_BEaddr), .in1(EX_JALaddr), .out(multiplexer_10_out), .sel(EX_JAL));
  assign and_8_out = EX_Result & not_8_out;  // AND_Gate and_8, 32 bits wide
  assign not_8_out = ~32'h1;  // NOT_Gate not_8, 32 bits wide
  Multiplexer #(.select(1), .width(32), .disabled("Z"), .enable("false")) multiplexer_11 (
    .in0(EX_R2), .in1(EX_imm), .out(multiplexer_11_out), .sel(EX_AluSrcB));
  and and_9 (and_9_out, EX_Aluequal, EX_BEQ);
  and and_10 (and_10_out, not_7_out, EX_BNE);
  and and_11 (and_11_out, EX_Alugreatequal, EX_BGE);
  or or_5 (EX_JUMP, EX_JAL, EX_JALR);
  Multiplexer #(.select(1), .width(32), .disabled("Z"), .enable("false")) multiplexer_12 (
    .in0(multiplexer_10_out), .in1(and_8_out), .out(EX_Branchaddr), .sel(EX_JALR));
  ALU alu_1 (
    .X(EX_R1), .Y(multiplexer_11_out), .AluOP(EX_AluOP), .Equal(EX_Aluequal), .Result(EX_Result),
    .out_4(EX_Alugreatequal), .out_6(EX_Aluless));  // open: Result_2
  or or_6 (EX_BE, and_9_out, and_10_out, and_11_out);
  or or_7 (EX_Branch, EX_JUMP, EX_BE);
  Comparator #(.width(1), .mode("twosComplement")) comparator_3 (
    .a(EX_Branch), .b(locker_2_out), .eq(comparator_3_eq));  // open: gt, lt
  not not_9 (EX_PredictErr, comparator_3_eq);
  Multiplexer #(.select(1), .width(32), .disabled("Z"), .enable("false")) multiplexer_13 (
    .in0(EX_Result), .in1(EX_AUIPCresult), .out(multiplexer_13_out), .sel(EX_AUIPC));
  EX_MEM ex_mem_1 (
    .RegWritein(EX_RegWrite), .MemToRegin(EX_MemToReg), .MemWritein(EX_MemWrite), .ALUOPin(EX_AluOP),
    .ALUSrcin(EX_AluSrcB), .ecallin(EX_ecall), .S_typein(EX_S_type), .BEQin(EX_BEQ), .BNEin(EX_BNE),
    .JALin(EX_JAL), .JALRin(EX_JALR), .AUIPCin(EX_AUIPC), .LBin(EX_LB), .BGEin(EX_BGE), .R1in(EX_R1),
    .R2in(EX_R2), .W_in(EX_W_num), .immin(EX_imm), .BEaddrin(EX_BEaddr), .PCin(EX_PC), .nextPCin(EX_nextPC),
    .JALaddrin(EX_JALaddr), .IRin(EX_IR), .BEin(EX_BE), .ALUResultin(multiplexer_13_out), .RESET(1'b0),
    .EN(EN), .CLK(CLK), .RegWriteout(MEM_RegWrite), .MemToRegout(MEM_MemToReg), .MemWriteout(MemWrite),
    .ALUOPout(MEM_AluOP), .ALUSrcout(MEM_AluSrcB), .ecallout(MEM_ecall), .S_typeout(MEM_S_type),
    .BEQout(MEM_BEQ), .BNEout(MEM_BNE), .JALout(MEM_JAL), .JALRout(MEM_JALR), .AUIPCout(MEM_AUIPC),
    .LBout(MEM_LB), .BGEout(MEM_BGE), .R1out(MEM_R1), .R2out(MDin), .W_out(MEM_W_num), .immout(MEM_imm),
    .BEaddrout(MEM_BEaddr), .PCout(M_PC), .nextPCout(MEM_nextPC), .JALaddrout(MEM_JALaddr), .IRout(MEM_IR),
    .BEout(MEM_BE), .ALUResultout(MEM_ALUout));
  RAM #(.addrWidth(10), .dataWidth(32), .bus("separate"), .Select("high")) ram_1 (
    .addr(MEM_ALUout[11:2]), .din(MDin), .data(ram_1_data), .str(MemWrite), .clk(CLK));  // open: sel, ld, clr
  Multiplexer #(.select(2), .width(8), .disabled("Z"), .enable("false")) multiplexer_14 (
    .in0(ram_1_data[7:0]), .in1(ram_1_data[15:8]), .in2(ram_1_data[23:16]), .in3(ram_1_data[31:24]),
    .out(multiplexer_14_out), .sel(MEM_ALUout[1:0]));
  assign bit_extender_4_out = {{24{multiplexer_14_out[7]}}, multiplexer_14_out};  // Bit_Extender bit_extender_4
  Multiplexer #(.select(1), .width(32), .disabled("Z"), .enable("false")) multiplexer_15 (
    .in0(ram_1_data), .in1(bit_extender_4_out), .out(multiplexer_15_out), .sel(MEM_LB));
  MEM_WB mem_wb_1 (
    .RegWritein(MEM_RegWrite), .MemToRegin(MEM_MemToReg), .MemWritein(MemWrite), .ALUOPin(MEM_AluOP),
    .ALUSrcin(MEM_AluSrcB), .ecallin(MEM_ecall), .S_typein(MEM_S_type), .BEQin(MEM_BEQ), .BNEin(MEM_BNE),
    .JALin(MEM_JAL), .JALRin(MEM_JALR), .AUIPCin(MEM_AUIPC), .LBin(MEM_LB), .BGEin(MEM_BGE),
    .W_in(MEM_W_num), .immin(MEM_imm), .BEaddrin(MEM_BEaddr), .PCin(M_PC), .nextPCin(MEM_nextPC),
    .JALaddrin(MEM_JALaddr), .IRin(MEM_IR), .BEin(MEM_BE), .ALUResultin(MEM_ALUout), .RESET(1'b0), .EN(EN),
    .CLK(CLK), .RegWriteout(RegWrite), .MemToRegout(WB_MemToReg), .MemWriteout(WB_MemWrite),
    .ALUOPout(WB_AluOP), .ALUSrcout(WB_AluSrcB), .ecallout(WB_ecall), .S_typeout(WB_S_type), .BEQout(WB_BEQ),
    .BNEout(WB_BNE), .JALout(WB_JAL), .JALRout(WB_JALR), .AUIPCout(WB_AUIPC), .LBout(WB_LB), .BGEout(WB_BGE),
    .W_out(WB_W_num), .immout(WB_imm), .BEaddrout(WB_BEaddr), .PCout(WB_PC), .nextPCout(WB_nextPC),
    .JALaddrout(WB_JALaddr), .IRout(WB_IR), .BEout(WB_BE), .ALUResultout(mem_wb_1_aluresultout),
    .Memin(multiplexer_15_out), .Memout(mem_wb_1_memout), .R1in(MEM_R1), .R1out(WB_R1), .R2in(MDin),
    .R2out(WB_R2));
  Multiplexer #(.select(1), .width(32), .disabled("Z"), .enable("false")) multiplexer_16 (
    .in0(mem_wb_1_aluresultout), .in1(mem_wb_1_memout), .out(multiplexer_16_out), .sel(WB_MemToReg));
  or or_8 (or_8_out, WB_JAL, WB_JALR);
  Multiplexer #(.select(1), .width(32), .disabled("Z"), .enable("false")) multiplexer_17 (
    .in0(multiplexer_16_out), .in1(WB_nextPC), .out(RDin), .sel(or_8_out));

  // Other names for the same wires on the sheet: ID_W_num[4:0] = ID_IR[11:7]; ID_IR (some bits) = funct[4:2];
  //   MEM_MemWrite = MemWrite; MEM_PC[31:0] = M_PC; MEM_R2[31:0] = MDin; WB_RegWrite = RegWrite

  // Notes on the sheet:
  //   中断源
  //   时空图监测，可删除
  //   中断等待指示
  //   数码管输出
  //   contents of 指令存储器 (hex, n*v repeats v):
  //   100493 100006f 100493 200913 300993 100006f 100493 200913 300993 100006f 100493 200913 300993
  //   100006f 100493 200913 300993 40c000ef 100413 100493 1f49493 900533 2200893 73 24d493 48463 fedff06f
  //   900533 2200893 73 100493 249493 900533 2200893 73 48463 fedff06f 100493 1f49493 900533 2200893 73
  //   4034d493 900533 2200893 73 4044d493 900533 2200893 73 4044d493 900533 2200893 73 4044d493 900533
  //   2200893 73 4044d493 900533 2200893 73 4044d493 900533 2200893 73 4044d493 900533 2200893 73 4044d493
  //   900533 2200893 73 100413 1f41993 41f9d993 433 c00913 300b13 140413 f47413 800293 100313 499993
  //   89e9b3 1300533 2200893 73 406282b3 fe0294e3 140413 f00f93 1f47433 1c41413 800293 100313 49d993
  //   89e9b3 1300533 2200893 73 406282b3 fe0294e3 1c45413 406b0b33 b0463 f95ff06f 2b3 fff2c293 829293
  //   ff2e293 500533 2200893 73 fff00413 493 84a023 140413 448493 84a023 140413 448493 84a023 140413
  //   448493 84a023 140413 448493 84a023 140413 448493 84a023 140413 448493 84a023 140413 448493 84a023
  //   140413 448493 84a023 140413 448493 84a023 140413 448493 84a023 140413 448493 84a023 140413 448493
  //   84a023 140413 448493 84a023 140413 448493 84a023 140413 448493 84a023 140413 448493 140413 433
  //   3c00493 42983 4aa03 149a2b3 28663 134a023 1442023 ffc48493 fe9412e3 800533 2200893 73 440413 3c00493
  //   fc9416e3 a00893 73 fff00293 7700493 849493 7748493 900533 2200893 73 1000e13 54c4b3 900533 2200893
  //   73 fffe0e13 fe0e16e3 a00893 73 13 430497 900533 2200893 73 430497 900533 2200893 73 430497 900533
  //   2200893 73 430497 900533 2200893 73 430497 900533 2200893 73 430497 900533 2200893 73 430497 900533
  //   2200893 73 430497 900533 2200893 73 a00893 73 313 1000e13 13 8400493 849493 8348493 400913 891913
  //   490913 849493 8248493 849493 8148493 891913 490913 891913 490913 932023 12484b3 430313 fffe0e13
  //   fe0e18e3 2000e13 313 30483 900533 2200893 73 130313 fffe0e13 fe0e14e3 a00893 73 f00493 900533
  //   2200893 73 fff48493 fe04d8e3 a00893 73 413 140413 800533 2200893 73 240413 800533 2200893 73 340413
  //   800533 2200893 73 440413 800533 2200893 73 540413 800533 2200893 73 640413 800533 2200893 73 740413
  //   800533 2200893 73 840413 800533 2200893 2200893 73 8067
  //   指令探针
  //   控制位
  //   流水调试日志用
  //   暂停节拍，不能为0
  //   戳工具置1进入计数暂停模式，ctrl+k时钟自动运行到对应节拍暂停
  //   ctrl+k关闭时钟连续运行，将控制位置零，进入单步调试模式调试
  //   JALR
  //   URET
  //   可计数暂停的时钟源
  //   Bne
  //   MemToReg
  //   MemWrite
  //   AluOP
  //   AluSrcB
  //   RegWrite
  //   为方便自动评测，需要输出流水线各段保存的PC值，注意是PC不是PC+4，另外ID段寄存器写入信息，Mem段内存写入信息也要输出
endmodule

module BTB (
  input  CLK,
  input  EX_isBranchIR,
  input  EX_BranchTaken,
  input  [31:0] PC,
  input  [31:0] EX_PC,
  input  [31:0] EX_Branchaddr,
  output PredictJump,
  output [31:0] Jumpaddr
);

  wire and_1_out, and_2_out, and_3_out, and_4_out, and_5_out, and_6_out, and_7_out, and_8_out, and_26_out,
       and_27_out, and_28_out, and_29_out, and_30_out, and_31_out, and_32_out, and_33_out, comparator_1_eq,
       comparator_2_eq, comparator_3_eq, comparator_4_eq, comparator_5_eq, comparator_6_eq, comparator_7_eq,
       comparator_8_eq, comparator_9_eq, comparator_10_eq, comparator_11_eq, comparator_12_eq,
       comparator_13_eq, comparator_14_eq, comparator_15_eq, comparator_16_eq, comparator_17_gt,
       comparator_18_gt, comparator_19_gt, comparator_20_gt, comparator_21_gt, comparator_22_gt,
       comparator_23_gt, comparator_24_gt, d_ff_1_q, d_ff_2_q, d_ff_3_q, d_ff_4_q, d_ff_5_q, d_ff_6_q,
       d_ff_7_q, d_ff_8_q, decoder_1_out0, decoder_1_out1, decoder_1_out2, decoder_1_out3, decoder_1_out4,
       decoder_1_out5, decoder_1_out6, decoder_1_out7, full, judge, L0, L1, L2, L3, L4, L5, L6, L7, or_1_out,
       or_2_out, or_3_out, or_4_out, or_5_out, or_6_out, or_7_out, or_8_out, read0, read1, read2, read3,
       read4, read5, read6, read7, readhit, readmiss, v0, v1, v2, v3, v4, v5, v6, v7, write0, write1, write2,
       write3, write4, write5, write6, write7, writehit, writemiss;
  wire [1:0] multiplexer_1_out, multiplexer_3_out, multiplexer_5_out, multiplexer_7_out, multiplexer_9_out,
       multiplexer_11_out, multiplexer_13_out, multiplexer_15_out, next0, next1, next2, next3, next4, next5,
       next6, next7, pre0, pre1, pre2, pre3, pre4, pre5, pre6, pre7, \双位预测状态转换_1_s0 , \双位预测状态转换_2_s0 ,
       \双位预测状态转换_3_s0 , \双位预测状态转换_4_s0 , \双位预测状态转换_5_s0 , \双位预测状态转换_6_s0 , \双位预测状态转换_7_s0 , \双位预测状态转换_8_s0 ;
  wire [2:0] empty_num, max3_1_max_num, max3_2_max_num, max3_3_max_num, max3_4_max_num, max3_5_max_num,
       max3_6_max_num, MAX_num, multiplexer_17_out;
  wire [31:0] cnt0, cnt1, cnt2, cnt3, cnt4, cnt5, cnt6, cnt7, Daddr0, Daddr1, Daddr2, Daddr3, Daddr4, Daddr5,
       Daddr6, Daddr7, MAX, max3_1_max, max3_2_max, max3_3_max, max3_4_max, max3_5_max, max3_6_max, PC0, PC1,
       PC2, PC3, PC4, PC5, PC6, PC7;

  Register #(.width(1), .trigger("rising"), .Select("low")) register_1 (
    .D(1'b1), .en(write0), .Q(v0), .clk(CLK));  // open: clr
  Register #(.width(1), .trigger("rising"), .Select("low")) register_2 (
    .D(1'b1), .en(write1), .Q(v1), .clk(CLK));  // open: clr
  Register #(.width(1), .trigger("rising"), .Select("low")) register_3 (
    .D(1'b1), .en(write2), .Q(v2), .clk(CLK));  // open: clr
  Register #(.width(1), .trigger("rising"), .Select("low")) register_4 (
    .D(1'b1), .en(write3), .Q(v3), .clk(CLK));  // open: clr
  Register #(.width(1), .trigger("rising"), .Select("low")) register_5 (
    .D(1'b1), .en(write4), .Q(v4), .clk(CLK));  // open: clr
  Register #(.width(1), .trigger("rising"), .Select("low")) register_6 (
    .D(1'b1), .en(write5), .Q(v5), .clk(CLK));  // open: clr
  Register #(.width(1), .trigger("rising"), .Select("low")) register_7 (
    .D(1'b1), .en(write6), .Q(v6), .clk(CLK));  // open: clr
  Register #(.width(1), .trigger("rising"), .Select("low")) register_8 (
    .D(1'b1), .en(write7), .Q(v7), .clk(CLK));  // open: clr
  and and_1 (and_1_out, judge, write0);
  and and_2 (and_2_out, judge, write1);
  and and_3 (and_3_out, judge, write2);
  and and_4 (and_4_out, judge, write3);
  and and_5 (and_5_out, judge, write4);
  and and_6 (and_6_out, judge, write5);
  and and_7 (and_7_out, judge, write6);
  and and_8 (and_8_out, judge, write7);
  Register #(.width(32), .trigger("rising"), .Select("low")) register_9 (
    .D(EX_PC), .en(and_1_out), .Q(PC0), .clk(CLK));  // open: clr
  Register #(.width(32), .trigger("rising"), .Select("low")) register_10 (
    .D(EX_PC), .en(and_2_out), .Q(PC1), .clk(CLK));  // open: clr
  Register #(.width(32), .trigger("rising"), .Select("low")) register_11 (
    .D(EX_PC), .en(and_3_out), .Q(PC2), .clk(CLK));  // open: clr
  Register #(.width(32), .trigger("rising"), .Select("low")) register_12 (
    .D(EX_PC), .en(and_4_out), .Q(PC3), .clk(CLK));  // open: clr
  Register #(.width(32), .trigger("rising"), .Select("low")) register_13 (
    .D(EX_PC), .en(and_5_out), .Q(PC4), .clk(CLK));  // open: clr
  Register #(.width(32), .trigger("rising"), .Select("low")) register_14 (
    .D(EX_PC), .en(and_6_out), .Q(PC5), .clk(CLK));  // open: clr
  Register #(.width(32), .trigger("rising"), .Select("low")) register_15 (
    .D(EX_PC), .en(and_7_out), .Q(PC6), .clk(CLK));  // open: clr
  Register #(.width(32), .trigger("rising"), .Select("low")) register_16 (
    .D(EX_PC), .en(and_8_out), .Q(PC7), .clk(CLK));  // open: clr
  Register #(.width(32), .trigger("rising"), .Select("low")) register_17 (
    .D(EX_Branchaddr), .en(write0), .Q(Daddr0), .clk(CLK));  // open: clr
  Register #(.width(32), .trigger("rising"), .Select("low")) register_18 (
    .D(EX_Branchaddr), .en(write1), .Q(Daddr1), .clk(CLK));  // open: clr
  Register #(.width(32), .trigger("rising"), .Select("low")) register_19 (
    .D(EX_Branchaddr), .en(write2), .Q(Daddr2), .clk(CLK));  // open: clr
  Register #(.width(32), .trigger("rising"), .Select("low")) register_20 (
    .D(EX_Branchaddr), .en(write3), .Q(Daddr3), .clk(CLK));  // open: clr
  Register #(.width(32), .trigger("rising"), .Select("low")) register_21 (
    .D(EX_Branchaddr), .en(write4), .Q(Daddr4), .clk(CLK));  // open: clr
  Register #(.width(32), .trigger("rising"), .Select("low")) register_22 (
    .D(EX_Branchaddr), .en(write5), .Q(Daddr5), .clk(CLK));  // open: clr
  Register #(.width(32), .trigger("rising"), .Select("low")) register_23 (
    .D(EX_Branchaddr), .en(write6), .Q(Daddr6), .clk(CLK));  // open: clr
  Register #(.width(32), .trigger("rising"), .Select("low")) register_24 (
    .D(EX_Branchaddr), .en(write7), .Q(Daddr7), .clk(CLK));  // open: clr
  Register #(.width(2), .trigger("rising"), .Select("low")) register_25 (
    .D(next0), .en(write0), .Q(pre0), .clk(CLK));  // open: clr
  Register #(.width(2), .trigger("rising"), .Select("low")) register_26 (
    .D(next1), .en(write1), .Q(pre1), .clk(CLK));  // open: clr
  Register #(.width(2), .trigger("rising"), .Select("low")) register_27 (
    .D(next2), .en(write2), .Q(pre2), .clk(CLK));  // open: clr
  Register #(.width(2), .trigger("rising"), .Select("low")) register_28 (
    .D(next3), .en(write3), .Q(pre3), .clk(CLK));  // open: clr
  Register #(.width(2), .trigger("rising"), .Select("low")) register_29 (
    .D(next4), .en(write4), .Q(pre4), .clk(CLK));  // open: clr
  Register #(.width(2), .trigger("rising"), .Select("low")) register_30 (
    .D(next5), .en(write5), .Q(pre5), .clk(CLK));  // open: clr
  Register #(.width(2), .trigger("rising"), .Select("low")) register_31 (
    .D(next6), .en(write6), .Q(pre6), .clk(CLK));  // open: clr
  Register #(.width(2), .trigger("rising"), .Select("low")) register_32 (
    .D(next7), .en(write7), .Q(pre7), .clk(CLK));  // open: clr
  Counter #(.width(32), .max('hffffffff), .ongoal("wrap"), .trigger("rising"), .behavior("new")) counter_0 (
    .D({32{1'b0}}), .Q(cnt0), .clk(CLK), .clr(d_ff_1_q));  // open: load, count, carry, preset, down
  or or_1 (or_1_out, read0, write0);
  Counter #(.width(32), .max('hffffffff), .ongoal("wrap"), .trigger("rising"), .behavior("new")) counter_1 (
    .D({32{1'b0}}), .Q(cnt1), .clk(CLK), .clr(d_ff_2_q));  // open: load, count, carry, preset, down
  or or_2 (or_2_out, read1, write1);
  Counter #(.width(32), .max('hffffffff), .ongoal("wrap"), .trigger("rising"), .behavior("new")) counter_2 (
    .D({32{1'b0}}), .Q(cnt2), .clk(CLK), .clr(d_ff_3_q));  // open: load, count, carry, preset, down
  or or_3 (or_3_out, read2, write2);
  Counter #(.width(32), .max('hffffffff), .ongoal("wrap"), .trigger("rising"), .behavior("new")) counter_3 (
    .D({32{1'b0}}), .Q(cnt3), .clk(CLK), .clr(d_ff_4_q));  // open: load, count, carry, preset, down
  or or_4 (or_4_out, read3, write3);
  Counter #(.width(32), .max('hffffffff), .ongoal("wrap"), .trigger("rising"), .behavior("new")) counter_4 (
    .D({32{1'b0}}), .Q(cnt4), .clk(CLK), .clr(d_ff_5_q));  // open: load, count, carry, preset, down
  or or_5 (or_5_out, read4, write4);
  Counter #(.width(32), .max('hffffffff), .ongoal("wrap"), .trigger("rising"), .behavior("new")) counter_5 (
    .D({32{1'b0}}), .Q(cnt5), .clk(CLK), .clr(d_ff_6_q));  // open: load, count, carry, preset, down
  or or_6 (or_6_out, read5, write5);
  Counter #(.width(32), .max('hffffffff), .ongoal("wrap"), .trigger("rising"), .behavior("new")) counter_6 (
    .D({32{1'b0}}), .Q(cnt6), .clk(CLK), .clr(d_ff_7_q));  // open: load, count, carry, preset, down
  or or_7 (or_7_out, read6, write6);
  Counter #(.width(32), .max('hffffffff), .ongoal("wrap"), .trigger("rising"), .behavior("new")) counter_7 (
    .D({32{1'b0}}), .Q(cnt7), .clk(CLK), .clr(d_ff_8_q));  // open: load, count, carry, preset, down
  or or_8 (or_8_out, read7, write7);
  D_Flip_Flop #(.trigger("rising"), .Pre_Clr_Positions("ABOVE_BELOW"), .NegatePresetClear("false"), .enable("true"), .NewFFLayout("false")) d_ff_1 (
    .clk(CLK), .D(or_1_out), .Q(d_ff_1_q));  // open: Qn, preset, en, reset
  D_Flip_Flop #(.trigger("rising"), .Pre_Clr_Positions("ABOVE_BELOW"), .NegatePresetClear("false"), .enable("true"), .NewFFLayout("false")) d_ff_2 (
    .clk(CLK), .D(or_2_out), .Q(d_ff_2_q));  // open: Qn, preset, en, reset
  D_Flip_Flop #(.trigger("rising"), .Pre_Clr_Positions("ABOVE_BELOW"), .NegatePresetClear("false"), .enable("true"), .NewFFLayout("false")) d_ff_3 (
    .clk(CLK), .D(or_3_out), .Q(d_ff_3_q));  // open: Qn, preset, en, reset
  D_Flip_Flop #(.trigger("rising"), .Pre_Clr_Positions("ABOVE_BELOW"), .NegatePresetClear("false"), .enable("true"), .NewFFLayout("false")) d_ff_4 (
    .clk(CLK), .D(or_4_out), .Q(d_ff_4_q));  // open: Qn, preset, en, reset
  D_Flip_Flop #(.trigger("rising"), .Pre_Clr_Positions("ABOVE_BELOW"), .NegatePresetClear("false"), .enable("true"), .NewFFLayout("false")) d_ff_5 (
    .clk(CLK), .D(or_5_out), .Q(d_ff_5_q));  // open: Qn, preset, en, reset
  D_Flip_Flop #(.trigger("rising"), .Pre_Clr_Positions("ABOVE_BELOW"), .NegatePresetClear("false"), .enable("true"), .NewFFLayout("false")) d_ff_6 (
    .clk(CLK), .D(or_6_out), .Q(d_ff_6_q));  // open: Qn, preset, en, reset
  D_Flip_Flop #(.trigger("rising"), .Pre_Clr_Positions("ABOVE_BELOW"), .NegatePresetClear("false"), .enable("true"), .NewFFLayout("false")) d_ff_7 (
    .clk(CLK), .D(or_7_out), .Q(d_ff_7_q));  // open: Qn, preset, en, reset
  D_Flip_Flop #(.trigger("rising"), .Pre_Clr_Positions("ABOVE_BELOW"), .NegatePresetClear("false"), .enable("true"), .NewFFLayout("false")) d_ff_8 (
    .clk(CLK), .D(or_8_out), .Q(d_ff_8_q));  // open: Qn, preset, en, reset
  Comparator #(.width(32), .mode("twosComplement")) comparator_1 (
    .a(PC0), .b(PC), .eq(comparator_1_eq));  // open: gt, lt
  Comparator #(.width(32), .mode("twosComplement")) comparator_2 (
    .a(PC1), .b(PC), .eq(comparator_2_eq));  // open: gt, lt
  Comparator #(.width(32), .mode("twosComplement")) comparator_3 (
    .a(PC2), .b(PC), .eq(comparator_3_eq));  // open: gt, lt
  Comparator #(.width(32), .mode("twosComplement")) comparator_4 (
    .a(PC3), .b(PC), .eq(comparator_4_eq));  // open: gt, lt
  Comparator #(.width(32), .mode("twosComplement")) comparator_5 (
    .a(PC4), .b(PC), .eq(comparator_5_eq));  // open: gt, lt
  Comparator #(.width(32), .mode("twosComplement")) comparator_6 (
    .a(PC5), .b(PC), .eq(comparator_6_eq));  // open: gt, lt
  Comparator #(.width(32), .mode("twosComplement")) comparator_7 (
    .a(PC6), .b(PC), .eq(comparator_7_eq));  // open: gt, lt
  Comparator #(.width(32), .mode("twosComplement")) comparator_8 (
    .a(PC7), .b(PC), .eq(comparator_8_eq));  // open: gt, lt
  \双位预测状态转换  \u_双位预测状态转换_1  (
    .P1(pre0[1]), .P0(pre0[0]), .IsJump(EX_BranchTaken), .S1(\双位预测状态转换_1_s0 [1]), .S0(\双位预测状态转换_1_s0 [0]));
  \双位预测状态转换  \u_双位预测状态转换_2  (
    .P1(pre1[1]), .P0(pre1[0]), .IsJump(EX_BranchTaken), .S1(\双位预测状态转换_2_s0 [1]), .S0(\双位预测状态转换_2_s0 [0]));
  \双位预测状态转换  \u_双位预测状态转换_3  (
    .P1(pre2[1]), .P0(pre2[0]), .IsJump(EX_BranchTaken), .S1(\双位预测状态转换_3_s0 [1]), .S0(\双位预测状态转换_3_s0 [0]));
  \双位预测状态转换  \u_双位预测状态转换_4  (
    .P1(pre3[1]), .P0(pre3[0]), .IsJump(EX_BranchTaken), .S1(\双位预测状态转换_4_s0 [1]), .S0(\双位预测状态转换_4_s0 [0]));
  \双位预测状态转换  \u_双位预测状态转换_5  (
    .P1(pre4[1]), .P0(pre4[0]), .IsJump(EX_BranchTaken), .S1(\双位预测状态转换_5_s0 [1]), .S0(\双位预测状态转换_5_s0 [0]));
  \双位预测状态转换  \u_双位预测状态转换_6  (
    .P1(pre5[1]), .P0(pre5[0]), .IsJump(EX_BranchTaken), .S1(\双位预测状态转换_6_s0 [1]), .S0(\双位预测状态转换_6_s0 [0]));
  \双位预测状态转换  \u_双位预测状态转换_7  (
    .P1(pre6[1]), .P0(pre6[0]), .IsJump(EX_BranchTaken), .S1(\双位预测状态转换_7_s0 [1]), .S0(\双位预测状态转换_7_s0 [0]));
  \双位预测状态转换  \u_双位预测状态转换_8  (
    .P1(pre7[1]), .P0(pre7[0]), .IsJump(EX_BranchTaken), .S1(\双位预测状态转换_8_s0 [1]), .S0(\双位预测状态转换_8_s0 [0]));
  and and_9 (read0, comparator_1_eq, v0);
  and and_10 (read1, comparator_2_eq, v1);
  and and_11 (read2, comparator_3_eq, v2);
  and and_12 (read3, comparator_4_eq, v3);
  and and_13 (read4, comparator_5_eq, v4);
  and and_14 (read5, comparator_6_eq, v5);
  and and_15 (read6, comparator_7_eq, v6);
  and and_16 (read7, comparator_8_eq, v7);
  Multiplexer #(.select(1), .width(2), .disabled("Z"), .enable("false")) multiplexer_1 (
    .in0(2'b00), .in1(2'b10), .out(multiplexer_1_out), .sel(EX_BranchTaken));
  Multiplexer #(.select(1), .width(2), .disabled("Z"), .enable("false")) multiplexer_2 (
    .in0(multiplexer_1_out), .in1(\双位预测状态转换_1_s0 ), .out(next0), .sel(writehit));
  Multiplexer #(.select(1), .width(2), .disabled("Z"), .enable("false")) multiplexer_3 (
    .in0(2'b00), .in1(2'b10), .out(multiplexer_3_out), .sel(EX_BranchTaken));
  Multiplexer #(.select(1), .width(2), .disabled("Z"), .enable("false")) multiplexer_4 (
    .in0(multiplexer_3_out), .in1(\双位预测状态转换_2_s0 ), .out(next1), .sel(writehit));
  Multiplexer #(.select(1), .width(2), .disabled("Z"), .enable("false")) multiplexer_5 (
    .in0(2'b00), .in1(2'b10), .out(multiplexer_5_out), .sel(EX_BranchTaken));
  Multiplexer #(.select(1), .width(2), .disabled("Z"), .enable("false")) multiplexer_6 (
    .in0(multiplexer_5_out), .in1(\双位预测状态转换_3_s0 ), .out(next2), .sel(writehit));
  Multiplexer #(.select(1), .width(2), .disabled("Z"), .enable("false")) multiplexer_7 (
    .in0(2'b00), .in1(2'b10), .out(multiplexer_7_out), .sel(EX_BranchTaken));
  Multiplexer #(.select(1), .width(2), .disabled("Z"), .enable("false")) multiplexer_8 (
    .in0(multiplexer_7_out), .in1(\双位预测状态转换_4_s0 ), .out(next3), .sel(writehit));
  Multiplexer #(.select(1), .width(2), .disabled("Z"), .enable("false")) multiplexer_9 (
    .in0(2'b00), .in1(2'b10), .out(multiplexer_9_out), .sel(EX_BranchTaken));
  Multiplexer #(.select(1), .width(2), .disabled("Z"), .enable("false")) multiplexer_10 (
    .in0(multiplexer_9_out), .in1(\双位预测状态转换_5_s0 ), .out(next4), .sel(writehit));
  Multiplexer #(.select(1), .width(2), .disabled("Z"), .enable("false")) multiplexer_11 (
    .in0(2'b00), .in1(2'b10), .out(multiplexer_11_out), .sel(EX_BranchTaken));
  Multiplexer #(.select(1), .width(2), .disabled("Z"), .enable("false")) multiplexer_12 (
    .in0(multiplexer_11_out), .in1(\双位预测状态转换_6_s0 ), .out(next5), .sel(writehit));
  Multiplexer #(.select(1), .width(2), .disabled("Z"), .enable("false")) multiplexer_13 (
    .in0(2'b00), .in1(2'b10), .out(multiplexer_13_out), .sel(EX_BranchTaken));
  Multiplexer #(.select(1), .width(2), .disabled("Z"), .enable("false")) multiplexer_14 (
    .in0(multiplexer_13_out), .in1(\双位预测状态转换_7_s0 ), .out(next6), .sel(writehit));
  Multiplexer #(.select(1), .width(2), .disabled("Z"), .enable("false")) multiplexer_15 (
    .in0(2'b00), .in1(2'b10), .out(multiplexer_15_out), .sel(EX_BranchTaken));
  Multiplexer #(.select(1), .width(2), .disabled("Z"), .enable("false")) multiplexer_16 (
    .in0(multiplexer_15_out), .in1(\双位预测状态转换_8_s0 ), .out(next7), .sel(writehit));
  or or_9 (readhit, read0, read1, read2, read3, read4, read5, read6, read7);
  not not_1 (readmiss, readhit);
  MAX3 max3_1 (.Y(cnt0), .X(cnt1), .Y_num(3'b000), .X_num(3'b001), .MAX(max3_1_max), .Max_num(max3_1_max_num));
  MAX3 max3_2 (.Y(cnt2), .X(cnt3), .Y_num(3'b010), .X_num(3'b011), .MAX(max3_2_max), .Max_num(max3_2_max_num));
  MAX3 max3_3 (.Y(cnt4), .X(cnt5), .Y_num(3'b100), .X_num(3'b101), .MAX(max3_3_max), .Max_num(max3_3_max_num));
  MAX3 max3_4 (.Y(cnt6), .X(cnt7), .Y_num(3'b110), .X_num(3'b111), .MAX(max3_4_max), .Max_num(max3_4_max_num));
  MAX3 max3_5 (
    .Y(max3_1_max), .X(max3_2_max), .Y_num(max3_1_max_num), .X_num(max3_2_max_num), .MAX(max3_5_max),
    .Max_num(max3_5_max_num));
  MAX3 max3_6 (
    .Y(max3_3_max), .X(max3_4_max), .Y_num(max3_3_max_num), .X_num(max3_4_max_num), .MAX(max3_6_max),
    .Max_num(max3_6_max_num));
  Comparator #(.width(32), .mode("twosComplement")) comparator_9 (
    .a(PC0), .b(EX_PC), .eq(comparator_9_eq));  // open: gt, lt
  Comparator #(.width(32), .mode("twosComplement")) comparator_10 (
    .a(PC1), .b(EX_PC), .eq(comparator_10_eq));  // open: gt, lt
  Comparator #(.width(32), .mode("twosComplement")) comparator_11 (
    .a(PC2), .b(EX_PC), .eq(comparator_11_eq));  // open: gt, lt
  Comparator #(.width(32), .mode("twosComplement")) comparator_12 (
    .a(PC3), .b(EX_PC), .eq(comparator_12_eq));  // open: gt, lt
  Comparator #(.width(32), .mode("twosComplement")) comparator_13 (
    .a(PC4), .b(EX_PC), .eq(comparator_13_eq));  // open: gt, lt
  Comparator #(.width(32), .mode("twosComplement")) comparator_14 (
    .a(PC5), .b(EX_PC), .eq(comparator_14_eq));  // open: gt, lt
  Comparator #(.width(32), .mode("twosComplement")) comparator_15 (
    .a(PC6), .b(EX_PC), .eq(comparator_15_eq));  // open: gt, lt
  Comparator #(.width(32), .mode("twosComplement")) comparator_16 (
    .a(PC7), .b(EX_PC), .eq(comparator_16_eq));  // open: gt, lt
  and and_17 (L0, comparator_9_eq, v0);
  and and_18 (L1, comparator_10_eq, v1);
  and and_19 (L2, comparator_11_eq, v2);
  and and_20 (L3, comparator_12_eq, v3);
  and and_21 (L4, comparator_13_eq, v4);
  and and_22 (L5, comparator_14_eq, v5);
  and and_23 (L6, comparator_15_eq, v6);
  and and_24 (L7, comparator_16_eq, v7);
  MAX3 max3_7 (
    .Y(max3_5_max), .X(max3_6_max), .Y_num(max3_5_max_num), .X_num(max3_6_max_num), .MAX(MAX),
    .Max_num(MAX_num));
  and and_25 (full, v0, v1, v2, v3, v4, v5, v6, v7);
  or or_10 (writehit, L0, L1, L2, L3, L4, L5, L6, L7);
  not not_2 (writemiss, writehit);
  Priority_Encoder #(.select(3), .disabled("Z")) priority_encoder_1 (
    .in0(1'b1), .in1(v0), .in2(v1), .in3(v2), .in4(v3), .in5(v4), .in6(v5), .in7(v6), .out(empty_num));  // open: gs, en_out, en_in
  Multiplexer #(.select(1), .width(3), .disabled("Z"), .enable("false")) multiplexer_17 (
    .in0(empty_num), .in1(MAX_num), .out(multiplexer_17_out), .sel(full));
  assign PredictJump = readmiss ? 1'b0 : 1'bz;  // Controlled_Buffer controlled_buffer_1
  assign PredictJump = read0 ? comparator_17_gt : 1'bz;  // Controlled_Buffer controlled_buffer_2
  Comparator #(.width(2), .mode("unsigned")) comparator_17 (
    .a(pre0), .b(2'b01), .gt(comparator_17_gt));  // open: eq, lt
  assign PredictJump = read1 ? comparator_18_gt : 1'bz;  // Controlled_Buffer controlled_buffer_3
  Comparator #(.width(2), .mode("unsigned")) comparator_18 (
    .a(pre1), .b(2'b01), .gt(comparator_18_gt));  // open: eq, lt
  assign PredictJump = read2 ? comparator_19_gt : 1'bz;  // Controlled_Buffer controlled_buffer_4
  Comparator #(.width(2), .mode("unsigned")) comparator_19 (
    .a(pre2), .b(2'b01), .gt(comparator_19_gt));  // open: eq, lt
  assign PredictJump = read3 ? comparator_20_gt : 1'bz;  // Controlled_Buffer controlled_buffer_5
  Comparator #(.width(2), .mode("unsigned")) comparator_20 (
    .a(pre3), .b(2'b01), .gt(comparator_20_gt));  // open: eq, lt
  assign PredictJump = read4 ? comparator_21_gt : 1'bz;  // Controlled_Buffer controlled_buffer_6
  Comparator #(.width(2), .mode("unsigned")) comparator_21 (
    .a(pre4), .b(2'b01), .gt(comparator_21_gt));  // open: eq, lt
  assign PredictJump = read5 ? comparator_22_gt : 1'bz;  // Controlled_Buffer controlled_buffer_7
  Comparator #(.width(2), .mode("unsigned")) comparator_22 (
    .a(pre5), .b(2'b01), .gt(comparator_22_gt));  // open: eq, lt
  assign PredictJump = read6 ? comparator_23_gt : 1'bz;  // Controlled_Buffer controlled_buffer_8
  Comparator #(.width(2), .mode("unsigned")) comparator_23 (
    .a(pre6), .b(2'b01), .gt(comparator_23_gt));  // open: eq, lt
  assign PredictJump = read7 ? comparator_24_gt : 1'bz;  // Controlled_Buffer controlled_buffer_9
  Comparator #(.width(2), .mode("unsigned")) comparator_24 (
    .a(pre7), .b(2'b01), .gt(comparator_24_gt));  // open: eq, lt
  Decoder #(.select(3), .tristate("false"), .disabled("Z"), .enable("false")) decoder_1 (
    .out0(decoder_1_out0), .out1(decoder_1_out1), .out2(decoder_1_out2), .out3(decoder_1_out3),
    .out4(decoder_1_out4), .out5(decoder_1_out5), .out6(decoder_1_out6), .out7(decoder_1_out7),
    .sel(multiplexer_17_out));
  and and_26 (and_26_out, decoder_1_out0, judge);
  and and_27 (and_27_out, decoder_1_out1, judge);
  and and_28 (and_28_out, decoder_1_out2, judge);
  and and_29 (and_29_out, decoder_1_out3, judge);
  and and_30 (and_30_out, decoder_1_out4, judge);
  and and_31 (and_31_out, decoder_1_out5, judge);
  and and_32 (and_32_out, decoder_1_out6, judge);
  and and_33 (and_33_out, decoder_1_out7, judge);
  or or_11 (write0, and_26_out, L0);
  or or_12 (write1, and_27_out, L1);
  or or_13 (write2, and_28_out, L2);
  or or_14 (write3, and_29_out, L3);
  or or_15 (write4, and_30_out, L4);
  or or_16 (write5, and_31_out, L5);
  or or_17 (write6, and_32_out, L6);
  or or_18 (write7, and_33_out, L7);
  assign Jumpaddr = readmiss ? {32{1'b0}} : 32'bz;  // Controlled_Buffer controlled_buffer_10
  assign Jumpaddr = read0 ? Daddr0 : 32'bz;  // Controlled_Buffer controlled_buffer_11
  assign Jumpaddr = read1 ? Daddr1 : 32'bz;  // Controlled_Buffer controlled_buffer_12
  assign Jumpaddr = read2 ? Daddr2 : 32'bz;  // Controlled_Buffer controlled_buffer_13
  assign Jumpaddr = read3 ? Daddr3 : 32'bz;  // Controlled_Buffer controlled_buffer_14
  assign Jumpaddr = read4 ? Daddr4 : 32'bz;  // Controlled_Buffer controlled_buffer_15
  assign Jumpaddr = read5 ? Daddr5 : 32'bz;  // Controlled_Buffer controlled_buffer_16
  assign Jumpaddr = read6 ? Daddr6 : 32'bz;  // Controlled_Buffer controlled_buffer_17
  assign Jumpaddr = read7 ? Daddr7 : 32'bz;  // Controlled_Buffer controlled_buffer_18
  and and_34 (judge, EX_isBranchIR, writemiss);

  // Notes on the sheet:
  //   读命中检测
  //   写命中检测
  //   命中则假设能跳转，否则返回0
endmodule

module locker (
  input  in,
  input  CLK,
  input  EN,
  input  RST,
  output out
);

  wire multiplexer_1_out;

  Multiplexer #(.select(1), .width(1), .disabled("Z"), .enable("false")) multiplexer_1 (
    .in0(in), .in1(1'b0), .out(multiplexer_1_out), .sel(RST));
  Register #(.width(1), .trigger("rising"), .Select("low")) register_1 (
    .D(multiplexer_1_out), .en(EN), .Q(out), .clk(CLK));  // open: clr
endmodule

module MAX3 (
  input  [31:0] Y,
  input  [31:0] X,
  input  [2:0] Y_num,
  input  [2:0] X_num,
  output [31:0] MAX,
  output [2:0] Max_num
);

  wire comparator_1_eq, comparator_1_gt, or_1_out;

  Multiplexer #(.select(1), .width(32), .disabled("Z"), .enable("false")) multiplexer_1 (
    .in0(Y), .in1(X), .out(MAX), .sel(or_1_out));
  Comparator #(.width(32), .mode("unsigned")) comparator_1 (
    .a(X), .b(Y), .gt(comparator_1_gt), .eq(comparator_1_eq));  // open: lt
  or or_1 (or_1_out, comparator_1_gt, comparator_1_eq);
  Multiplexer #(.select(1), .width(3), .disabled("Z"), .enable("false")) multiplexer_2 (
    .in0(Y_num), .in1(X_num), .out(Max_num), .sel(or_1_out));

  // Notes on the sheet:
  //   输出两个输入中的较大值，并输出较大值的3位编号
endmodule
